// Logisim project flappy bird.circ as structural Verilog: 2 circuits, main circuit main
// 2
module main (
  input  in_1
);

  wire clock_1_out, jump_out;
  wire [7:0] adder_1_out, adder_2_out, adder_3_out, multiplexer_1_out, Position_q, shifter_1_out, Velocity_q,
       wall_position_q;
  wire [31:0] show_1_out_5, show_1_out_6, show_1_out_7, show_1_out_8, show_1_out_9, show_1_out_10,
       show_1_out_11, show_1_out_12, show_1_out_13, show_1_out_14, show_1_out_15, show_1_out_16,
       show_1_out_17, show_1_out_18, show_1_out_19, show_1_out_20, show_1_out_22, show_1_out_23,
       show_1_out_24, show_1_out_25, show_1_out_26, show_1_out_27, show_1_out_29, show_1_out_30,
       show_1_out_31, show_1_out_32, show_1_out_33, show_1_out_34, show_1_out_35, show_1_out_36;

  Adder adder_1 (.a(Velocity_q), .b({8{1'b1}}), .out(adder_1_out));  // open: cin, cout
  Multiplexer #(.width(8)) multiplexer_1 (
    .in0(adder_1_out), .in1(8'h20), .out(multiplexer_1_out), .sel(jump_out));  // open: en
  Clock clock_1 (.out(clock_1_out));
  // Probe on Velocity_q
  Register Velocity (.D(multiplexer_1_out), .Q(Velocity_q), .clk(clock_1_out));  // open: en, clr
  Shifter #(.shift("ar")) shifter_1 (.in(Velocity_q), .\dist (3'b100), .out(shifter_1_out));
  Adder adder_2 (.a(Position_q), .b(shifter_1_out), .out(adder_2_out));  // open: cin, cout
  Register Position (.D(adder_2_out), .Q(Position_q), .clk(clock_1_out));  // open: en, clr
  // Probe on Position_q
  Adder adder_3 (.a(wall_position_q), .b(8'hfe), .out(adder_3_out));  // open: cin, cout
  Register wall_position (.D(adder_3_out), .Q(wall_position_q), .clk(clock_1_out));  // open: en, clr
  Button jump (.out(jump_out));
  DotMatrix #(.matrixcols(30), .matrixrows(32)) dotmatrix_1 (
    .col0(show_1_out_20), .col1(show_1_out_13), .col2(show_1_out_8), .col3(show_1_out_5),
    .col4(show_1_out_24), .col5(show_1_out_16), .col6(show_1_out_10), .col7(show_1_out_6),
    .col8(show_1_out_27), .col9(show_1_out_19), .col10(show_1_out_12), .col11(show_1_out_7),
    .col12(show_1_out_30), .col13(show_1_out_23), .col14(show_1_out_15), .col15(show_1_out_9),
    .col16(show_1_out_32), .col17(show_1_out_26), .col18(show_1_out_18), .col19(show_1_out_11),
    .col20(show_1_out_34), .col21(show_1_out_29), .col22(show_1_out_22), .col23(show_1_out_14),
    .col24(show_1_out_35), .col25(show_1_out_31), .col26(show_1_out_25), .col27(show_1_out_17),
    .col28(show_1_out_36), .col29(show_1_out_33));
  show show_1 (
    .Player_pos(Position_q), .Clock(clock_1_out), .Wall_form(32'hfff000ff), .Wall_pos(wall_position_q),
    .out_20(show_1_out_20), .out_13(show_1_out_13), .out_8(show_1_out_8), .out_5(show_1_out_5),
    .out_24(show_1_out_24), .out_16(show_1_out_16), .out_10(show_1_out_10), .out_6(show_1_out_6),
    .out_27(show_1_out_27), .out_19(show_1_out_19), .out_12(show_1_out_12), .out_7(show_1_out_7),
    .out_30(show_1_out_30), .out_23(show_1_out_23), .out_15(show_1_out_15), .out_9(show_1_out_9),
    .out_32(show_1_out_32), .out_26(show_1_out_26), .out_18(show_1_out_18), .out_11(show_1_out_11),
    .out_34(show_1_out_34), .out_29(show_1_out_29), .out_22(show_1_out_22), .out_14(show_1_out_14),
    .out_35(show_1_out_35), .out_31(show_1_out_31), .out_25(show_1_out_25), .out_17(show_1_out_17),
    .out_36(show_1_out_36), .out_33(show_1_out_33));  // open: out_28, out_21
endmodule

module show (
  input  [7:0] Player_pos,
  input  Clock,
  input  [31:0] Wall_form,
  input  [7:0] Wall_pos,
  output [31:0] out_5,
  output [31:0] out_6,
  output [31:0] out_7,
  output [31:0] out_8,
  output [31:0] out_9,
  output [31:0] out_10,
  output [31:0] out_11,
  output [31:0] out_12,
  output [31:0] out_13,
  output [31:0] out_14,
  output [31:0] out_15,
  output [31:0] out_16,
  output [31:0] out_17,
  output [31:0] out_18,
  output [31:0] out_19,
  output [31:0] out_20,
  output [31:0] out_21,
  output [31:0] out_22,
  output [31:0] out_23,
  output [31:0] out_24,
  output [31:0] out_25,
  output [31:0] out_26,
  output [31:0] out_27,
  output [31:0] out_28,
  output [31:0] out_29,
  output [31:0] out_30,
  output [31:0] out_31,
  output [31:0] out_32,
  output [31:0] out_33,
  output [31:0] out_34,
  output [31:0] out_35,
  output [31:0] out_36
);

  wire [31:0] demultiplexer_1_out0, demultiplexer_2_out0, demultiplexer_2_out1, demultiplexer_2_out2,
       demultiplexer_2_out3, demultiplexer_2_out4, demultiplexer_2_out5, demultiplexer_2_out6,
       demultiplexer_2_out7, demultiplexer_2_out8, demultiplexer_2_out9, demultiplexer_2_out10,
       demultiplexer_2_out11, demultiplexer_2_out12, demultiplexer_2_out13, demultiplexer_2_out14,
       demultiplexer_2_out15, demultiplexer_2_out16, demultiplexer_2_out17, demultiplexer_2_out18,
       demultiplexer_2_out19, demultiplexer_2_out20, demultiplexer_2_out21, demultiplexer_2_out22,
       demultiplexer_2_out23, demultiplexer_2_out24, demultiplexer_2_out25, demultiplexer_2_out26,
       demultiplexer_2_out27, demultiplexer_2_out28, demultiplexer_2_out29, demultiplexer_2_out30,
       demultiplexer_2_out31, multiplier_1_out, or_4_out, or_5_out, or_6_out, Position_2_q, Position_q;

  Demultiplexer #(.select(5)) demultiplexer_1 (
    .out0(demultiplexer_1_out0[0]), .out1(demultiplexer_1_out0[1]), .out2(demultiplexer_1_out0[2]),
    .out3(demultiplexer_1_out0[3]), .out4(demultiplexer_1_out0[4]), .out5(demultiplexer_1_out0[5]),
    .out6(demultiplexer_1_out0[6]), .out7(demultiplexer_1_out0[7]), .out8(demultiplexer_1_out0[8]),
    .out9(demultiplexer_1_out0[9]), .out10(demultiplexer_1_out0[10]), .out11(demultiplexer_1_out0[11]),
    .out12(demultiplexer_1_out0[12]), .out13(demultiplexer_1_out0[13]), .out14(demultiplexer_1_out0[14]),
    .out15(demultiplexer_1_out0[15]), .out16(demultiplexer_1_out0[16]), .out17(demultiplexer_1_out0[17]),
    .out18(demultiplexer_1_out0[18]), .out19(demultiplexer_1_out0[19]), .out20(demultiplexer_1_out0[20]),
    .out21(demultiplexer_1_out0[21]), .out22(demultiplexer_1_out0[22]), .out23(demultiplexer_1_out0[23]),
    .out24(demultiplexer_1_out0[24]), .out25(demultiplexer_1_out0[25]), .out26(demultiplexer_1_out0[26]),
    .out27(demultiplexer_1_out0[27]), .out28(demultiplexer_1_out0[28]), .out29(demultiplexer_1_out0[29]),
    .out30(demultiplexer_1_out0[30]), .out31(demultiplexer_1_out0[31]), .in(1'b1), .sel(Player_pos[7:3]));  // open: en
  Demultiplexer #(.select(5), .width(32)) demultiplexer_2 (
    .out0(demultiplexer_2_out0), .out1(demultiplexer_2_out1), .out2(demultiplexer_2_out2),
    .out3(demultiplexer_2_out3), .out4(demultiplexer_2_out4), .out5(demultiplexer_2_out5),
    .out6(demultiplexer_2_out6), .out7(demultiplexer_2_out7), .out8(demultiplexer_2_out8),
    .out9(demultiplexer_2_out9), .out10(demultiplexer_2_out10), .out11(demultiplexer_2_out11),
    .out12(demultiplexer_2_out12), .out13(demultiplexer_2_out13), .out14(demultiplexer_2_out14),
    .out15(demultiplexer_2_out15), .out16(demultiplexer_2_out16), .out17(demultiplexer_2_out17),
    .out18(demultiplexer_2_out18), .out19(demultiplexer_2_out19), .out20(demultiplexer_2_out20),
    .out21(demultiplexer_2_out21), .out22(demultiplexer_2_out22), .out23(demultiplexer_2_out23),
    .out24(demultiplexer_2_out24), .out25(demultiplexer_2_out25), .out26(demultiplexer_2_out26),
    .out27(demultiplexer_2_out27), .out28(demultiplexer_2_out28), .out29(demultiplexer_2_out29),
    .out30(demultiplexer_2_out30), .out31(demultiplexer_2_out31), .in(Wall_form), .sel(Wall_pos[7:3]));  // open: en
  // Probe on demultiplexer_1_out0
  Multiplier #(.width(32)) multiplier_1 (
    .a(demultiplexer_1_out0), .b(32'h7), .out(multiplier_1_out));  // open: cin, cout
  Register #(.width(32)) Position (.D(multiplier_1_out), .Q(Position_q), .clk(Clock));  // open: en, clr
  Register #(.width(32)) Position_2 (.D(Position_q), .Q(Position_2_q), .clk(Clock));  // open: en, clr
  assign out_20 = demultiplexer_2_out0 | demultiplexer_2_out1 | demultiplexer_2_out2 | demultiplexer_2_out3 | demultiplexer_2_out4;  // OR_Gate or_1, 32 bits wide
  assign out_13 = demultiplexer_2_out1 | demultiplexer_2_out2 | demultiplexer_2_out3 | demultiplexer_2_out4 | demultiplexer_2_out5;  // OR_Gate or_2, 32 bits wide
  assign out_8 = demultiplexer_2_out2 | demultiplexer_2_out3 | demultiplexer_2_out4 | demultiplexer_2_out5 | demultiplexer_2_out6;  // OR_Gate or_3, 32 bits wide
  assign or_4_out = demultiplexer_2_out3 | demultiplexer_2_out4 | demultiplexer_2_out5 | demultiplexer_2_out6 | demultiplexer_2_out7;  // OR_Gate or_4, 32 bits wide
  assign or_5_out = demultiplexer_2_out4 | demultiplexer_2_out5 | demultiplexer_2_out6 | demultiplexer_2_out7 | demultiplexer_2_out8;  // OR_Gate or_5, 32 bits wide
  assign or_6_out = demultiplexer_2_out5 | demultiplexer_2_out6 | demultiplexer_2_out7 | demultiplexer_2_out8 | demultiplexer_2_out9;  // OR_Gate or_6, 32 bits wide
  assign out_10 = demultiplexer_2_out6 | demultiplexer_2_out7 | demultiplexer_2_out8 | demultiplexer_2_out9 | demultiplexer_2_out10;  // OR_Gate or_7, 32 bits wide
  assign out_6 = demultiplexer_2_out7 | demultiplexer_2_out8 | demultiplexer_2_out9 | demultiplexer_2_out10 | demultiplexer_2_out11;  // OR_Gate or_8, 32 bits wide
  assign out_27 = demultiplexer_2_out8 | demultiplexer_2_out9 | demultiplexer_2_out10 | demultiplexer_2_out11 | demultiplexer_2_out12;  // OR_Gate or_9, 32 bits wide
  assign out_19 = demultiplexer_2_out9 | demultiplexer_2_out10 | demultiplexer_2_out11 | demultiplexer_2_out12 | demultiplexer_2_out13;  // OR_Gate or_10, 32 bits wide
  assign out_12 = demultiplexer_2_out10 | demultiplexer_2_out11 | demultiplexer_2_out12 | demultiplexer_2_out13 | demultiplexer_2_out14;  // OR_Gate or_11, 32 bits wide
  assign out_7 = demultiplexer_2_out11 | demultiplexer_2_out12 | demultiplexer_2_out13 | demultiplexer_2_out14 | demultiplexer_2_out15;  // OR_Gate or_12, 32 bits wide
  assign out_30 = demultiplexer_2_out12 | demultiplexer_2_out13 | demultiplexer_2_out14 | demultiplexer_2_out15 | demultiplexer_2_out16;  // OR_Gate or_13, 32 bits wide
  assign out_23 = demultiplexer_2_out13 | demultiplexer_2_out14 | demultiplexer_2_out15 | demultiplexer_2_out16 | demultiplexer_2_out17;  // OR_Gate or_14, 32 bits wide
  assign out_15 = demultiplexer_2_out14 | demultiplexer_2_out15 | demultiplexer_2_out16 | demultiplexer_2_out17 | demultiplexer_2_out18;  // OR_Gate or_15, 32 bits wide
  assign out_9 = demultiplexer_2_out15 | demultiplexer_2_out16 | demultiplexer_2_out17 | demultiplexer_2_out18 | demultiplexer_2_out19;  // OR_Gate or_16, 32 bits wide
  assign out_32 = demultiplexer_2_out16 | demultiplexer_2_out17 | demultiplexer_2_out18 | demultiplexer_2_out19 | demultiplexer_2_out20;  // OR_Gate or_17, 32 bits wide
  assign out_26 = demultiplexer_2_out17 | demultiplexer_2_out18 | demultiplexer_2_out19 | demultiplexer_2_out20 | demultiplexer_2_out21;  // OR_Gate or_18, 32 bits wide
  assign out_18 = demultiplexer_2_out18 | demultiplexer_2_out19 | demultiplexer_2_out20 | demultiplexer_2_out21 | demultiplexer_2_out22;  // OR_Gate or_19, 32 bits wide
  assign out_11 = demultiplexer_2_out19 | demultiplexer_2_out20 | demultiplexer_2_out21 | demultiplexer_2_out22 | demultiplexer_2_out23;  // OR_Gate or_20, 32 bits wide
  assign out_34 = demultiplexer_2_out20 | demultiplexer_2_out21 | demultiplexer_2_out22 | demultiplexer_2_out23 | demultiplexer_2_out24;  // OR_Gate or_21, 32 bits wide
  assign out_29 = demultiplexer_2_out21 | demultiplexer_2_out22 | demultiplexer_2_out23 | demultiplexer_2_out24 | demultiplexer_2_out25;  // OR_Gate or_22, 32 bits wide
  assign out_22 = demultiplexer_2_out22 | demultiplexer_2_out23 | demultiplexer_2_out24 | demultiplexer_2_out25 | demultiplexer_2_out26;  // OR_Gate or_23, 32 bits wide
  assign out_14 = demultiplexer_2_out23 | demultiplexer_2_out24 | demultiplexer_2_out25 | demultiplexer_2_out26 | demultiplexer_2_out27;  // OR_Gate or_24, 32 bits wide
  assign out_35 = demultiplexer_2_out24 | demultiplexer_2_out25 | demultiplexer_2_out26 | demultiplexer_2_out27 | demultiplexer_2_out28;  // OR_Gate or_25, 32 bits wide
  assign out_31 = demultiplexer_2_out25 | demultiplexer_2_out26 | demultiplexer_2_out27 | demultiplexer_2_out28 | demultiplexer_2_out29;  // OR_Gate or_26, 32 bits wide
  assign out_25 = demultiplexer_2_out26 | demultiplexer_2_out27 | demultiplexer_2_out28 | demultiplexer_2_out29 | demultiplexer_2_out30;  // OR_Gate or_27, 32 bits wide
  assign out_17 = demultiplexer_2_out27 | demultiplexer_2_out28 | demultiplexer_2_out29 | demultiplexer_2_out30 | demultiplexer_2_out31;  // OR_Gate or_28, 32 bits wide
  assign out_36 = demultiplexer_2_out28 | demultiplexer_2_out29 | demultiplexer_2_out30 | demultiplexer_2_out31 | {32{1'b0}};  // OR_Gate or_29, 32 bits wide
  assign out_33 = demultiplexer_2_out29 | demultiplexer_2_out30 | demultiplexer_2_out31 | {32{1'b0}} | {32{1'b0}};  // OR_Gate or_30, 32 bits wide
  assign out_28 = demultiplexer_2_out30 | demultiplexer_2_out31 | {32{1'b0}} | {32{1'b0}} | {32{1'b0}};  // OR_Gate or_31, 32 bits wide
  assign out_21 = demultiplexer_2_out31 | {32{1'b0}} | {32{1'b0}} | {32{1'b0}} | {32{1'b0}};  // OR_Gate or_32, 32 bits wide
  assign out_5 = Position_2_q | or_4_out;  // OR_Gate or_33, 32 bits wide
  assign out_24 = Position_q | or_5_out;  // OR_Gate or_34, 32 bits wide
  assign out_16 = multiplier_1_out | or_6_out;  // OR_Gate or_35, 32 bits wide
endmodule
