// Logisim project graphics processor.circ as structural Verilog: 5 circuits, main circuit main
module main (
  input  in_1,
  input  in_2,
  input  in_3
);

  wire and_1_out, and_2_out, clock_1_out, comparator_1_eq, comparator_2_eq, comparator_3_gt, not_1_out;
  wire [4:0] counter_1_q, counter_2_q, counter_3_q;
  wire [10:0] counter_4_q;
  wire [25:0] ball, ball_1_updated_ball, bit_extender_1_out, controlled_buffer_1_out, multiplexer_1_out,
       multiplexer_2_out, multiplexer_3_out, random_1_out;
  wire [31:0] graphics2_1_out_4, graphics2_1_out_5, graphics2_1_out_6, graphics2_1_out_7, graphics2_1_out_8,
       graphics2_1_out_9, graphics2_1_out_10, graphics2_1_out_11, graphics2_1_out_12, graphics2_1_out_13,
       graphics2_1_out_14, graphics2_1_out_15, graphics2_1_out_16, graphics2_1_out_17, graphics2_1_out_18,
       graphics2_1_out_19, graphics2_1_out_20, graphics2_1_out_21, graphics2_1_out_22, graphics2_1_out_23,
       graphics2_1_out_24, graphics2_1_out_25, graphics2_1_out_26, graphics2_1_out_27, graphics2_1_out_28,
       graphics2_1_out_29, graphics2_1_out_30, graphics2_1_out_31, graphics2_1_out_32, graphics2_1_out_33,
       graphics2_1_out_34, graphics2_1_out_35, graphics3_1_out_4, register_2_q, rom_1_data, shifter_1_out;

  Clock clock_1 (.out(clock_1_out));
  Counter #(.width(5), .max('h1f)) counter_1 (.Q(counter_1_q), .clk(clock_1_out));  // open: load, D, count, carry, clr
  // Probe on random_1_out
  Random #(.width(26)) random_1 (.clk(and_1_out), .out(random_1_out));  // open: next, clr
  assign controlled_buffer_1_out = not_1_out ? random_1_out : 26'bz;  // Controlled_Buffer controlled_buffer_1
  and and_1 (and_1_out, clock_1_out, not_1_out);
  not not_1 (not_1_out, comparator_3_gt);
  ROM #(.addrWidth(5), .dataWidth(32)) rom_1 (.addr(counter_1_q), .data(rom_1_data));  // open: sel
  // Probe on bit_extender_1_out
  Bit_Extender #(.in_width(32), .out_width(26)) bit_extender_1 (.in(shifter_1_out), .out(bit_extender_1_out));
  Shifter #(.width(32), .shift("lr")) shifter_1 (.in(rom_1_data), .\dist (5'b00110), .out(shifter_1_out));
  RAM #(.addrWidth(5), .dataWidth(26)) ram_1 (
    .addr(counter_1_q), .data(controlled_buffer_1_out), .clk(clock_1_out), .ld(comparator_3_gt));  // open: sel, clr
  ball ball_1 (
    .start_vx({8{1'b1}}), .start_vy(8'hf0), .ball_data(ball), .Clock(comparator_2_eq), .Reset(in_3),
    .Updated_ball(ball_1_updated_ball));
  // Probe on multiplexer_1_out
  Multiplexer #(.width(26)) multiplexer_1 (
    .in0(bit_extender_1_out), .in1(controlled_buffer_1_out), .out(multiplexer_1_out), .sel(in_1));  // open: en
  Counter #(.width(5), .max('h1f)) counter_2 (.Q(counter_2_q), .clk(and_2_out));  // open: load, D, count, carry, clr
  and and_2 (and_2_out, clock_1_out, comparator_3_gt);
  Comparator #(.width(5), .mode("unsigned")) comparator_1 (
    .a(counter_2_q), .b({5{1'b1}}), .eq(comparator_1_eq));  // open: gt, lt
  Comparator #(.width(5), .mode("unsigned")) comparator_2 (
    .a(counter_2_q), .b({5{1'b0}}), .eq(comparator_2_eq));  // open: gt, lt
  Multiplexer #(.width(26)) multiplexer_2 (
    .in0(ball_1_updated_ball), .in1(26'h224e00), .out(multiplexer_2_out), .sel(in_3));  // open: en
  Multiplexer #(.width(26)) multiplexer_3 (
    .in0(multiplexer_1_out), .in1(ball), .out(multiplexer_3_out), .sel(comparator_1_eq));  // open: en
  graphics3 graphics3_1 (
    .object(multiplexer_3_out), .row(counter_3_q), .row_state(register_2_q), .out_4(graphics3_1_out_4));
  Counter #(.width(5), .max('h1f)) counter_3 (
    .Q(counter_3_q), .clk(comparator_2_eq));  // open: load, D, count, carry, clr
  Register #(.width(26)) register_1 (.D(multiplexer_2_out), .Q(ball), .clk(comparator_2_eq));  // open: en, clr
  Register #(.width(32)) register_2 (
    .D(graphics3_1_out_4), .Q(register_2_q), .clk(and_2_out), .clr(comparator_2_eq));  // open: en
  // Probe on ball[1:0]
  // Probe on ball[25:18]
  DotMatrix #(.matrixcols(32), .matrixrows(32)) dotmatrix_1 (
    .col0(graphics2_1_out_4), .col1(graphics2_1_out_5), .col2(graphics2_1_out_6), .col3(graphics2_1_out_7),
    .col4(graphics2_1_out_8), .col5(graphics2_1_out_9), .col6(graphics2_1_out_10), .col7(graphics2_1_out_11),
    .col8(graphics2_1_out_12), .col9(graphics2_1_out_13), .col10(graphics2_1_out_14),
    .col11(graphics2_1_out_15), .col12(graphics2_1_out_16), .col13(graphics2_1_out_17),
    .col14(graphics2_1_out_18), .col15(graphics2_1_out_19), .col16(graphics2_1_out_20),
    .col17(graphics2_1_out_21), .col18(graphics2_1_out_22), .col19(graphics2_1_out_23),
    .col20(graphics2_1_out_24), .col21(graphics2_1_out_25), .col22(graphics2_1_out_26),
    .col23(graphics2_1_out_27), .col24(graphics2_1_out_28), .col25(graphics2_1_out_29),
    .col26(graphics2_1_out_30), .col27(graphics2_1_out_31), .col28(graphics2_1_out_32),
    .col29(graphics2_1_out_33), .col30(graphics2_1_out_34), .col31(graphics2_1_out_35));
  graphics2 graphics2_1 (
    .in_1(register_2_q), .clock(comparator_2_eq), .clock_state(counter_3_q), .out_4(graphics2_1_out_4),
    .out_5(graphics2_1_out_5), .out_6(graphics2_1_out_6), .out_7(graphics2_1_out_7),
    .out_8(graphics2_1_out_8), .out_9(graphics2_1_out_9), .out_10(graphics2_1_out_10),
    .out_11(graphics2_1_out_11), .out_12(graphics2_1_out_12), .out_13(graphics2_1_out_13),
    .out_14(graphics2_1_out_14), .out_15(graphics2_1_out_15), .out_16(graphics2_1_out_16),
    .out_17(graphics2_1_out_17), .out_18(graphics2_1_out_18), .out_19(graphics2_1_out_19),
    .out_20(graphics2_1_out_20), .out_21(graphics2_1_out_21), .out_22(graphics2_1_out_22),
    .out_23(graphics2_1_out_23), .out_24(graphics2_1_out_24), .out_25(graphics2_1_out_25),
    .out_26(graphics2_1_out_26), .out_27(graphics2_1_out_27), .out_28(graphics2_1_out_28),
    .out_29(graphics2_1_out_29), .out_30(graphics2_1_out_30), .out_31(graphics2_1_out_31),
    .out_32(graphics2_1_out_32), .out_33(graphics2_1_out_33), .out_34(graphics2_1_out_34),
    .out_35(graphics2_1_out_35));
  Counter #(.width(11), .max('h7ff)) counter_4 (
    .Q(counter_4_q), .clk(clock_1_out));  // open: load, D, count, carry, clr
  // Probe on ball[9:2]
  // Probe on ball[17:10]
  Comparator #(.width(11), .mode("unsigned")) comparator_3 (
    .a(counter_4_q), .b(11'h300), .gt(comparator_3_gt));  // open: eq, lt

  // Other names for the same wires on the sheet: ball_type[1:0] = ball[1:0]; ball_size[7:0] = ball[25:18]

  // Notes on the sheet:
  //   contents of rom_1 (hex, n*v repeats v):
  //   605800c0 6000a080 60600040 6060ff40 0 40f8c0c0 40c00080 40b880c0 40804080 0 0 40408080 407840c0
endmodule

module graphics2 (
  input  [31:0] in_1,
  input  clock,
  input  [4:0] clock_state,
  output [31:0] out_4,
  output [31:0] out_5,
  output [31:0] out_6,
  output [31:0] out_7,
  output [31:0] out_8,
  output [31:0] out_9,
  output [31:0] out_10,
  output [31:0] out_11,
  output [31:0] out_12,
  output [31:0] out_13,
  output [31:0] out_14,
  output [31:0] out_15,
  output [31:0] out_16,
  output [31:0] out_17,
  output [31:0] out_18,
  output [31:0] out_19,
  output [31:0] out_20,
  output [31:0] out_21,
  output [31:0] out_22,
  output [31:0] out_23,
  output [31:0] out_24,
  output [31:0] out_25,
  output [31:0] out_26,
  output [31:0] out_27,
  output [31:0] out_28,
  output [31:0] out_29,
  output [31:0] out_30,
  output [31:0] out_31,
  output [31:0] out_32,
  output [31:0] out_33,
  output [31:0] out_34,
  output [31:0] out_35
);

  wire [31:0] demultiplexer_1_out0, demultiplexer_1_out1, demultiplexer_1_out2, demultiplexer_1_out3,
       demultiplexer_1_out4, demultiplexer_1_out5, demultiplexer_1_out6, demultiplexer_1_out7,
       demultiplexer_1_out8, demultiplexer_1_out9, demultiplexer_1_out10, demultiplexer_1_out11,
       demultiplexer_1_out12, demultiplexer_1_out13, demultiplexer_1_out14, demultiplexer_1_out15,
       demultiplexer_1_out16, demultiplexer_1_out17, demultiplexer_1_out18, demultiplexer_1_out19,
       demultiplexer_1_out20, demultiplexer_1_out21, demultiplexer_1_out22, demultiplexer_1_out23,
       demultiplexer_1_out24, demultiplexer_1_out25, demultiplexer_1_out26, demultiplexer_1_out27,
       demultiplexer_1_out28, demultiplexer_1_out29, demultiplexer_1_out30, demultiplexer_1_out31;

  Demultiplexer #(.select(5), .width(32), .tristate("true")) demultiplexer_1 (
    .out0(demultiplexer_1_out0), .out1(demultiplexer_1_out1), .out2(demultiplexer_1_out2),
    .out3(demultiplexer_1_out3), .out4(demultiplexer_1_out4), .out5(demultiplexer_1_out5),
    .out6(demultiplexer_1_out6), .out7(demultiplexer_1_out7), .out8(demultiplexer_1_out8),
    .out9(demultiplexer_1_out9), .out10(demultiplexer_1_out10), .out11(demultiplexer_1_out11),
    .out12(demultiplexer_1_out12), .out13(demultiplexer_1_out13), .out14(demultiplexer_1_out14),
    .out15(demultiplexer_1_out15), .out16(demultiplexer_1_out16), .out17(demultiplexer_1_out17),
    .out18(demultiplexer_1_out18), .out19(demultiplexer_1_out19), .out20(demultiplexer_1_out20),
    .out21(demultiplexer_1_out21), .out22(demultiplexer_1_out22), .out23(demultiplexer_1_out23),
    .out24(demultiplexer_1_out24), .out25(demultiplexer_1_out25), .out26(demultiplexer_1_out26),
    .out27(demultiplexer_1_out27), .out28(demultiplexer_1_out28), .out29(demultiplexer_1_out29),
    .out30(demultiplexer_1_out30), .out31(demultiplexer_1_out31), .in(in_1), .sel(clock_state));  // open: en
  Register #(.width(32)) register_1 (.D(demultiplexer_1_out0), .Q(out_4), .clk(clock));  // open: en, clr
  Register #(.width(32)) register_2 (.D(demultiplexer_1_out1), .Q(out_5), .clk(clock));  // open: en, clr
  Register #(.width(32)) register_3 (.D(demultiplexer_1_out2), .Q(out_6), .clk(clock));  // open: en, clr
  Register #(.width(32)) register_4 (.D(demultiplexer_1_out3), .Q(out_7), .clk(clock));  // open: en, clr
  Register #(.width(32)) register_5 (.D(demultiplexer_1_out4), .Q(out_8), .clk(clock));  // open: en, clr
  Register #(.width(32)) register_6 (.D(demultiplexer_1_out5), .Q(out_9), .clk(clock));  // open: en, clr
  Register #(.width(32)) register_7 (.D(demultiplexer_1_out6), .Q(out_10), .clk(clock));  // open: en, clr
  Register #(.width(32)) register_8 (.D(demultiplexer_1_out7), .Q(out_11), .clk(clock));  // open: en, clr
  Register #(.width(32)) register_9 (.D(demultiplexer_1_out8), .Q(out_12), .clk(clock));  // open: en, clr
  Register #(.width(32)) register_10 (.D(demultiplexer_1_out9), .Q(out_13), .clk(clock));  // open: en, clr
  Register #(.width(32)) register_11 (.D(demultiplexer_1_out10), .Q(out_14), .clk(clock));  // open: en, clr
  Register #(.width(32)) register_12 (.D(demultiplexer_1_out11), .Q(out_15), .clk(clock));  // open: en, clr
  Register #(.width(32)) register_13 (.D(demultiplexer_1_out12), .Q(out_16), .clk(clock));  // open: en, clr
  Register #(.width(32)) register_14 (.D(demultiplexer_1_out13), .Q(out_17), .clk(clock));  // open: en, clr
  Register #(.width(32)) register_15 (.D(demultiplexer_1_out14), .Q(out_18), .clk(clock));  // open: en, clr
  Register #(.width(32)) register_16 (.D(demultiplexer_1_out15), .Q(out_19), .clk(clock));  // open: en, clr
  Register #(.width(32)) register_17 (.D(demultiplexer_1_out16), .Q(out_20), .clk(clock));  // open: en, clr
  Register #(.width(32)) register_18 (.D(demultiplexer_1_out17), .Q(out_21), .clk(clock));  // open: en, clr
  Register #(.width(32)) register_19 (.D(demultiplexer_1_out18), .Q(out_22), .clk(clock));  // open: en, clr
  Register #(.width(32)) register_20 (.D(demultiplexer_1_out19), .Q(out_23), .clk(clock));  // open: en, clr
  Register #(.width(32)) register_21 (.D(demultiplexer_1_out20), .Q(out_24), .clk(clock));  // open: en, clr
  Register #(.width(32)) register_22 (.D(demultiplexer_1_out21), .Q(out_25), .clk(clock));  // open: en, clr
  Register #(.width(32)) register_23 (.D(demultiplexer_1_out22), .Q(out_26), .clk(clock));  // open: en, clr
  Register #(.width(32)) register_24 (.D(demultiplexer_1_out23), .Q(out_27), .clk(clock));  // open: en, clr
  Register #(.width(32)) register_25 (.D(demultiplexer_1_out24), .Q(out_28), .clk(clock));  // open: en, clr
  Register #(.width(32)) register_26 (.D(demultiplexer_1_out25), .Q(out_29), .clk(clock));  // open: en, clr
  Register #(.width(32)) register_27 (.D(demultiplexer_1_out26), .Q(out_30), .clk(clock));  // open: en, clr
  Register #(.width(32)) register_28 (.D(demultiplexer_1_out27), .Q(out_31), .clk(clock));  // open: en, clr
  Register #(.width(32)) register_29 (.D(demultiplexer_1_out28), .Q(out_32), .clk(clock));  // open: en, clr
  Register #(.width(32)) register_30 (.D(demultiplexer_1_out29), .Q(out_33), .clk(clock));  // open: en, clr
  Register #(.width(32)) register_31 (.D(demultiplexer_1_out30), .Q(out_34), .clk(clock));  // open: en, clr
  Register #(.width(32)) register_32 (.D(demultiplexer_1_out31), .Q(out_35), .clk(clock));  // open: en, clr
endmodule

module graphics3 (
  input  [25:0] object,
  input  [4:0] row,
  input  [31:0] row_state,
  output [31:0] out_4
);

  wire adder_2_cout, and_1_out, comparator_1_eq, comparator_2_gt, comparator_3_eq, comparator_3_lt, or_1_out,
       or_2_out;
  wire [4:0] adder_1_out, adder_2_out, multiplexer_1_out, negator_1_out, subtractor_1_out, transistor_1_out;
  wire [31:0] decoder_1_out0, multiplier_1_out, not_1_out, shifter_1_out, transistor_3_out, transistor_5_out;

  // Probe on object[1:0]
  // Probe on object[9:2]
  // Probe on object[17:10]
  // Probe on object[25:18]
  // Probe on row
  // Probe on object[9:5]
  // Probe on object[17:13]
  // Probe on object[25:21]
  Subtractor #(.width(5)) subtractor_1 (.a(object[9:5]), .b(row), .out(subtractor_1_out));  // open: bin, bout
  Negator #(.width(5)) negator_1 (.in(subtractor_1_out), .out(negator_1_out));
  Multiplexer #(.select(2), .width(5)) multiplexer_1 (
    .in0({5{1'b0}}), .in1({5{1'b0}}), .in2(negator_1_out), .in3(subtractor_1_out), .out(multiplexer_1_out),
    .sel(object[1:0]));  // open: en
  Decoder #(.select(5)) decoder_1 (
    .out0(decoder_1_out0[0]), .out1(decoder_1_out0[1]), .out2(decoder_1_out0[2]), .out3(decoder_1_out0[3]),
    .out4(decoder_1_out0[4]), .out5(decoder_1_out0[5]), .out6(decoder_1_out0[6]), .out7(decoder_1_out0[7]),
    .out8(decoder_1_out0[8]), .out9(decoder_1_out0[9]), .out10(decoder_1_out0[10]),
    .out11(decoder_1_out0[11]), .out12(decoder_1_out0[12]), .out13(decoder_1_out0[13]),
    .out14(decoder_1_out0[14]), .out15(decoder_1_out0[15]), .out16(decoder_1_out0[16]),
    .out17(decoder_1_out0[17]), .out18(decoder_1_out0[18]), .out19(decoder_1_out0[19]),
    .out20(decoder_1_out0[20]), .out21(decoder_1_out0[21]), .out22(decoder_1_out0[22]),
    .out23(decoder_1_out0[23]), .out24(decoder_1_out0[24]), .out25(decoder_1_out0[25]),
    .out26(decoder_1_out0[26]), .out27(decoder_1_out0[27]), .out28(decoder_1_out0[28]),
    .out29(decoder_1_out0[29]), .out30(decoder_1_out0[30]), .out31(decoder_1_out0[31]), .sel(adder_1_out));  // open: en
  Adder #(.width(5)) adder_1 (.a(multiplexer_1_out), .b(object[17:13]), .out(adder_1_out));  // open: cin, cout
  Comparator #(.width(2)) comparator_1 (.a(object[1:0]), .b(2'b01), .eq(comparator_1_eq));  // open: gt, lt
  // Probe on decoder_1_out0
  Shifter #(.width(32)) shifter_1 (.in({32{1'b1}}), .\dist (object[25:21]), .out(shifter_1_out));
  Transistor #(.width(5)) transistor_1 (.in(object[25:21]), .out(transistor_1_out), .gate(comparator_1_eq));
  Transistor #(.\type ("n"), .width(5)) transistor_2 (.in(5'b00001), .out(transistor_1_out), .gate(comparator_1_eq));
  assign not_1_out = ~shifter_1_out;  // NOT_Gate not_1, 32 bits wide
  Adder #(.width(5)) adder_2 (
    .a(object[9:5]), .b(transistor_1_out), .out(adder_2_out), .cout(adder_2_cout));  // open: cin
  Multiplier #(.width(32)) multiplier_1 (.a(decoder_1_out0), .b(not_1_out), .out(multiplier_1_out));  // open: cin, cout
  Comparator #(.width(5), .mode("unsigned")) comparator_2 (
    .a(adder_2_out), .b(row), .gt(comparator_2_gt));  // open: eq, lt
  or or_1 (or_1_out, comparator_2_gt, adder_2_cout);
  or or_2 (or_2_out, comparator_3_eq, comparator_3_lt);
  Comparator #(.width(5), .mode("unsigned")) comparator_3 (
    .a(object[9:5]), .b(row), .eq(comparator_3_eq), .lt(comparator_3_lt));  // open: gt
  Transistor #(.width(32)) transistor_3 (.in(decoder_1_out0), .out(transistor_3_out), .gate(comparator_1_eq));
  Transistor #(.\type ("n"), .width(32)) transistor_4 (
    .in(multiplier_1_out), .out(transistor_3_out), .gate(comparator_1_eq));
  and and_1 (and_1_out, or_1_out, or_2_out);
  Transistor #(.width(32)) transistor_5 (.in({32{1'b0}}), .out(transistor_5_out), .gate(and_1_out));
  Transistor #(.\type ("n"), .width(32)) transistor_6 (.in(transistor_3_out), .out(transistor_5_out), .gate(and_1_out));
  assign out_4 = transistor_5_out | row_state;  // OR_Gate or_3, 32 bits wide
endmodule

module ball (
  input  [7:0] start_vx,
  input  [7:0] start_vy,
  input  [25:0] ball_data,
  input  Clock,
  input  Reset,
  output [25:0] Updated_ball
);

  wire [7:0] adder_2_out, multiplexer_1_out, multiplexer_2_out, shifter_1_out, shifter_2_out, velo_x_q,
       velo_y_q;

  Pull_Resistor pull_resistor_1 (.node(start_vx));
  Pull_Resistor pull_resistor_2 (.node(start_vy));
  // Probe on ball_data[1:0]
  // Probe on ball_data[25:18]
  // Probe on ball_data[9:2]
  // Probe on ball_data[17:10]
  Register velo_x (.D(multiplexer_1_out), .Q(velo_x_q), .clk(Clock));  // open: en, clr
  Multiplexer #(.width(8)) multiplexer_1 (
    .in0(velo_x_q), .in1(start_vx), .out(multiplexer_1_out), .sel(Reset));  // open: en
  Multiplexer #(.width(8)) multiplexer_2 (
    .in0(adder_2_out), .in1(start_vy), .out(multiplexer_2_out), .sel(Reset));  // open: en
  Shifter #(.shift("ar")) shifter_1 (.in(velo_x_q), .\dist (3'b110), .out(shifter_1_out));
  Adder adder_1 (.a(shifter_1_out), .b(ball_data[9:2]), .out(Updated_ball[9:2]));  // open: cin, cout
  Register velo_y (.D(multiplexer_2_out), .Q(velo_y_q), .clk(Clock));  // open: en, clr
  Pull_Resistor pull_resistor_3 (.node(Reset));
  Adder adder_2 (.a({8{1'b1}}), .b(velo_y_q), .out(adder_2_out));  // open: cin, cout
  Shifter #(.shift("ar")) shifter_2 (.in(velo_y_q), .\dist (3'b110), .out(shifter_2_out));
  Adder adder_3 (.a(shifter_2_out), .b(ball_data[17:10]), .out(Updated_ball[17:10]));  // open: cin, cout

  assign {Updated_ball[25:18], Updated_ball[1:0]} = {ball_data[25:18], ball_data[1:0]};

  // Other names for the same wires on the sheet: ball_type[1:0] = ball_data[1:0]; ball_size[7:0] = ball_data[25:18]
endmodule

module graphics1 (
  input  [25:0] in_1,
  input  in_2,
  input  in_3,
  output [31:0] out_4,
  output [31:0] out_5,
  output [31:0] out_6,
  output [31:0] out_7,
  output [31:0] out_8,
  output [31:0] out_9,
  output [31:0] out_10,
  output [31:0] out_11,
  output [31:0] out_12,
  output [31:0] out_13,
  output [31:0] out_14,
  output [31:0] out_15,
  output [31:0] out_16,
  output [31:0] out_17,
  output [31:0] out_18,
  output [31:0] out_19,
  output [31:0] out_20,
  output [31:0] out_21,
  output [31:0] out_22,
  output [31:0] out_23,
  output [31:0] out_24,
  output [31:0] out_25,
  output [31:0] out_26,
  output [31:0] out_27,
  output [31:0] out_28,
  output [31:0] out_29,
  output [31:0] out_30,
  output [31:0] out_31,
  output [31:0] out_32,
  output [31:0] out_33,
  output [31:0] out_34,
  output [31:0] out_35
);

  wire [31:0] graphics3_1_out_4, graphics3_2_out_4, graphics3_3_out_4, graphics3_4_out_4, graphics3_5_out_4,
       graphics3_6_out_4, graphics3_7_out_4, graphics3_8_out_4, graphics3_9_out_4, graphics3_10_out_4,
       graphics3_11_out_4, graphics3_12_out_4, graphics3_13_out_4, graphics3_14_out_4, graphics3_15_out_4,
       graphics3_16_out_4, graphics3_17_out_4, graphics3_18_out_4, graphics3_19_out_4, graphics3_20_out_4,
       graphics3_21_out_4, graphics3_22_out_4, graphics3_23_out_4, graphics3_24_out_4, graphics3_25_out_4,
       graphics3_26_out_4, graphics3_27_out_4, graphics3_28_out_4, graphics3_29_out_4, graphics3_30_out_4,
       graphics3_31_out_4, graphics3_32_out_4;

  graphics3 graphics3_1 (.object(in_1), .row({5{1'b0}}), .row_state(out_4), .out_4(graphics3_1_out_4));
  Register #(.width(32)) register_1 (.D(graphics3_1_out_4), .Q(out_4), .clk(in_2), .clr(in_3));  // open: en
  graphics3 graphics3_2 (.object(in_1), .row(5'b00001), .row_state(out_8), .out_4(graphics3_2_out_4));
  Register #(.width(32)) register_2 (.D(graphics3_2_out_4), .Q(out_8), .clk(in_2), .clr(in_3));  // open: en
  graphics3 graphics3_3 (.object(in_1), .row(5'b00010), .row_state(out_12), .out_4(graphics3_3_out_4));
  graphics3 graphics3_4 (.object(in_1), .row(5'b00011), .row_state(out_16), .out_4(graphics3_4_out_4));
  graphics3 graphics3_5 (.object(in_1), .row(5'b00100), .row_state(out_20), .out_4(graphics3_5_out_4));
  graphics3 graphics3_6 (.object(in_1), .row(5'b00101), .row_state(out_24), .out_4(graphics3_6_out_4));
  graphics3 graphics3_7 (.object(in_1), .row(5'b00110), .row_state(out_28), .out_4(graphics3_7_out_4));
  Register #(.width(32)) register_3 (.D(graphics3_3_out_4), .Q(out_12), .clk(in_2), .clr(in_3));  // open: en
  Register #(.width(32)) register_4 (.D(graphics3_4_out_4), .Q(out_16), .clk(in_2), .clr(in_3));  // open: en
  Register #(.width(32)) register_5 (.D(graphics3_5_out_4), .Q(out_20), .clk(in_2), .clr(in_3));  // open: en
  Register #(.width(32)) register_6 (.D(graphics3_6_out_4), .Q(out_24), .clk(in_2), .clr(in_3));  // open: en
  Register #(.width(32)) register_7 (.D(graphics3_7_out_4), .Q(out_28), .clk(in_2), .clr(in_3));  // open: en
  Register #(.width(32)) register_8 (.D(graphics3_8_out_4), .Q(out_32), .clk(in_2), .clr(in_3));  // open: en
  graphics3 graphics3_8 (.object(in_1), .row(5'b00111), .row_state(out_32), .out_4(graphics3_8_out_4));
  graphics3 graphics3_9 (.object(in_1), .row(5'b01000), .row_state(out_5), .out_4(graphics3_9_out_4));
  graphics3 graphics3_10 (.object(in_1), .row(5'b01001), .row_state(out_9), .out_4(graphics3_10_out_4));
  graphics3 graphics3_11 (.object(in_1), .row(5'b01010), .row_state(out_13), .out_4(graphics3_11_out_4));
  graphics3 graphics3_12 (.object(in_1), .row(5'b01011), .row_state(out_17), .out_4(graphics3_12_out_4));
  Register #(.width(32)) register_9 (.D(graphics3_9_out_4), .Q(out_5), .clk(in_2), .clr(in_3));  // open: en
  Register #(.width(32)) register_10 (.D(graphics3_10_out_4), .Q(out_9), .clk(in_2), .clr(in_3));  // open: en
  Register #(.width(32)) register_11 (.D(graphics3_11_out_4), .Q(out_13), .clk(in_2), .clr(in_3));  // open: en
  Register #(.width(32)) register_12 (.D(graphics3_12_out_4), .Q(out_17), .clk(in_2), .clr(in_3));  // open: en
  graphics3 graphics3_13 (.object(in_1), .row(5'b01100), .row_state(out_21), .out_4(graphics3_13_out_4));
  Register #(.width(32)) register_13 (.D(graphics3_13_out_4), .Q(out_21), .clk(in_2), .clr(in_3));  // open: en
  Register #(.width(32)) register_14 (.D(graphics3_14_out_4), .Q(out_25), .clk(in_2), .clr(in_3));  // open: en
  graphics3 graphics3_14 (.object(in_1), .row(5'b01101), .row_state(out_25), .out_4(graphics3_14_out_4));
  graphics3 graphics3_15 (.object(in_1), .row(5'b01110), .row_state(out_29), .out_4(graphics3_15_out_4));
  Register #(.width(32)) register_15 (.D(graphics3_15_out_4), .Q(out_29), .clk(in_2), .clr(in_3));  // open: en
  graphics3 graphics3_16 (.object(in_1), .row(5'b01111), .row_state(out_33), .out_4(graphics3_16_out_4));
  Register #(.width(32)) register_16 (.D(graphics3_16_out_4), .Q(out_33), .clk(in_2), .clr(in_3));  // open: en
  graphics3 graphics3_17 (.object(in_1), .row(5'b10000), .row_state(out_6), .out_4(graphics3_17_out_4));
  graphics3 graphics3_18 (.object(in_1), .row(5'b10001), .row_state(out_10), .out_4(graphics3_18_out_4));
  Register #(.width(32)) register_17 (.D(graphics3_17_out_4), .Q(out_6), .clk(in_2), .clr(in_3));  // open: en
  Register #(.width(32)) register_18 (.D(graphics3_18_out_4), .Q(out_10), .clk(in_2), .clr(in_3));  // open: en
  graphics3 graphics3_19 (.object(in_1), .row(5'b10010), .row_state(out_14), .out_4(graphics3_19_out_4));
  Register #(.width(32)) register_19 (.D(graphics3_19_out_4), .Q(out_14), .clk(in_2), .clr(in_3));  // open: en
  graphics3 graphics3_20 (.object(in_1), .row(5'b10011), .row_state(out_18), .out_4(graphics3_20_out_4));
  Register #(.width(32)) register_20 (.D(graphics3_20_out_4), .Q(out_18), .clk(in_2), .clr(in_3));  // open: en
  Register #(.width(32)) register_21 (.D(graphics3_21_out_4), .Q(out_22), .clk(in_2), .clr(in_3));  // open: en
  graphics3 graphics3_21 (.object(in_1), .row(5'b10100), .row_state(out_22), .out_4(graphics3_21_out_4));
  graphics3 graphics3_22 (.object(in_1), .row(5'b10101), .row_state(out_26), .out_4(graphics3_22_out_4));
  graphics3 graphics3_23 (.object(in_1), .row(5'b10110), .row_state(out_30), .out_4(graphics3_23_out_4));
  graphics3 graphics3_24 (.object(in_1), .row(5'b10111), .row_state(out_34), .out_4(graphics3_24_out_4));
  Register #(.width(32)) register_22 (.D(graphics3_22_out_4), .Q(out_26), .clk(in_2), .clr(in_3));  // open: en
  Register #(.width(32)) register_23 (.D(graphics3_23_out_4), .Q(out_30), .clk(in_2), .clr(in_3));  // open: en
  Register #(.width(32)) register_24 (.D(graphics3_24_out_4), .Q(out_34), .clk(in_2), .clr(in_3));  // open: en
  graphics3 graphics3_25 (.object(in_1), .row(5'b11000), .row_state(out_7), .out_4(graphics3_25_out_4));
  Register #(.width(32)) register_25 (.D(graphics3_25_out_4), .Q(out_7), .clk(in_2), .clr(in_3));  // open: en
  Register #(.width(32)) register_26 (.D(graphics3_26_out_4), .Q(out_11), .clk(in_2), .clr(in_3));  // open: en
  graphics3 graphics3_26 (.object(in_1), .row(5'b11001), .row_state(out_11), .out_4(graphics3_26_out_4));
  graphics3 graphics3_27 (.object(in_1), .row(5'b11010), .row_state(out_15), .out_4(graphics3_27_out_4));
  graphics3 graphics3_28 (.object(in_1), .row(5'b11011), .row_state(out_19), .out_4(graphics3_28_out_4));
  graphics3 graphics3_29 (.object(in_1), .row(5'b11100), .row_state(out_23), .out_4(graphics3_29_out_4));
  graphics3 graphics3_30 (.object(in_1), .row(5'b11101), .row_state(out_27), .out_4(graphics3_30_out_4));
  graphics3 graphics3_31 (.object(in_1), .row(5'b11110), .row_state(out_31), .out_4(graphics3_31_out_4));
  Register #(.width(32)) register_27 (.D(graphics3_27_out_4), .Q(out_15), .clk(in_2), .clr(in_3));  // open: en
  Register #(.width(32)) register_28 (.D(graphics3_28_out_4), .Q(out_19), .clk(in_2), .clr(in_3));  // open: en
  Register #(.width(32)) register_29 (.D(graphics3_29_out_4), .Q(out_23), .clk(in_2), .clr(in_3));  // open: en
  Register #(.width(32)) register_30 (.D(graphics3_30_out_4), .Q(out_27), .clk(in_2), .clr(in_3));  // open: en
  Register #(.width(32)) register_31 (.D(graphics3_31_out_4), .Q(out_31), .clk(in_2), .clr(in_3));  // open: en
  graphics3 graphics3_32 (.object(in_1), .row({5{1'b1}}), .row_state(out_35), .out_4(graphics3_32_out_4));
  Register #(.width(32)) register_32 (.D(graphics3_32_out_4), .Q(out_35), .clk(in_2), .clr(in_3));  // open: en
endmodule
