// Logisim project pinball v0+.circ as structural Verilog: 9 circuits, main circuit main
module main (
);

  wire ball_1_collision_happened, ball_1_finished, ball_1_out_of_screen, buffer_1_out, button1,
       button1pressed, button2, button2pressed, clock_1_out, counter_1_carry, counter_2_carry, counter_3_q,
       counter_4_carry, counter_6_carry, counter_7_carry, LOAD_GAME_out, loading, loading_clock,
       loading_door, not_1_out, or_1_out, or_2_out, or_3_out, reset_ball_out, RESET_out;
  wire [1:0] ball_1_active_screen;
  wire [2:0] multiplexer_1_out, object_collide_num, object_load;
  wire [3:0] counter_5_q, counter_6_q;
  wire [4:0] ball_1_ball_x, ball_1_ball_y, column_draw, column_load, multiplexer_4_out;
  wire [25:0] door1, door2, object_collide1, object_collide2, object_collide3, object_collide4, rom_1_data,
       rom_2_data;
  wire [31:0] draw_object_1_result, draw_object_2_result, draw_object_3_result, draw_object_4_result,
       graphics_man_1_screen_1, graphics_man_1_screen_2, graphics_man_1_screen_3, graphics_man_1_screen_4,
       screen1, screen2, screen3, screen4, screen_memo_1_out_4, screen_memo_1_out_5, screen_memo_1_out_6,
       screen_memo_1_out_7, screen_memo_1_out_8, screen_memo_1_out_9, screen_memo_1_out_10,
       screen_memo_1_out_11, screen_memo_1_out_12, screen_memo_1_out_13, screen_memo_1_out_14,
       screen_memo_1_out_15, screen_memo_1_out_16, screen_memo_1_out_17, screen_memo_1_out_18,
       screen_memo_1_out_19, screen_memo_1_out_20, screen_memo_1_out_21, screen_memo_1_out_22,
       screen_memo_1_out_23, screen_memo_1_out_24, screen_memo_1_out_25, screen_memo_1_out_26,
       screen_memo_1_out_27, screen_memo_1_out_28, screen_memo_1_out_29, screen_memo_1_out_30,
       screen_memo_1_out_31, screen_memo_1_out_32, screen_memo_1_out_33, screen_memo_1_out_34,
       screen_memo_1_out_35, screen_memo_2_out_4, screen_memo_2_out_5, screen_memo_2_out_6,
       screen_memo_2_out_7, screen_memo_2_out_8, screen_memo_2_out_9, screen_memo_2_out_10,
       screen_memo_2_out_11, screen_memo_2_out_12, screen_memo_2_out_13, screen_memo_2_out_14,
       screen_memo_2_out_15, screen_memo_2_out_16, screen_memo_2_out_17, screen_memo_2_out_18,
       screen_memo_2_out_19, screen_memo_2_out_20, screen_memo_2_out_21, screen_memo_2_out_22,
       screen_memo_2_out_23, screen_memo_2_out_24, screen_memo_2_out_25, screen_memo_2_out_26,
       screen_memo_2_out_27, screen_memo_2_out_28, screen_memo_2_out_29, screen_memo_2_out_30,
       screen_memo_2_out_31, screen_memo_2_out_32, screen_memo_2_out_33, screen_memo_2_out_34,
       screen_memo_2_out_35, screen_memo_3_out_4, screen_memo_3_out_5, screen_memo_3_out_6,
       screen_memo_3_out_7, screen_memo_3_out_8, screen_memo_3_out_9, screen_memo_3_out_10,
       screen_memo_3_out_11, screen_memo_3_out_12, screen_memo_3_out_13, screen_memo_3_out_14,
       screen_memo_3_out_15, screen_memo_3_out_16, screen_memo_3_out_17, screen_memo_3_out_18,
       screen_memo_3_out_19, screen_memo_3_out_20, screen_memo_3_out_21, screen_memo_3_out_22,
       screen_memo_3_out_23, screen_memo_3_out_24, screen_memo_3_out_25, screen_memo_3_out_26,
       screen_memo_3_out_27, screen_memo_3_out_28, screen_memo_3_out_29, screen_memo_3_out_30,
       screen_memo_3_out_31, screen_memo_3_out_32, screen_memo_3_out_33, screen_memo_3_out_34,
       screen_memo_3_out_35, screen_memo_4_out_4, screen_memo_4_out_5, screen_memo_4_out_6,
       screen_memo_4_out_7, screen_memo_4_out_8, screen_memo_4_out_9, screen_memo_4_out_10,
       screen_memo_4_out_11, screen_memo_4_out_12, screen_memo_4_out_13, screen_memo_4_out_14,
       screen_memo_4_out_15, screen_memo_4_out_16, screen_memo_4_out_17, screen_memo_4_out_18,
       screen_memo_4_out_19, screen_memo_4_out_20, screen_memo_4_out_21, screen_memo_4_out_22,
       screen_memo_4_out_23, screen_memo_4_out_24, screen_memo_4_out_25, screen_memo_4_out_26,
       screen_memo_4_out_27, screen_memo_4_out_28, screen_memo_4_out_29, screen_memo_4_out_30,
       screen_memo_4_out_31, screen_memo_4_out_32, screen_memo_4_out_33, screen_memo_4_out_34,
       screen_memo_4_out_35;

  Clock clock_1 (.out(clock_1_out));
  and and_1 (loading_clock, clock_1_out, loading);
  buf buffer_1 (buffer_1_out, buffer_1_out);
  Counter #(.width(5), .max('h1f)) counter_1 (
    .Q(column_draw), .carry(counter_1_carry), .clk(clock_1_out));  // open: load, D, count, clr
  Multiplexer #(.width(3), .enable("false")) multiplexer_1 (
    .in0(object_collide_num), .in1(object_load), .out(multiplexer_1_out), .sel(loading));
  D_Flip_Flop d_ff_1 (.clk(counter_1_carry), .D(1'b0), .Q(button1), .preset(button1pressed));  // open: Qn, en, reset
  ball ball_1 (
    .RESET(reset_ball_out), .wall_on_screen_4(object_collide1), .wall_on_screen_3(object_collide2),
    .wall_on_screen_2(object_collide3), .wall_on_screen_1(object_collide4),
    .active_screen(ball_1_active_screen), .ball_x(ball_1_ball_x), .ball_y(ball_1_ball_y),
    .next_wall(or_1_out), .collision_happened(ball_1_collision_happened), .finished(ball_1_finished),
    .out_of_screen(ball_1_out_of_screen), .update_ball_state(counter_2_carry));
  or or_1 (or_1_out, ball_1_finished, reset_ball_out);
  D_Flip_Flop d_ff_2 (.clk(counter_1_carry), .D(1'b0), .Q(button2), .preset(button2pressed));  // open: Qn, en, reset
  Comparator #(.width(3)) comparator_1 (.a(3'b111), .b(multiplexer_1_out), .eq(loading_door));  // open: gt, lt
  ROM #(.addrWidth(3), .dataWidth(26)) rom_1 (.addr(multiplexer_1_out), .data(rom_1_data));  // open: sel
  ROM #(.addrWidth(3), .dataWidth(26)) rom_2 (.addr(multiplexer_1_out), .data(rom_2_data));  // open: sel
  ROM #(.addrWidth(3), .dataWidth(26)) rom_3 (.addr(multiplexer_1_out), .data(object_collide3));  // open: sel
  ROM #(.addrWidth(3), .dataWidth(26)) rom_4 (.addr(multiplexer_1_out), .data(object_collide4));  // open: sel
  // Probe on ball_1_ball_y
  Counter #(.width(3), .max('h7)) counter_2 (
    .Q(object_collide_num), .carry(counter_2_carry), .clk(ball_1_finished), .clr(reset_ball_out));  // open: load, D, count
  Register #(.width(26), .trigger("falling")) register_1 (
    .D(rom_1_data), .en(loading), .Q(door1), .clk(loading_door));  // open: clr
  Register #(.width(26), .trigger("falling")) register_2 (
    .D(rom_2_data), .en(loading), .Q(door2), .clk(loading_door));  // open: clr
  // Probe on ball_1_ball_x
  // Probe on ball_1_active_screen
  Multiplexer #(.width(26)) multiplexer_2 (
    .in0(rom_1_data), .in1({26{1'b0}}), .out(object_collide1), .sel(loading_door));  // open: en
  Multiplexer #(.width(26)) multiplexer_3 (
    .in0(rom_2_data), .in1({26{1'b0}}), .out(object_collide2), .sel(loading_door));  // open: en
  graphics_man graphics_man_1 (
    .active_screen(ball_1_active_screen), .ball_x(ball_1_ball_x), .ball_y(ball_1_ball_y), .active_1(button1),
    .door_1(door1), .active_2(button2), .door_2(door2), .state0(screen1), .state1(screen2), .state2(screen3),
    .state3(screen4), .x(column_draw), .screen_1(graphics_man_1_screen_1),
    .screen_2(graphics_man_1_screen_2), .screen_3(graphics_man_1_screen_3), .screen_4(graphics_man_1_screen_4));
  Multiplexer #(.width(5), .enable("false")) multiplexer_4 (
    .in0(column_draw), .in1(column_load), .out(multiplexer_4_out), .sel(loading));
  draw_object draw_object_1 (
    .object(object_collide1), .row_x(multiplexer_4_out), .base(screen1), .result(draw_object_1_result));
  draw_object draw_object_2 (
    .object(object_collide2), .row_x(multiplexer_4_out), .base(screen2), .result(draw_object_2_result));
  draw_object draw_object_3 (
    .object(object_collide3), .row_x(multiplexer_4_out), .base(screen3), .result(draw_object_3_result));
  draw_object draw_object_4 (
    .object(object_collide4), .row_x(multiplexer_4_out), .base(screen4), .result(draw_object_4_result));
  LED led_1 (.in(counter_3_q));
  Counter #(.width(1), .max('h1), .trigger("falling")) counter_3 (
    .Q(counter_3_q), .clk(ball_1_out_of_screen));  // open: load, D, count, carry, clr
  Counter #(.width(3), .max('h7), .trigger("falling")) counter_4 (
    .Q(object_load), .carry(counter_4_carry), .clk(loading_clock), .clr(not_1_out));  // open: load, D, count
  Hex_Digit_Display hex_digit_display_1 (.value(counter_5_q));  // open: dp
  Hex_Digit_Display hex_digit_display_2 (.value(counter_6_q));  // open: dp
  Counter #(.width(4), .max('h9), .trigger("falling")) counter_5 (
    .Q(counter_5_q), .clk(counter_6_carry), .clr(reset_ball_out));  // open: load, D, count, carry
  Counter #(.width(4), .max('h9)) counter_6 (
    .Q(counter_6_q), .carry(counter_6_carry), .clk(ball_1_collision_happened), .clr(reset_ball_out));  // open: load, D, count
  RAM #(.addrWidth(5), .dataWidth(32), .bus("separate")) ram_1 (
    .addr(multiplexer_4_out), .din(draw_object_1_result), .data(screen1), .clk(loading_clock), .clr(or_2_out));  // open: str, sel, ld
  RAM #(.addrWidth(5), .dataWidth(32), .bus("separate")) ram_2 (
    .addr(multiplexer_4_out), .din(draw_object_2_result), .data(screen2), .clk(loading_clock), .clr(or_2_out));  // open: str, sel, ld
  RAM #(.addrWidth(5), .dataWidth(32), .bus("separate")) ram_3 (
    .addr(multiplexer_4_out), .din(draw_object_3_result), .data(screen3), .clk(loading_clock), .clr(or_2_out));  // open: str, sel, ld
  RAM #(.addrWidth(5), .dataWidth(32), .bus("separate")) ram_4 (
    .addr(multiplexer_4_out), .din(draw_object_4_result), .data(screen4), .clk(loading_clock), .clr(or_2_out));  // open: str, sel, ld
  Counter #(.width(5), .max('h1f), .trigger("falling")) counter_7 (
    .Q(column_load), .carry(counter_7_carry), .clk(counter_4_carry), .clr(not_1_out));  // open: load, D, count
  DotMatrix #(.matrixcols(32), .matrixrows(32)) dotmatrix_1 (
    .col0(screen_memo_1_out_4), .col1(screen_memo_1_out_5), .col2(screen_memo_1_out_6),
    .col3(screen_memo_1_out_7), .col4(screen_memo_1_out_8), .col5(screen_memo_1_out_9),
    .col6(screen_memo_1_out_10), .col7(screen_memo_1_out_11), .col8(screen_memo_1_out_12),
    .col9(screen_memo_1_out_13), .col10(screen_memo_1_out_14), .col11(screen_memo_1_out_15),
    .col12(screen_memo_1_out_16), .col13(screen_memo_1_out_17), .col14(screen_memo_1_out_18),
    .col15(screen_memo_1_out_19), .col16(screen_memo_1_out_20), .col17(screen_memo_1_out_21),
    .col18(screen_memo_1_out_22), .col19(screen_memo_1_out_23), .col20(screen_memo_1_out_24),
    .col21(screen_memo_1_out_25), .col22(screen_memo_1_out_26), .col23(screen_memo_1_out_27),
    .col24(screen_memo_1_out_28), .col25(screen_memo_1_out_29), .col26(screen_memo_1_out_30),
    .col27(screen_memo_1_out_31), .col28(screen_memo_1_out_32), .col29(screen_memo_1_out_33),
    .col30(screen_memo_1_out_34), .col31(screen_memo_1_out_35));
  screen_memo screen_memo_1 (
    .new_column(graphics_man_1_screen_3), .out_4(screen_memo_1_out_4), .out_5(screen_memo_1_out_5),
    .out_6(screen_memo_1_out_6), .out_7(screen_memo_1_out_7), .out_8(screen_memo_1_out_8),
    .out_9(screen_memo_1_out_9), .out_10(screen_memo_1_out_10), .out_11(screen_memo_1_out_11),
    .out_12(screen_memo_1_out_12), .out_13(screen_memo_1_out_13), .out_14(screen_memo_1_out_14),
    .out_15(screen_memo_1_out_15), .out_16(screen_memo_1_out_16), .out_17(screen_memo_1_out_17),
    .out_18(screen_memo_1_out_18), .out_19(screen_memo_1_out_19), .out_20(screen_memo_1_out_20),
    .out_21(screen_memo_1_out_21), .out_22(screen_memo_1_out_22), .out_23(screen_memo_1_out_23),
    .out_24(screen_memo_1_out_24), .out_25(screen_memo_1_out_25), .out_26(screen_memo_1_out_26),
    .out_27(screen_memo_1_out_27), .out_28(screen_memo_1_out_28), .out_29(screen_memo_1_out_29),
    .out_30(screen_memo_1_out_30), .out_31(screen_memo_1_out_31), .out_32(screen_memo_1_out_32),
    .out_33(screen_memo_1_out_33), .out_34(screen_memo_1_out_34), .out_35(screen_memo_1_out_35),
    .clock(clock_1_out), .x(column_draw));
  screen_memo screen_memo_2 (
    .new_column(graphics_man_1_screen_1), .out_4(screen_memo_2_out_4), .out_5(screen_memo_2_out_5),
    .out_6(screen_memo_2_out_6), .out_7(screen_memo_2_out_7), .out_8(screen_memo_2_out_8),
    .out_9(screen_memo_2_out_9), .out_10(screen_memo_2_out_10), .out_11(screen_memo_2_out_11),
    .out_12(screen_memo_2_out_12), .out_13(screen_memo_2_out_13), .out_14(screen_memo_2_out_14),
    .out_15(screen_memo_2_out_15), .out_16(screen_memo_2_out_16), .out_17(screen_memo_2_out_17),
    .out_18(screen_memo_2_out_18), .out_19(screen_memo_2_out_19), .out_20(screen_memo_2_out_20),
    .out_21(screen_memo_2_out_21), .out_22(screen_memo_2_out_22), .out_23(screen_memo_2_out_23),
    .out_24(screen_memo_2_out_24), .out_25(screen_memo_2_out_25), .out_26(screen_memo_2_out_26),
    .out_27(screen_memo_2_out_27), .out_28(screen_memo_2_out_28), .out_29(screen_memo_2_out_29),
    .out_30(screen_memo_2_out_30), .out_31(screen_memo_2_out_31), .out_32(screen_memo_2_out_32),
    .out_33(screen_memo_2_out_33), .out_34(screen_memo_2_out_34), .out_35(screen_memo_2_out_35),
    .clock(clock_1_out), .x(column_draw));
  DotMatrix #(.matrixcols(32), .matrixrows(32)) dotmatrix_2 (
    .col0(screen_memo_2_out_4), .col1(screen_memo_2_out_5), .col2(screen_memo_2_out_6),
    .col3(screen_memo_2_out_7), .col4(screen_memo_2_out_8), .col5(screen_memo_2_out_9),
    .col6(screen_memo_2_out_10), .col7(screen_memo_2_out_11), .col8(screen_memo_2_out_12),
    .col9(screen_memo_2_out_13), .col10(screen_memo_2_out_14), .col11(screen_memo_2_out_15),
    .col12(screen_memo_2_out_16), .col13(screen_memo_2_out_17), .col14(screen_memo_2_out_18),
    .col15(screen_memo_2_out_19), .col16(screen_memo_2_out_20), .col17(screen_memo_2_out_21),
    .col18(screen_memo_2_out_22), .col19(screen_memo_2_out_23), .col20(screen_memo_2_out_24),
    .col21(screen_memo_2_out_25), .col22(screen_memo_2_out_26), .col23(screen_memo_2_out_27),
    .col24(screen_memo_2_out_28), .col25(screen_memo_2_out_29), .col26(screen_memo_2_out_30),
    .col27(screen_memo_2_out_31), .col28(screen_memo_2_out_32), .col29(screen_memo_2_out_33),
    .col30(screen_memo_2_out_34), .col31(screen_memo_2_out_35));
  or or_2 (or_2_out, RESET_out, LOAD_GAME_out);
  Counter #(.width(1), .max('h1), .trigger("falling")) counter_8 (
    .Q(loading), .clk(or_3_out));  // open: load, D, count, carry, clr
  or or_3 (or_3_out, counter_7_carry, LOAD_GAME_out);
  not not_1 (not_1_out, loading);
  Button RESET (.out(RESET_out));
  Button reset_ball (.out(reset_ball_out));
  Button left (.out(button1pressed));
  Button LOAD_GAME (.out(LOAD_GAME_out));
  screen_memo screen_memo_3 (
    .new_column(graphics_man_1_screen_4), .out_4(screen_memo_3_out_4), .out_5(screen_memo_3_out_5),
    .out_6(screen_memo_3_out_6), .out_7(screen_memo_3_out_7), .out_8(screen_memo_3_out_8),
    .out_9(screen_memo_3_out_9), .out_10(screen_memo_3_out_10), .out_11(screen_memo_3_out_11),
    .out_12(screen_memo_3_out_12), .out_13(screen_memo_3_out_13), .out_14(screen_memo_3_out_14),
    .out_15(screen_memo_3_out_15), .out_16(screen_memo_3_out_16), .out_17(screen_memo_3_out_17),
    .out_18(screen_memo_3_out_18), .out_19(screen_memo_3_out_19), .out_20(screen_memo_3_out_20),
    .out_21(screen_memo_3_out_21), .out_22(screen_memo_3_out_22), .out_23(screen_memo_3_out_23),
    .out_24(screen_memo_3_out_24), .out_25(screen_memo_3_out_25), .out_26(screen_memo_3_out_26),
    .out_27(screen_memo_3_out_27), .out_28(screen_memo_3_out_28), .out_29(screen_memo_3_out_29),
    .out_30(screen_memo_3_out_30), .out_31(screen_memo_3_out_31), .out_32(screen_memo_3_out_32),
    .out_33(screen_memo_3_out_33), .out_34(screen_memo_3_out_34), .out_35(screen_memo_3_out_35),
    .clock(clock_1_out), .x(column_draw));
  DotMatrix #(.matrixcols(32), .matrixrows(32)) dotmatrix_3 (
    .col0(screen_memo_3_out_4), .col1(screen_memo_3_out_5), .col2(screen_memo_3_out_6),
    .col3(screen_memo_3_out_7), .col4(screen_memo_3_out_8), .col5(screen_memo_3_out_9),
    .col6(screen_memo_3_out_10), .col7(screen_memo_3_out_11), .col8(screen_memo_3_out_12),
    .col9(screen_memo_3_out_13), .col10(screen_memo_3_out_14), .col11(screen_memo_3_out_15),
    .col12(screen_memo_3_out_16), .col13(screen_memo_3_out_17), .col14(screen_memo_3_out_18),
    .col15(screen_memo_3_out_19), .col16(screen_memo_3_out_20), .col17(screen_memo_3_out_21),
    .col18(screen_memo_3_out_22), .col19(screen_memo_3_out_23), .col20(screen_memo_3_out_24),
    .col21(screen_memo_3_out_25), .col22(screen_memo_3_out_26), .col23(screen_memo_3_out_27),
    .col24(screen_memo_3_out_28), .col25(screen_memo_3_out_29), .col26(screen_memo_3_out_30),
    .col27(screen_memo_3_out_31), .col28(screen_memo_3_out_32), .col29(screen_memo_3_out_33),
    .col30(screen_memo_3_out_34), .col31(screen_memo_3_out_35));
  screen_memo screen_memo_4 (
    .new_column(graphics_man_1_screen_2), .out_4(screen_memo_4_out_4), .out_5(screen_memo_4_out_5),
    .out_6(screen_memo_4_out_6), .out_7(screen_memo_4_out_7), .out_8(screen_memo_4_out_8),
    .out_9(screen_memo_4_out_9), .out_10(screen_memo_4_out_10), .out_11(screen_memo_4_out_11),
    .out_12(screen_memo_4_out_12), .out_13(screen_memo_4_out_13), .out_14(screen_memo_4_out_14),
    .out_15(screen_memo_4_out_15), .out_16(screen_memo_4_out_16), .out_17(screen_memo_4_out_17),
    .out_18(screen_memo_4_out_18), .out_19(screen_memo_4_out_19), .out_20(screen_memo_4_out_20),
    .out_21(screen_memo_4_out_21), .out_22(screen_memo_4_out_22), .out_23(screen_memo_4_out_23),
    .out_24(screen_memo_4_out_24), .out_25(screen_memo_4_out_25), .out_26(screen_memo_4_out_26),
    .out_27(screen_memo_4_out_27), .out_28(screen_memo_4_out_28), .out_29(screen_memo_4_out_29),
    .out_30(screen_memo_4_out_30), .out_31(screen_memo_4_out_31), .out_32(screen_memo_4_out_32),
    .out_33(screen_memo_4_out_33), .out_34(screen_memo_4_out_34), .out_35(screen_memo_4_out_35),
    .clock(clock_1_out), .x(column_draw));
  DotMatrix #(.matrixcols(32), .matrixrows(32)) dotmatrix_4 (
    .col0(screen_memo_4_out_4), .col1(screen_memo_4_out_5), .col2(screen_memo_4_out_6),
    .col3(screen_memo_4_out_7), .col4(screen_memo_4_out_8), .col5(screen_memo_4_out_9),
    .col6(screen_memo_4_out_10), .col7(screen_memo_4_out_11), .col8(screen_memo_4_out_12),
    .col9(screen_memo_4_out_13), .col10(screen_memo_4_out_14), .col11(screen_memo_4_out_15),
    .col12(screen_memo_4_out_16), .col13(screen_memo_4_out_17), .col14(screen_memo_4_out_18),
    .col15(screen_memo_4_out_19), .col16(screen_memo_4_out_20), .col17(screen_memo_4_out_21),
    .col18(screen_memo_4_out_22), .col19(screen_memo_4_out_23), .col20(screen_memo_4_out_24),
    .col21(screen_memo_4_out_25), .col22(screen_memo_4_out_26), .col23(screen_memo_4_out_27),
    .col24(screen_memo_4_out_28), .col25(screen_memo_4_out_29), .col26(screen_memo_4_out_30),
    .col27(screen_memo_4_out_31), .col28(screen_memo_4_out_32), .col29(screen_memo_4_out_33),
    .col30(screen_memo_4_out_34), .col31(screen_memo_4_out_35));
  Button right (.out(button2pressed));

  // Notes on the sheet:
  //   buffer_1 drives only 1 and floats otherwise
  //   Data loader
  //   contents of rom_1 (hex, n*v repeats v):
  //   0 3100f00 1101000 3101f10 0 0 0 100010
  //   contents of rom_2 (hex, n*v repeats v):
  //   0 2080010 1080818 2081018 108181f 2101000 0 100000
  //   contents of rom_3 (hex, n*v repeats v):
  //   0 2050000 1050505 2160a05 51f1b 0 0 2100010
  //   contents of rom_4 (hex, n*v repeats v):
  //   0 110001f 3101f10 101f00 3100f00
  //   todo: make it reset everything
  //   lose indicator
  //   SCORE
endmodule

module ball (
  input  update_ball_state,
  input  RESET,
  input  [25:0] wall_on_screen_1,
  input  [25:0] wall_on_screen_2,
  input  [25:0] wall_on_screen_3,
  input  [25:0] wall_on_screen_4,
  input  next_wall,
  output [1:0] active_screen,
  output [4:0] ball_x,
  output [4:0] ball_y,
  output out_of_screen,
  output collision_happened,
  output finished
);

  wire and_1_out, buffer_1_out, buffer_2_out, buffer_3_out, buffer_4_out, cdm_8_mark5_1_p1, cdm_8_mark5_1_p2,
       cdm_8_mark5_1_p4, cdm_8_mark5_1_p5, cdm_8_mark5_1_p6, cdm_8_mark5_1_p7, cdm_8_mark5_1_p8,
       cdm_8_mark5_1_p9, cl, clock_2_out, code, counter_2_carry, data, I_Osel, In_Out_prime, mem,
       move_1_owf_x, move_1_owf_y, nand_1_out, not_1_out, not_2_out, or_1_out, RAM, undriven, undriven_2,
       write;
  wire [1:0] ball_x_t, ball_y_t;
  wire [3:0] I_Oadr;
  wire [7:0] bit_extender_1_out, bit_extender_2_out, bit_extender_3_out, bit_extender_4_out,
       bit_extender_5_out, cdm_8_mark5_1_p13, cdm_8_mark5_1_p14, demultiplexer_1_out1, demultiplexer_1_out2,
       I_Odat, new_speed_x, new_speed_y, speed_y, transform_1_x_2, transform_1_y_2, transform_2_x_2,
       transform_2_y_2, transform_3_x_2, transform_3_y_2;
  wire [7:1] collision_q, finished_q;
  wire [7:4] cdm_8_mark5_1_p12;
  wire [25:0] multiplexer_1_out;
  wire [31:0] counter_1_q, multiplexer_2_out, multiplexer_3_out, new_ball_data;

  Multiplexer #(.select(2), .width(26)) multiplexer_1 (
    .in0(wall_on_screen_1), .in1(wall_on_screen_2), .in2(wall_on_screen_3), .in3(wall_on_screen_4),
    .out(multiplexer_1_out), .sel(active_screen));  // open: en
  Multiplexer #(.width(32)) multiplexer_2 (
    .in0({active_screen[1], ball_y, ball_y_t, active_screen[0], ball_x, ball_x_t, new_speed_y, new_speed_x}),
    .in1(new_ball_data), .out(multiplexer_2_out), .sel(update_ball_state));  // open: en
  Multiplexer #(.width(32)) multiplexer_3 (
    .in0(multiplexer_2_out), .in1(32'h8080ffff), .out(multiplexer_3_out), .sel(RESET));  // open: en
  // Probe on {active_screen[0], ball_x, ball_x_t}
  // Probe on {active_screen[1], ball_y, ball_y_t}
  // Probe on new_ball_data[7:0]
  // Probe on speed_y
  Register #(.width(32), .trigger("falling")) ball_data (
    .D(multiplexer_3_out),
    .Q({active_screen[1], ball_y, ball_y_t, active_screen[0], ball_x, ball_x_t, speed_y, new_ball_data[7:0]}),
    .clk(or_1_out));  // open: en, clr
  or or_1 (or_1_out, RESET, finished);
  assign bit_extender_1_out = {{3{1'b0}}, ball_x};  // Bit_Extender bit_extender_1
  assign bit_extender_2_out = {{3{1'b0}}, ball_y};  // Bit_Extender bit_extender_2
  assign bit_extender_3_out = {{5{new_ball_data[7]}}, new_ball_data[7:5]};  // Bit_Extender bit_extender_3
  assign bit_extender_4_out = {{5{speed_y[7]}}, speed_y[7:5]};  // Bit_Extender bit_extender_4
  // Probe on multiplexer_1_out[25:24]
  // Probe on multiplexer_1_out[7:0]
  // Probe on multiplexer_1_out[15:8]
  // Probe on multiplexer_1_out[23:16]
  // Probe on active_screen
  // Probe on bit_extender_1_out
  // Probe on bit_extender_2_out
  // Probe on bit_extender_3_out
  // Probe on bit_extender_4_out
  buf buffer_1 (buffer_1_out, buffer_1_out);
  transform transform_1 (
    .\type (multiplexer_1_out[25:24]), .y(bit_extender_2_out), .x_2(transform_1_x_2), .x(bit_extender_1_out),
    .y_2(transform_1_y_2), .usigned(1'b1));
  transform transform_2 (
    .\type (multiplexer_1_out[25:24]), .y(bit_extender_4_out), .x_2(transform_2_x_2), .x(bit_extender_3_out),
    .y_2(transform_2_y_2), .usigned(1'b0));
  transform transform_3 (
    .\type (multiplexer_1_out[25:24]), .y(multiplexer_1_out[15:8]), .x_2(transform_3_x_2),
    .x(multiplexer_1_out[7:0]), .y_2(transform_3_y_2), .usigned(1'b1));
  or or_2 (out_of_screen, move_1_owf_x, move_1_owf_y);
  // Probe on transform_1_x_2
  // Probe on transform_1_y_2
  // Probe on transform_2_x_2
  // Probe on transform_2_y_2
  // Probe on transform_3_x_2
  // Probe on transform_3_y_2
  Adder adder_1 (.a({8{1'b1}}), .b(speed_y), .out(new_ball_data[15:8]));  // open: cin, cout
  move move_1 (
    .start_vx(new_ball_data[7:0]), .start_vy(speed_y), .start_ball_x({active_screen[0], ball_x, ball_x_t}),
    .start_ball_y({active_screen[1], ball_y, ball_y_t}), .owf_x(move_1_owf_x), .owf_y(move_1_owf_y),
    .result_x(new_ball_data[23:16]), .result_y(new_ball_data[31:24]));
  assign bit_extender_5_out = {{7{1'b0}}, next_wall};  // Bit_Extender bit_extender_5
  // Probe on cdm_8_mark5_1_p1
  buf buffer_2 (buffer_2_out, buffer_2_out);
  // Probe on cdm_8_mark5_1_p2
  // Probe on cdm_8_mark5_1_p4
  // Probe on cdm_8_mark5_1_p5
  // Probe on cdm_8_mark5_1_p6
  Clock clock_1 (.out(cl));
  and and_1 (and_1_out, I_Osel, In_Out_prime);
  Multiplexer #(.select(4), .width(8)) multiplexer_4 (
    .in1(bit_extender_5_out), .in2(transform_1_x_2), .in3(transform_3_x_2), .in4(multiplexer_1_out[23:16]),
    .in5(transform_1_y_2), .in6(transform_3_y_2), .in7(transform_2_y_2), .out(I_Odat), .sel(I_Oadr),
    .en(and_1_out));  // open: in0, in8, in9, in10, in11, in12, in13, in14, in15
  // Probe on cdm_8_mark5_1_p7
  // Probe on cdm_8_mark5_1_p8
  // CdM_8_mark5 cdm_8_mark5_1: pin names not known; wires that end beside it: cdm_8_mark5_1_p1, cdm_8_mark5_1_p2, cl, cdm_8_mark5_1_p4, cdm_8_mark5_1_p5, cdm_8_mark5_1_p6, cdm_8_mark5_1_p7, cdm_8_mark5_1_p8, cdm_8_mark5_1_p9, mem, In_Out_prime, {cdm_8_mark5_1_p12, I_Oadr}, cdm_8_mark5_1_p13, cdm_8_mark5_1_p14
  and and_2 (I_Osel, not_2_out, cl, data);
  Decoder #(.disabled(0)) decoder_1 (.out0(code), .out1(data), .sel(cdm_8_mark5_1_p9), .en(mem));
  assign I_Odat = not_1_out ? cdm_8_mark5_1_p13 : 8'bz;  // Controlled_Buffer controlled_buffer_1
  not not_1 (not_1_out, In_Out_prime);
  assign cdm_8_mark5_1_p14 = In_Out_prime ? I_Odat : 8'bz;  // Controlled_Buffer controlled_buffer_2
  not not_2 (not_2_out, nand_1_out);
  and and_3 (RAM, nand_1_out, data);
  nand nand_1 (nand_1_out, cdm_8_mark5_1_p12[4], cdm_8_mark5_1_p12[5], cdm_8_mark5_1_p12[6], cdm_8_mark5_1_p12[7]);
  buf buffer_3 (buffer_3_out, buffer_3_out);
  and and_4 (write, I_Osel, ~In_Out_prime);  // AND_Gate
  Demultiplexer #(.select(4), .width(8), .tristate("true"), .disabled(0)) demultiplexer_1 (
    .out1(demultiplexer_1_out1), .out2(demultiplexer_1_out2), .in(I_Odat), .sel(I_Oadr), .en(write));  // open: out0, out3, out4, out5, out6, out7, out8, out9, out10, out11, out12, out13, out14, out15
  ROM rom_1 (.addr({cdm_8_mark5_1_p12, I_Oadr}), .data(I_Odat), .sel(code));
  RAM ram_1 (.addr({cdm_8_mark5_1_p12, I_Oadr}), .data(I_Odat), .sel(RAM), .clk(cl), .ld(In_Out_prime));  // open: clr
  Register #(.trigger("falling")) u_finished (
    .D(demultiplexer_1_out1), .Q({finished_q, finished}), .clk(write));  // open: en, clr
  Register #(.trigger("falling")) collision (
    .D(demultiplexer_1_out2), .Q({collision_q, collision_happened}), .clk(write));  // open: en, clr
  Counter #(.width(32), .max('hffffffff)) counter_1 (.Q(counter_1_q), .clk(cl));  // open: load, D, count, carry, clr
  buf buffer_4 (buffer_4_out, buffer_4_out);
  Multiplexer #(.width(8)) multiplexer_5 (
    .in0(new_ball_data[7:0]), .in1(new_ball_data[7:0]), .out(new_speed_x), .sel(collision_happened),
    .en(undriven));
  Multiplexer #(.width(8)) multiplexer_6 (
    .in0(speed_y), .in1(new_ball_data[7:0]), .out(new_speed_y), .sel(collision_happened), .en(undriven_2));
  // Probe on counter_1_q
  Counter #(.width(2), .max('h3)) counter_2 (
    .carry(counter_2_carry), .clk(clock_2_out));  // open: load, D, count, Q, clr
  Clock clock_2 (.out(clock_2_out));
  // NOT_Gate not_3 is placed but not wired

  // Other names for the same wires on the sheet: ball_x_t[7:2] = {active_screen[0], ball_x};
  //   ball_y_t[7:2] = {active_screen[1], ball_y}; speed_x[7:0] = new_ball_data[7:0]; rd_wr_prime = In_Out_prime

  // Notes on the sheet:
  //   speed x, y
  //   ball x, y
  //   buffer_1 drives only 1 and floats otherwise
  //   Input to processor
  //   buffer_2 drives only 1 and floats otherwise
  //   buffer_3 drives only 1 and floats otherwise
  //   output
  //   instr memory
  //   contents of rom_1 (hex, n*v repeats v):
  //   d0 f0 c1 d1 8 a4 c5 cd 0 d0 f1 35 3a b1 5 e0 d a2 8c a2 b1 8c b2 79 ec 49 8c b3 1e 76 ec 49 8c b1 8c
  //   b2 76 e1 2b d1 1 ee 4b 8c b3 1b 76 e8 3e 77 eb 38 d1 1 ee 3a d1 0 ee 4b ee 49 77 ec 45 d1 1 ee 47 d1
  //   0 ee 4b d1 0 d0 f1 8c a1 88 d1 1 a1 ee 9
  //   data memory
  //   buffer_4 drives only 1 and floats otherwise
  //   Hz checker
endmodule

module collide0 (
  input  [7:0] start_vx,
  input  [7:0] start_vy,
  input  [7:0] start_ball_x,
  input  [7:0] start_ball_y,
  output [7:0] res_vx,
  output [7:0] res_vy
);

  wire move_1_owf_x, move_1_owf_y;
  wire [7:0] negator_1_out, negator_2_out;

  move move_1 (
    .start_vx(start_vx), .start_vy(start_vy), .start_ball_x(start_ball_x), .start_ball_y(start_ball_y),
    .owf_x(move_1_owf_x), .owf_y(move_1_owf_y));  // open: result_x, result_y
  Negator negator_1 (.in(start_vx), .out(negator_1_out));
  Multiplexer #(.width(8)) multiplexer_1 (
    .in0(start_vx), .in1(negator_1_out), .out(res_vx), .sel(move_1_owf_x));  // open: en
  Negator negator_2 (.in(start_vy), .out(negator_2_out));
  Multiplexer #(.width(8)) multiplexer_2 (
    .in0(start_vy), .in1(negator_2_out), .out(res_vy), .sel(move_1_owf_y));  // open: en
endmodule

module move (
  input  [7:0] start_vx,
  input  [7:0] start_vy,
  input  [7:0] start_ball_x,
  input  [7:0] start_ball_y,
  output [7:0] result_x,
  output [7:0] result_y,
  output owf_x,
  output owf_y
);

  wire adder_1_cout, adder_2_cout;
  wire [7:0] shifter_1_out, shifter_2_out;

  // Probe on start_ball_x
  // Probe on start_ball_y
  Shifter #(.shift("ar")) shifter_1 (.in(start_vx), .\dist (3'b001), .out(shifter_1_out));
  Adder adder_1 (.a(shifter_1_out), .b(start_ball_x), .out(result_x), .cout(adder_1_cout));  // open: cin
  xor xor_1 (owf_x, start_vx[7], adder_1_cout);
  Shifter #(.shift("ar")) shifter_2 (.in(start_vy), .\dist (3'b001), .out(shifter_2_out));
  Adder adder_2 (.a(shifter_2_out), .b(start_ball_y), .out(result_y), .cout(adder_2_cout));  // open: cin
  xor xor_2 (owf_y, start_vy[7], adder_2_cout);
endmodule

module graphics_ultra (
  input  [31:0] base,
  input  input_ball,
  input  [4:0] ball_x,
  input  [4:0] ball_y,
  input  is_active,
  input  [25:0] object,
  input  [4:0] current_x,
  output [31:0] out_8
);

  wire adder_1_cout, and_1_out, and_2_out, comparator_1_eq, comparator_2_gt, comparator_3_eq,
       comparator_3_lt, or_2_out, or_3_out;
  wire [4:0] adder_1_out;
  wire [31:0] decoder_1_out0, demultiplexer_1_out0, multiplexer_1_out, transistor_1_out;

  // Probe on object[7:0]
  // Probe on object[15:8]
  // Probe on object[23:16]
  and and_1 (and_1_out, input_ball, comparator_1_eq);
  Comparator #(.width(5), .mode("unsigned")) comparator_1 (
    .a(ball_x), .b(current_x), .eq(comparator_1_eq));  // open: gt, lt
  // Probe on object[4:0]
  // Probe on object[12:8]
  // Probe on object[20:16]
  Demultiplexer #(.select(5), .enable("false")) demultiplexer_1 (
    .out0(demultiplexer_1_out0[0]), .out1(demultiplexer_1_out0[1]), .out2(demultiplexer_1_out0[2]),
    .out3(demultiplexer_1_out0[3]), .out4(demultiplexer_1_out0[4]), .out5(demultiplexer_1_out0[5]),
    .out6(demultiplexer_1_out0[6]), .out7(demultiplexer_1_out0[7]), .out8(demultiplexer_1_out0[8]),
    .out9(demultiplexer_1_out0[9]), .out10(demultiplexer_1_out0[10]), .out11(demultiplexer_1_out0[11]),
    .out12(demultiplexer_1_out0[12]), .out13(demultiplexer_1_out0[13]), .out14(demultiplexer_1_out0[14]),
    .out15(demultiplexer_1_out0[15]), .out16(demultiplexer_1_out0[16]), .out17(demultiplexer_1_out0[17]),
    .out18(demultiplexer_1_out0[18]), .out19(demultiplexer_1_out0[19]), .out20(demultiplexer_1_out0[20]),
    .out21(demultiplexer_1_out0[21]), .out22(demultiplexer_1_out0[22]), .out23(demultiplexer_1_out0[23]),
    .out24(demultiplexer_1_out0[24]), .out25(demultiplexer_1_out0[25]), .out26(demultiplexer_1_out0[26]),
    .out27(demultiplexer_1_out0[27]), .out28(demultiplexer_1_out0[28]), .out29(demultiplexer_1_out0[29]),
    .out30(demultiplexer_1_out0[30]), .out31(demultiplexer_1_out0[31]), .in(and_1_out), .sel(ball_y));
  Decoder #(.select(5), .enable("false")) decoder_1 (
    .out0(decoder_1_out0[0]), .out1(decoder_1_out0[1]), .out2(decoder_1_out0[2]), .out3(decoder_1_out0[3]),
    .out4(decoder_1_out0[4]), .out5(decoder_1_out0[5]), .out6(decoder_1_out0[6]), .out7(decoder_1_out0[7]),
    .out8(decoder_1_out0[8]), .out9(decoder_1_out0[9]), .out10(decoder_1_out0[10]),
    .out11(decoder_1_out0[11]), .out12(decoder_1_out0[12]), .out13(decoder_1_out0[13]),
    .out14(decoder_1_out0[14]), .out15(decoder_1_out0[15]), .out16(decoder_1_out0[16]),
    .out17(decoder_1_out0[17]), .out18(decoder_1_out0[18]), .out19(decoder_1_out0[19]),
    .out20(decoder_1_out0[20]), .out21(decoder_1_out0[21]), .out22(decoder_1_out0[22]),
    .out23(decoder_1_out0[23]), .out24(decoder_1_out0[24]), .out25(decoder_1_out0[25]),
    .out26(decoder_1_out0[26]), .out27(decoder_1_out0[27]), .out28(decoder_1_out0[28]),
    .out29(decoder_1_out0[29]), .out30(decoder_1_out0[30]), .out31(decoder_1_out0[31]), .sel(object[12:8]));
  Pull_Resistor pull_resistor_1 (.node(base));
  Multiplexer #(.width(32)) multiplexer_1 (
    .in0({32{1'b0}}), .in1(transistor_1_out), .out(multiplexer_1_out), .sel(is_active));  // open: en
  Pull_Resistor pull_resistor_2 (.node(is_active));
  assign out_8 = base | demultiplexer_1_out0 | multiplexer_1_out;  // OR_Gate or_1, 32 bits wide
  Adder #(.width(5)) adder_1 (.a(object[4:0]), .b(object[20:16]), .out(adder_1_out), .cout(adder_1_cout));  // open: cin
  // Probe on decoder_1_out0
  Comparator #(.width(5), .mode("unsigned")) comparator_2 (
    .a(adder_1_out), .b(current_x), .gt(comparator_2_gt));  // open: eq, lt
  Comparator #(.width(5), .mode("unsigned")) comparator_3 (
    .a(object[4:0]), .b(current_x), .eq(comparator_3_eq), .lt(comparator_3_lt));  // open: gt
  or or_2 (or_2_out, comparator_2_gt, adder_1_cout);
  and and_2 (and_2_out, or_2_out, or_3_out);
  or or_3 (or_3_out, comparator_3_eq, comparator_3_lt);
  Transistor #(.width(32)) transistor_1 (.in({32{1'b0}}), .out(transistor_1_out), .gate(and_2_out));
  Transistor #(.\type ("n"), .width(32)) transistor_2 (.in(decoder_1_out0), .out(transistor_1_out), .gate(and_2_out));

  // Other names for the same wires on the sheet: current_row[4:0] = current_x
endmodule

module screen_memo (
  input  [31:0] new_column,
  input  clock,
  input  [4:0] x,
  output [31:0] out_4,
  output [31:0] out_5,
  output [31:0] out_6,
  output [31:0] out_7,
  output [31:0] out_8,
  output [31:0] out_9,
  output [31:0] out_10,
  output [31:0] out_11,
  output [31:0] out_12,
  output [31:0] out_13,
  output [31:0] out_14,
  output [31:0] out_15,
  output [31:0] out_16,
  output [31:0] out_17,
  output [31:0] out_18,
  output [31:0] out_19,
  output [31:0] out_20,
  output [31:0] out_21,
  output [31:0] out_22,
  output [31:0] out_23,
  output [31:0] out_24,
  output [31:0] out_25,
  output [31:0] out_26,
  output [31:0] out_27,
  output [31:0] out_28,
  output [31:0] out_29,
  output [31:0] out_30,
  output [31:0] out_31,
  output [31:0] out_32,
  output [31:0] out_33,
  output [31:0] out_34,
  output [31:0] out_35
);

  wire [31:0] demultiplexer_1_out0, demultiplexer_1_out1, demultiplexer_1_out2, demultiplexer_1_out3,
       demultiplexer_1_out4, demultiplexer_1_out5, demultiplexer_1_out6, demultiplexer_1_out7,
       demultiplexer_1_out8, demultiplexer_1_out9, demultiplexer_1_out10, demultiplexer_1_out11,
       demultiplexer_1_out12, demultiplexer_1_out13, demultiplexer_1_out14, demultiplexer_1_out15,
       demultiplexer_1_out16, demultiplexer_1_out17, demultiplexer_1_out18, demultiplexer_1_out19,
       demultiplexer_1_out20, demultiplexer_1_out21, demultiplexer_1_out22, demultiplexer_1_out23,
       demultiplexer_1_out24, demultiplexer_1_out25, demultiplexer_1_out26, demultiplexer_1_out27,
       demultiplexer_1_out28, demultiplexer_1_out29, demultiplexer_1_out30, demultiplexer_1_out31;

  Demultiplexer #(.select(5), .width(32), .tristate("true")) demultiplexer_1 (
    .out0(demultiplexer_1_out0), .out1(demultiplexer_1_out1), .out2(demultiplexer_1_out2),
    .out3(demultiplexer_1_out3), .out4(demultiplexer_1_out4), .out5(demultiplexer_1_out5),
    .out6(demultiplexer_1_out6), .out7(demultiplexer_1_out7), .out8(demultiplexer_1_out8),
    .out9(demultiplexer_1_out9), .out10(demultiplexer_1_out10), .out11(demultiplexer_1_out11),
    .out12(demultiplexer_1_out12), .out13(demultiplexer_1_out13), .out14(demultiplexer_1_out14),
    .out15(demultiplexer_1_out15), .out16(demultiplexer_1_out16), .out17(demultiplexer_1_out17),
    .out18(demultiplexer_1_out18), .out19(demultiplexer_1_out19), .out20(demultiplexer_1_out20),
    .out21(demultiplexer_1_out21), .out22(demultiplexer_1_out22), .out23(demultiplexer_1_out23),
    .out24(demultiplexer_1_out24), .out25(demultiplexer_1_out25), .out26(demultiplexer_1_out26),
    .out27(demultiplexer_1_out27), .out28(demultiplexer_1_out28), .out29(demultiplexer_1_out29),
    .out30(demultiplexer_1_out30), .out31(demultiplexer_1_out31), .in(new_column), .sel(x));  // open: en
  Register #(.width(32)) register_1 (.D(demultiplexer_1_out0), .Q(out_4), .clk(clock));  // open: en, clr
  Register #(.width(32)) register_2 (.D(demultiplexer_1_out1), .Q(out_5), .clk(clock));  // open: en, clr
  Register #(.width(32)) register_3 (.D(demultiplexer_1_out2), .Q(out_6), .clk(clock));  // open: en, clr
  Register #(.width(32)) register_4 (.D(demultiplexer_1_out3), .Q(out_7), .clk(clock));  // open: en, clr
  Register #(.width(32)) register_5 (.D(demultiplexer_1_out4), .Q(out_8), .clk(clock));  // open: en, clr
  Register #(.width(32)) register_6 (.D(demultiplexer_1_out5), .Q(out_9), .clk(clock));  // open: en, clr
  Register #(.width(32)) register_7 (.D(demultiplexer_1_out6), .Q(out_10), .clk(clock));  // open: en, clr
  Register #(.width(32)) register_8 (.D(demultiplexer_1_out7), .Q(out_11), .clk(clock));  // open: en, clr
  Register #(.width(32)) register_9 (.D(demultiplexer_1_out8), .Q(out_12), .clk(clock));  // open: en, clr
  Register #(.width(32)) register_10 (.D(demultiplexer_1_out9), .Q(out_13), .clk(clock));  // open: en, clr
  Register #(.width(32)) register_11 (.D(demultiplexer_1_out10), .Q(out_14), .clk(clock));  // open: en, clr
  Register #(.width(32)) register_12 (.D(demultiplexer_1_out11), .Q(out_15), .clk(clock));  // open: en, clr
  Register #(.width(32)) register_13 (.D(demultiplexer_1_out12), .Q(out_16), .clk(clock));  // open: en, clr
  Register #(.width(32)) register_14 (.D(demultiplexer_1_out13), .Q(out_17), .clk(clock));  // open: en, clr
  Register #(.width(32)) register_15 (.D(demultiplexer_1_out14), .Q(out_18), .clk(clock));  // open: en, clr
  Register #(.width(32)) register_16 (.D(demultiplexer_1_out15), .Q(out_19), .clk(clock));  // open: en, clr
  Register #(.width(32)) register_17 (.D(demultiplexer_1_out16), .Q(out_20), .clk(clock));  // open: en, clr
  Register #(.width(32)) register_18 (.D(demultiplexer_1_out17), .Q(out_21), .clk(clock));  // open: en, clr
  Register #(.width(32)) register_19 (.D(demultiplexer_1_out18), .Q(out_22), .clk(clock));  // open: en, clr
  Register #(.width(32)) register_20 (.D(demultiplexer_1_out19), .Q(out_23), .clk(clock));  // open: en, clr
  Register #(.width(32)) register_21 (.D(demultiplexer_1_out20), .Q(out_24), .clk(clock));  // open: en, clr
  Register #(.width(32)) register_22 (.D(demultiplexer_1_out21), .Q(out_25), .clk(clock));  // open: en, clr
  Register #(.width(32)) register_23 (.D(demultiplexer_1_out22), .Q(out_26), .clk(clock));  // open: en, clr
  Register #(.width(32)) register_24 (.D(demultiplexer_1_out23), .Q(out_27), .clk(clock));  // open: en, clr
  Register #(.width(32)) register_25 (.D(demultiplexer_1_out24), .Q(out_28), .clk(clock));  // open: en, clr
  Register #(.width(32)) register_26 (.D(demultiplexer_1_out25), .Q(out_29), .clk(clock));  // open: en, clr
  Register #(.width(32)) register_27 (.D(demultiplexer_1_out26), .Q(out_30), .clk(clock));  // open: en, clr
  Register #(.width(32)) register_28 (.D(demultiplexer_1_out27), .Q(out_31), .clk(clock));  // open: en, clr
  Register #(.width(32)) register_29 (.D(demultiplexer_1_out28), .Q(out_32), .clk(clock));  // open: en, clr
  Register #(.width(32)) register_30 (.D(demultiplexer_1_out29), .Q(out_33), .clk(clock));  // open: en, clr
  Register #(.width(32)) register_31 (.D(demultiplexer_1_out30), .Q(out_34), .clk(clock));  // open: en, clr
  Register #(.width(32)) register_32 (.D(demultiplexer_1_out31), .Q(out_35), .clk(clock));  // open: en, clr
endmodule

module graphics_man (
  input  [31:0] state0,
  input  [31:0] state1,
  input  [31:0] state2,
  input  [31:0] state3,
  input  [1:0] active_screen,
  input  [4:0] ball_x,
  input  [4:0] ball_y,
  input  active_1,
  input  [25:0] door_1,
  input  active_2,
  input  [25:0] door_2,
  input  [4:0] x,
  output [31:0] screen_1,
  output [31:0] screen_2,
  output [31:0] screen_3,
  output [31:0] screen_4
);

  wire decoder_1_out0, decoder_1_out1, decoder_1_out2, decoder_1_out3;

  Decoder #(.select(2)) decoder_1 (
    .out0(decoder_1_out0), .out1(decoder_1_out1), .out2(decoder_1_out2), .out3(decoder_1_out3),
    .sel(active_screen));  // open: en
  graphics_ultra graphics_ultra_1 (
    .input_ball(decoder_1_out0), .ball_x(ball_x), .ball_y(ball_y), .is_active(active_1), .object(door_1),
    .base(state0), .current_x(x), .out_8(screen_1));
  graphics_ultra graphics_ultra_2 (
    .input_ball(decoder_1_out1), .ball_x(ball_x), .ball_y(ball_y), .is_active(active_2), .object(door_2),
    .base(state1), .current_x(x), .out_8(screen_2));
  graphics_ultra graphics_ultra_3 (
    .input_ball(decoder_1_out2), .ball_x(ball_x), .ball_y(ball_y), .base(state2), .current_x(x),
    .out_8(screen_3));  // open: is_active, object
  graphics_ultra graphics_ultra_4 (
    .input_ball(decoder_1_out3), .ball_x(ball_x), .ball_y(ball_y), .base(state3), .current_x(x),
    .out_8(screen_4));  // open: is_active, object
endmodule

module draw_object (
  input  [31:0] base,
  input  [25:0] object,
  input  [4:0] row_x,
  output [31:0] result
);

  wire adder_2_cout, and_1_out, comparator_1_eq, comparator_2_gt, comparator_3_eq, comparator_3_lt, or_1_out,
       or_2_out;
  wire [4:0] adder_1_out, adder_2_out, multiplexer_1_out, negator_1_out, subtractor_1_out, transistor_1_out;
  wire [31:0] decoder_1_out0, multiplier_1_out, not_1_out, shifter_1_out, transistor_3_out, transistor_5_out;

  // Probe on object[25:24]
  // Probe on object[7:0]
  // Probe on object[15:8]
  // Probe on object[23:16]
  // Probe on row_x
  // Probe on object[4:0]
  // Probe on object[12:8]
  // Probe on object[20:16]
  Subtractor #(.width(5)) subtractor_1 (.a(object[4:0]), .b(row_x), .out(subtractor_1_out));  // open: bin, bout
  Multiplexer #(.select(2), .width(5)) multiplexer_1 (
    .in0({5{1'b0}}), .in1({5{1'b0}}), .in2(negator_1_out), .in3(subtractor_1_out), .out(multiplexer_1_out),
    .sel(object[25:24]));  // open: en
  Negator #(.width(5)) negator_1 (.in(subtractor_1_out), .out(negator_1_out));
  Decoder #(.select(5)) decoder_1 (
    .out0(decoder_1_out0[0]), .out1(decoder_1_out0[1]), .out2(decoder_1_out0[2]), .out3(decoder_1_out0[3]),
    .out4(decoder_1_out0[4]), .out5(decoder_1_out0[5]), .out6(decoder_1_out0[6]), .out7(decoder_1_out0[7]),
    .out8(decoder_1_out0[8]), .out9(decoder_1_out0[9]), .out10(decoder_1_out0[10]),
    .out11(decoder_1_out0[11]), .out12(decoder_1_out0[12]), .out13(decoder_1_out0[13]),
    .out14(decoder_1_out0[14]), .out15(decoder_1_out0[15]), .out16(decoder_1_out0[16]),
    .out17(decoder_1_out0[17]), .out18(decoder_1_out0[18]), .out19(decoder_1_out0[19]),
    .out20(decoder_1_out0[20]), .out21(decoder_1_out0[21]), .out22(decoder_1_out0[22]),
    .out23(decoder_1_out0[23]), .out24(decoder_1_out0[24]), .out25(decoder_1_out0[25]),
    .out26(decoder_1_out0[26]), .out27(decoder_1_out0[27]), .out28(decoder_1_out0[28]),
    .out29(decoder_1_out0[29]), .out30(decoder_1_out0[30]), .out31(decoder_1_out0[31]), .sel(adder_1_out));  // open: en
  Adder #(.width(5)) adder_1 (.a(multiplexer_1_out), .b(object[12:8]), .out(adder_1_out));  // open: cin, cout
  Comparator #(.width(2)) comparator_1 (.a(object[25:24]), .b(2'b01), .eq(comparator_1_eq));  // open: gt, lt
  // Probe on decoder_1_out0
  Shifter #(.width(32)) shifter_1 (.in({32{1'b1}}), .\dist (object[20:16]), .out(shifter_1_out));
  Transistor #(.width(5)) transistor_1 (.in(object[20:16]), .out(transistor_1_out), .gate(comparator_1_eq));
  Transistor #(.\type ("n"), .width(5)) transistor_2 (.in(5'b00001), .out(transistor_1_out), .gate(comparator_1_eq));
  assign not_1_out = ~shifter_1_out;  // NOT_Gate not_1, 32 bits wide
  Adder #(.width(5)) adder_2 (
    .a(object[4:0]), .b(transistor_1_out), .out(adder_2_out), .cout(adder_2_cout));  // open: cin
  Multiplier #(.width(32)) multiplier_1 (.a(decoder_1_out0), .b(not_1_out), .out(multiplier_1_out));  // open: cin, cout
  Comparator #(.width(5), .mode("unsigned")) comparator_2 (
    .a(adder_2_out), .b(row_x), .gt(comparator_2_gt));  // open: eq, lt
  or or_1 (or_1_out, comparator_2_gt, adder_2_cout);
  Comparator #(.width(5), .mode("unsigned")) comparator_3 (
    .a(object[4:0]), .b(row_x), .eq(comparator_3_eq), .lt(comparator_3_lt));  // open: gt
  or or_2 (or_2_out, comparator_3_eq, comparator_3_lt);
  Transistor #(.width(32)) transistor_3 (.in(decoder_1_out0), .out(transistor_3_out), .gate(comparator_1_eq));
  Transistor #(.\type ("n"), .width(32)) transistor_4 (
    .in(multiplier_1_out), .out(transistor_3_out), .gate(comparator_1_eq));
  and and_1 (and_1_out, or_1_out, or_2_out);
  Transistor #(.width(32)) transistor_5 (.in({32{1'b0}}), .out(transistor_5_out), .gate(and_1_out));
  Transistor #(.\type ("n"), .width(32)) transistor_6 (.in(transistor_3_out), .out(transistor_5_out), .gate(and_1_out));
  assign result = base | transistor_5_out;  // OR_Gate or_3, 32 bits wide
endmodule

module transform (
  input  usigned,
  input  [1:0] \type ,
  input  [7:0] x,
  input  [7:0] y,
  output [7:0] x_2,
  output [7:0] y_2
);

  wire [7:0] adder_1_out, adder_2_out, multiplexer_1_out, subtractor_1_out;

  Adder adder_1 (.a(x), .b(y), .out(adder_1_out));  // open: cin, cout
  Subtractor subtractor_1 (.a(x), .b(y), .out(subtractor_1_out));  // open: bin, bout
  Multiplexer #(.width(8)) multiplexer_1 (
    .in0({8{1'b0}}), .in1(8'h20), .out(multiplexer_1_out), .sel(usigned));  // open: en
  Adder adder_2 (.a(subtractor_1_out), .b(multiplexer_1_out), .out(adder_2_out));  // open: cin, cout
  Multiplexer #(.select(2), .width(8)) multiplexer_2 (
    .in0(x), .in1(y), .in2(adder_1_out), .in3(adder_2_out), .out(x_2), .sel(\type ));  // open: en
  Multiplexer #(.select(2), .width(8)) multiplexer_3 (
    .in0(y), .in1(x), .in2(adder_2_out), .in3(adder_1_out), .out(y_2), .sel(\type ));  // open: en
endmodule
