// Logisim project pinball v0.circ as structural Verilog: 8 circuits, main circuit main
module main (
  input  slow_x8,
  input  in_2,
  input  LOAD
);

  wire a_out, b_out, c_out, cdm_8_mark5_1_p1, cdm_8_mark5_1_p2, cdm_8_mark5_1_p4, cdm_8_mark5_1_p5,
       cdm_8_mark5_1_p6, cdm_8_mark5_1_p7, cdm_8_mark5_1_p8, cdm_8_mark5_1_p9, cl, clock_1_out, code,
       comparator_1_eq, comparator_2_eq, comparator_3_eq, d_out, data, I_Osel, In_Out_prime, mem,
       multiplexer_1_out, nand_1_out, nor_1_out, nor_2_out, not_1_out, not_2_out, not_3_out, not_4_out,
       not_5_out, not_6_out, not_7_out, not_8_out, not_9_out, or_1_out, RAM, read, reset_ball_out, RESET_out,
       transistor_1_out, transistor_4_out, write;
  wire [2:0] counter_1_q, I_Oadr;
  wire [3:0] register_1_q, register_1_q_2;
  wire [4:0] counter_2_q, counter_3_q, counter_4_q, transistor_2_out;
  wire [6:0] controlled_buffer_3_out, register_2_q;
  wire [7:0] cdm_8_mark5_1_p13, cdm_8_mark5_1_p14, demultiplexer_1_out1, I_Odat;
  wire [7:3] cdm_8_mark5_1_p12;
  wire [7:7] rs_latch_1_p3;
  wire [25:0] bit_extender_1_out, bit_extender_2_out, bit_extender_3_out, bit_extender_4_out;
  wire [31:0] ball_2_updated_ball, ball_q, draw_object_1_result, draw_object_2_result, draw_object_3_result,
       draw_object_4_result, graphics_man_1_screen_1, graphics_man_1_screen_2, graphics_man_1_screen_3,
       graphics_man_1_screen_4, multiplexer_2_out, ram_1_data, ram_2_data, ram_3_data, ram_4_data,
       rom_1_data, rom_2_data, rom_3_data, rom_4_data, screen_memo_1_out_4, screen_memo_1_out_5,
       screen_memo_1_out_6, screen_memo_1_out_7, screen_memo_1_out_8, screen_memo_1_out_9,
       screen_memo_1_out_10, screen_memo_1_out_11, screen_memo_1_out_12, screen_memo_1_out_13,
       screen_memo_1_out_14, screen_memo_1_out_15, screen_memo_1_out_16, screen_memo_1_out_17,
       screen_memo_1_out_18, screen_memo_1_out_19, screen_memo_1_out_20, screen_memo_1_out_21,
       screen_memo_1_out_22, screen_memo_1_out_23, screen_memo_1_out_24, screen_memo_1_out_25,
       screen_memo_1_out_26, screen_memo_1_out_27, screen_memo_1_out_28, screen_memo_1_out_29,
       screen_memo_1_out_30, screen_memo_1_out_31, screen_memo_1_out_32, screen_memo_1_out_33,
       screen_memo_1_out_34, screen_memo_1_out_35, screen_memo_2_out_4, screen_memo_2_out_5,
       screen_memo_2_out_6, screen_memo_2_out_7, screen_memo_2_out_8, screen_memo_2_out_9,
       screen_memo_2_out_10, screen_memo_2_out_11, screen_memo_2_out_12, screen_memo_2_out_13,
       screen_memo_2_out_14, screen_memo_2_out_15, screen_memo_2_out_16, screen_memo_2_out_17,
       screen_memo_2_out_18, screen_memo_2_out_19, screen_memo_2_out_20, screen_memo_2_out_21,
       screen_memo_2_out_22, screen_memo_2_out_23, screen_memo_2_out_24, screen_memo_2_out_25,
       screen_memo_2_out_26, screen_memo_2_out_27, screen_memo_2_out_28, screen_memo_2_out_29,
       screen_memo_2_out_30, screen_memo_2_out_31, screen_memo_2_out_32, screen_memo_2_out_33,
       screen_memo_2_out_34, screen_memo_2_out_35, screen_memo_3_out_4, screen_memo_3_out_5,
       screen_memo_3_out_6, screen_memo_3_out_7, screen_memo_3_out_8, screen_memo_3_out_9,
       screen_memo_3_out_10, screen_memo_3_out_11, screen_memo_3_out_12, screen_memo_3_out_13,
       screen_memo_3_out_14, screen_memo_3_out_15, screen_memo_3_out_16, screen_memo_3_out_17,
       screen_memo_3_out_18, screen_memo_3_out_19, screen_memo_3_out_20, screen_memo_3_out_21,
       screen_memo_3_out_22, screen_memo_3_out_23, screen_memo_3_out_24, screen_memo_3_out_25,
       screen_memo_3_out_26, screen_memo_3_out_27, screen_memo_3_out_28, screen_memo_3_out_29,
       screen_memo_3_out_30, screen_memo_3_out_31, screen_memo_3_out_32, screen_memo_3_out_33,
       screen_memo_3_out_34, screen_memo_3_out_35, screen_memo_4_out_4, screen_memo_4_out_5,
       screen_memo_4_out_6, screen_memo_4_out_7, screen_memo_4_out_8, screen_memo_4_out_9,
       screen_memo_4_out_10, screen_memo_4_out_11, screen_memo_4_out_12, screen_memo_4_out_13,
       screen_memo_4_out_14, screen_memo_4_out_15, screen_memo_4_out_16, screen_memo_4_out_17,
       screen_memo_4_out_18, screen_memo_4_out_19, screen_memo_4_out_20, screen_memo_4_out_21,
       screen_memo_4_out_22, screen_memo_4_out_23, screen_memo_4_out_24, screen_memo_4_out_25,
       screen_memo_4_out_26, screen_memo_4_out_27, screen_memo_4_out_28, screen_memo_4_out_29,
       screen_memo_4_out_30, screen_memo_4_out_31, screen_memo_4_out_32, screen_memo_4_out_33,
       screen_memo_4_out_34, screen_memo_4_out_35, shifter_1_out, shifter_2_out, shifter_3_out, shifter_4_out;

  Clock clock_1 (.out(clock_1_out));
  Counter #(.width(3), .max('h7)) counter_1 (.Q(counter_1_q), .clk(clock_1_out));  // open: load, D, count, carry, clr
  Comparator #(.width(3)) comparator_1 (.a(counter_1_q), .b(3'b000), .eq(comparator_1_eq));  // open: gt, lt
  Multiplexer multiplexer_1 (
    .in0(clock_1_out), .in1(comparator_1_eq), .out(multiplexer_1_out), .sel(slow_x8));  // open: en
  Counter #(.width(5), .max('h1f)) counter_2 (
    .Q(counter_2_q), .clk(multiplexer_1_out));  // open: load, D, count, carry, clr
  Transistor #(.\type ("n")) transistor_1 (.in(multiplexer_1_out), .out(transistor_1_out), .gate(LOAD));
  Comparator #(.width(5)) comparator_2 (.a(counter_3_q), .b({5{1'b0}}), .eq(comparator_2_eq));  // open: gt, lt
  Multiplexer #(.width(32)) multiplexer_2 (
    .in0(ball_2_updated_ball), .in1(32'h300800), .out(multiplexer_2_out), .sel(or_1_out));  // open: en
  Register #(.width(32)) ball (.D(multiplexer_2_out), .Q(ball_q), .clk(comparator_3_eq));  // open: en, clr
  Comparator #(.width(5)) comparator_3 (.a({5{1'b0}}), .b(counter_2_q), .eq(comparator_3_eq));  // open: gt, lt
  or or_1 (or_1_out, in_2, reset_ball_out);
  Counter #(.width(5), .max('h1f)) counter_3 (
    .Q(counter_3_q), .clk(transistor_1_out), .clr(RESET_out));  // open: load, D, count, carry
  Counter #(.width(5), .max('h1f)) counter_4 (
    .Q(counter_4_q), .clk(comparator_2_eq), .clr(RESET_out));  // open: load, D, count, carry
  ball ball_2 (
    .start_vx(10'h40), .ball_data(ball_q), .Updated_ball(ball_2_updated_ball), .Clock(comparator_3_eq),
    .Reset(or_1_out));  // open: start_vy
  ROM #(.addrWidth(5), .dataWidth(32)) rom_1 (.addr(counter_3_q), .data(rom_1_data));  // open: sel
  ROM #(.addrWidth(5), .dataWidth(32)) rom_2 (.addr(counter_3_q), .data(rom_2_data));  // open: sel
  ROM #(.addrWidth(5), .dataWidth(32)) rom_3 (.addr(counter_3_q), .data(rom_3_data));  // open: sel
  ROM #(.addrWidth(5), .dataWidth(32)) rom_4 (.addr(counter_3_q), .data(rom_4_data));  // open: sel
  Transistor #(.gate("br"), .width(5)) transistor_2 (.in(counter_2_q), .out(transistor_2_out), .gate(LOAD));
  Bit_Extender #(.in_width(32), .out_width(26)) bit_extender_1 (.in(shifter_1_out), .out(bit_extender_1_out));
  Shifter #(.width(32), .shift("lr")) shifter_1 (.in(rom_1_data), .\dist (5'b00110), .out(shifter_1_out));
  Bit_Extender #(.in_width(32), .out_width(26)) bit_extender_2 (.in(shifter_2_out), .out(bit_extender_2_out));
  Shifter #(.width(32), .shift("lr")) shifter_2 (.in(rom_2_data), .\dist (5'b00110), .out(shifter_2_out));
  Bit_Extender #(.in_width(32), .out_width(26)) bit_extender_3 (.in(shifter_3_out), .out(bit_extender_3_out));
  Shifter #(.width(32), .shift("lr")) shifter_3 (.in(rom_3_data), .\dist (5'b00110), .out(shifter_3_out));
  Shifter #(.width(32), .shift("lr")) shifter_4 (.in(rom_4_data), .\dist (5'b00110), .out(shifter_4_out));
  Bit_Extender #(.in_width(32), .out_width(26)) bit_extender_4 (.in(shifter_4_out), .out(bit_extender_4_out));
  Transistor #(.\type ("n"), .gate("br"), .width(5)) transistor_3 (
    .in(counter_4_q), .out(transistor_2_out), .gate(LOAD));
  Button RESET (.out(RESET_out));
  graphics_man graphics_man_1 (
    .ball_data(ball_2_updated_ball), .state0(ram_1_data), .state1(ram_1_data), .state2(ram_1_data),
    .state3(ram_1_data), .x(counter_2_q), .screen_1(graphics_man_1_screen_1),
    .screen_2(graphics_man_1_screen_2), .screen_3(graphics_man_1_screen_3), .screen_4(graphics_man_1_screen_4));  // open: clock, x_2
  draw_object draw_object_1 (
    .object(bit_extender_1_out), .row_x(transistor_2_out), .base(ram_1_data), .result(draw_object_1_result));
  draw_object draw_object_2 (
    .object(bit_extender_2_out), .row_x(transistor_2_out), .base(ram_2_data), .result(draw_object_2_result));
  draw_object draw_object_3 (
    .object(bit_extender_3_out), .row_x(transistor_2_out), .base(ram_3_data), .result(draw_object_3_result));
  draw_object draw_object_4 (
    .object(bit_extender_4_out), .row_x(transistor_2_out), .base(ram_4_data), .result(draw_object_4_result));
  RAM #(.addrWidth(5), .dataWidth(32), .bus("separate")) ram_1 (
    .addr(transistor_2_out), .din(draw_object_1_result), .data(ram_1_data), .clk(transistor_1_out),
    .clr(RESET_out));  // open: str, sel, ld
  RAM #(.addrWidth(5), .dataWidth(32), .bus("separate")) ram_2 (
    .addr(transistor_2_out), .din(draw_object_2_result), .data(ram_2_data), .clk(transistor_1_out),
    .clr(RESET_out));  // open: str, sel, ld
  RAM #(.addrWidth(5), .dataWidth(32), .bus("separate")) ram_3 (
    .addr(transistor_2_out), .din(draw_object_3_result), .data(ram_3_data), .clk(transistor_1_out),
    .clr(RESET_out));  // open: str, sel, ld
  RAM #(.addrWidth(5), .dataWidth(32), .bus("separate")) ram_4 (
    .addr(transistor_2_out), .din(draw_object_4_result), .data(ram_4_data), .clk(transistor_1_out),
    .clr(RESET_out));  // open: str, sel, ld
  screen_memo screen_memo_1 (
    .new_column(graphics_man_1_screen_3), .out_4(screen_memo_1_out_4), .out_5(screen_memo_1_out_5),
    .out_6(screen_memo_1_out_6), .out_7(screen_memo_1_out_7), .out_8(screen_memo_1_out_8),
    .out_9(screen_memo_1_out_9), .out_10(screen_memo_1_out_10), .out_11(screen_memo_1_out_11),
    .out_12(screen_memo_1_out_12), .out_13(screen_memo_1_out_13), .out_14(screen_memo_1_out_14),
    .out_15(screen_memo_1_out_15), .out_16(screen_memo_1_out_16), .out_17(screen_memo_1_out_17),
    .out_18(screen_memo_1_out_18), .out_19(screen_memo_1_out_19), .out_20(screen_memo_1_out_20),
    .out_21(screen_memo_1_out_21), .out_22(screen_memo_1_out_22), .out_23(screen_memo_1_out_23),
    .out_24(screen_memo_1_out_24), .out_25(screen_memo_1_out_25), .out_26(screen_memo_1_out_26),
    .out_27(screen_memo_1_out_27), .out_28(screen_memo_1_out_28), .out_29(screen_memo_1_out_29),
    .out_30(screen_memo_1_out_30), .out_31(screen_memo_1_out_31), .out_32(screen_memo_1_out_32),
    .out_33(screen_memo_1_out_33), .out_34(screen_memo_1_out_34), .out_35(screen_memo_1_out_35),
    .clock(multiplexer_1_out), .x(counter_2_q));
  DotMatrix #(.matrixcols(32), .matrixrows(32)) dotmatrix_1 (
    .col0(screen_memo_1_out_4), .col1(screen_memo_1_out_5), .col2(screen_memo_1_out_6),
    .col3(screen_memo_1_out_7), .col4(screen_memo_1_out_8), .col5(screen_memo_1_out_9),
    .col6(screen_memo_1_out_10), .col7(screen_memo_1_out_11), .col8(screen_memo_1_out_12),
    .col9(screen_memo_1_out_13), .col10(screen_memo_1_out_14), .col11(screen_memo_1_out_15),
    .col12(screen_memo_1_out_16), .col13(screen_memo_1_out_17), .col14(screen_memo_1_out_18),
    .col15(screen_memo_1_out_19), .col16(screen_memo_1_out_20), .col17(screen_memo_1_out_21),
    .col18(screen_memo_1_out_22), .col19(screen_memo_1_out_23), .col20(screen_memo_1_out_24),
    .col21(screen_memo_1_out_25), .col22(screen_memo_1_out_26), .col23(screen_memo_1_out_27),
    .col24(screen_memo_1_out_28), .col25(screen_memo_1_out_29), .col26(screen_memo_1_out_30),
    .col27(screen_memo_1_out_31), .col28(screen_memo_1_out_32), .col29(screen_memo_1_out_33),
    .col30(screen_memo_1_out_34), .col31(screen_memo_1_out_35));
  DotMatrix #(.matrixcols(32), .matrixrows(32)) dotmatrix_2 (
    .col0(screen_memo_2_out_4), .col1(screen_memo_2_out_5), .col2(screen_memo_2_out_6),
    .col3(screen_memo_2_out_7), .col4(screen_memo_2_out_8), .col5(screen_memo_2_out_9),
    .col6(screen_memo_2_out_10), .col7(screen_memo_2_out_11), .col8(screen_memo_2_out_12),
    .col9(screen_memo_2_out_13), .col10(screen_memo_2_out_14), .col11(screen_memo_2_out_15),
    .col12(screen_memo_2_out_16), .col13(screen_memo_2_out_17), .col14(screen_memo_2_out_18),
    .col15(screen_memo_2_out_19), .col16(screen_memo_2_out_20), .col17(screen_memo_2_out_21),
    .col18(screen_memo_2_out_22), .col19(screen_memo_2_out_23), .col20(screen_memo_2_out_24),
    .col21(screen_memo_2_out_25), .col22(screen_memo_2_out_26), .col23(screen_memo_2_out_27),
    .col24(screen_memo_2_out_28), .col25(screen_memo_2_out_29), .col26(screen_memo_2_out_30),
    .col27(screen_memo_2_out_31), .col28(screen_memo_2_out_32), .col29(screen_memo_2_out_33),
    .col30(screen_memo_2_out_34), .col31(screen_memo_2_out_35));
  screen_memo screen_memo_2 (
    .new_column(graphics_man_1_screen_1), .out_4(screen_memo_2_out_4), .out_5(screen_memo_2_out_5),
    .out_6(screen_memo_2_out_6), .out_7(screen_memo_2_out_7), .out_8(screen_memo_2_out_8),
    .out_9(screen_memo_2_out_9), .out_10(screen_memo_2_out_10), .out_11(screen_memo_2_out_11),
    .out_12(screen_memo_2_out_12), .out_13(screen_memo_2_out_13), .out_14(screen_memo_2_out_14),
    .out_15(screen_memo_2_out_15), .out_16(screen_memo_2_out_16), .out_17(screen_memo_2_out_17),
    .out_18(screen_memo_2_out_18), .out_19(screen_memo_2_out_19), .out_20(screen_memo_2_out_20),
    .out_21(screen_memo_2_out_21), .out_22(screen_memo_2_out_22), .out_23(screen_memo_2_out_23),
    .out_24(screen_memo_2_out_24), .out_25(screen_memo_2_out_25), .out_26(screen_memo_2_out_26),
    .out_27(screen_memo_2_out_27), .out_28(screen_memo_2_out_28), .out_29(screen_memo_2_out_29),
    .out_30(screen_memo_2_out_30), .out_31(screen_memo_2_out_31), .out_32(screen_memo_2_out_32),
    .out_33(screen_memo_2_out_33), .out_34(screen_memo_2_out_34), .out_35(screen_memo_2_out_35),
    .clock(multiplexer_1_out), .x(counter_2_q));
  // Probe on cdm_8_mark5_1_p1
  // Probe on cdm_8_mark5_1_p2
  // Probe on cdm_8_mark5_1_p4
  Clock clock_2 (.out(cl));
  not not_1 (not_1_out, not_1_out);
  // Probe on cdm_8_mark5_1_p5
  // Probe on cdm_8_mark5_1_p6
  // Probe on cdm_8_mark5_1_p7
  // Probe on cdm_8_mark5_1_p8
  and and_1 (I_Osel, not_3_out, cl, data);
  // CdM_8_mark5 cdm_8_mark5_1: pin names not known; wires that end beside it: cdm_8_mark5_1_p1, cdm_8_mark5_1_p2, cl, cdm_8_mark5_1_p4, cdm_8_mark5_1_p5, cdm_8_mark5_1_p6, cdm_8_mark5_1_p7, cdm_8_mark5_1_p8, cdm_8_mark5_1_p9, mem, In_Out_prime, {cdm_8_mark5_1_p12, I_Oadr}, cdm_8_mark5_1_p13, cdm_8_mark5_1_p14
  not not_2 (not_2_out, In_Out_prime);
  assign cdm_8_mark5_1_p14 = In_Out_prime ? I_Odat : 8'bz;  // Controlled_Buffer controlled_buffer_1
  not not_3 (not_3_out, nand_1_out);
  DotMatrix #(.matrixcols(32), .matrixrows(32)) dotmatrix_3 (
    .col0(screen_memo_3_out_4), .col1(screen_memo_3_out_5), .col2(screen_memo_3_out_6),
    .col3(screen_memo_3_out_7), .col4(screen_memo_3_out_8), .col5(screen_memo_3_out_9),
    .col6(screen_memo_3_out_10), .col7(screen_memo_3_out_11), .col8(screen_memo_3_out_12),
    .col9(screen_memo_3_out_13), .col10(screen_memo_3_out_14), .col11(screen_memo_3_out_15),
    .col12(screen_memo_3_out_16), .col13(screen_memo_3_out_17), .col14(screen_memo_3_out_18),
    .col15(screen_memo_3_out_19), .col16(screen_memo_3_out_20), .col17(screen_memo_3_out_21),
    .col18(screen_memo_3_out_22), .col19(screen_memo_3_out_23), .col20(screen_memo_3_out_24),
    .col21(screen_memo_3_out_25), .col22(screen_memo_3_out_26), .col23(screen_memo_3_out_27),
    .col24(screen_memo_3_out_28), .col25(screen_memo_3_out_29), .col26(screen_memo_3_out_30),
    .col27(screen_memo_3_out_31), .col28(screen_memo_3_out_32), .col29(screen_memo_3_out_33),
    .col30(screen_memo_3_out_34), .col31(screen_memo_3_out_35));
  screen_memo screen_memo_3 (
    .new_column(graphics_man_1_screen_4), .out_4(screen_memo_3_out_4), .out_5(screen_memo_3_out_5),
    .out_6(screen_memo_3_out_6), .out_7(screen_memo_3_out_7), .out_8(screen_memo_3_out_8),
    .out_9(screen_memo_3_out_9), .out_10(screen_memo_3_out_10), .out_11(screen_memo_3_out_11),
    .out_12(screen_memo_3_out_12), .out_13(screen_memo_3_out_13), .out_14(screen_memo_3_out_14),
    .out_15(screen_memo_3_out_15), .out_16(screen_memo_3_out_16), .out_17(screen_memo_3_out_17),
    .out_18(screen_memo_3_out_18), .out_19(screen_memo_3_out_19), .out_20(screen_memo_3_out_20),
    .out_21(screen_memo_3_out_21), .out_22(screen_memo_3_out_22), .out_23(screen_memo_3_out_23),
    .out_24(screen_memo_3_out_24), .out_25(screen_memo_3_out_25), .out_26(screen_memo_3_out_26),
    .out_27(screen_memo_3_out_27), .out_28(screen_memo_3_out_28), .out_29(screen_memo_3_out_29),
    .out_30(screen_memo_3_out_30), .out_31(screen_memo_3_out_31), .out_32(screen_memo_3_out_32),
    .out_33(screen_memo_3_out_33), .out_34(screen_memo_3_out_34), .out_35(screen_memo_3_out_35),
    .clock(multiplexer_1_out), .x(counter_2_q));
  screen_memo screen_memo_4 (
    .new_column(graphics_man_1_screen_2), .out_4(screen_memo_4_out_4), .out_5(screen_memo_4_out_5),
    .out_6(screen_memo_4_out_6), .out_7(screen_memo_4_out_7), .out_8(screen_memo_4_out_8),
    .out_9(screen_memo_4_out_9), .out_10(screen_memo_4_out_10), .out_11(screen_memo_4_out_11),
    .out_12(screen_memo_4_out_12), .out_13(screen_memo_4_out_13), .out_14(screen_memo_4_out_14),
    .out_15(screen_memo_4_out_15), .out_16(screen_memo_4_out_16), .out_17(screen_memo_4_out_17),
    .out_18(screen_memo_4_out_18), .out_19(screen_memo_4_out_19), .out_20(screen_memo_4_out_20),
    .out_21(screen_memo_4_out_21), .out_22(screen_memo_4_out_22), .out_23(screen_memo_4_out_23),
    .out_24(screen_memo_4_out_24), .out_25(screen_memo_4_out_25), .out_26(screen_memo_4_out_26),
    .out_27(screen_memo_4_out_27), .out_28(screen_memo_4_out_28), .out_29(screen_memo_4_out_29),
    .out_30(screen_memo_4_out_30), .out_31(screen_memo_4_out_31), .out_32(screen_memo_4_out_32),
    .out_33(screen_memo_4_out_33), .out_34(screen_memo_4_out_34), .out_35(screen_memo_4_out_35),
    .clock(multiplexer_1_out), .x(counter_2_q));
  DotMatrix #(.matrixcols(32), .matrixrows(32)) dotmatrix_4 (
    .col0(screen_memo_4_out_4), .col1(screen_memo_4_out_5), .col2(screen_memo_4_out_6),
    .col3(screen_memo_4_out_7), .col4(screen_memo_4_out_8), .col5(screen_memo_4_out_9),
    .col6(screen_memo_4_out_10), .col7(screen_memo_4_out_11), .col8(screen_memo_4_out_12),
    .col9(screen_memo_4_out_13), .col10(screen_memo_4_out_14), .col11(screen_memo_4_out_15),
    .col12(screen_memo_4_out_16), .col13(screen_memo_4_out_17), .col14(screen_memo_4_out_18),
    .col15(screen_memo_4_out_19), .col16(screen_memo_4_out_20), .col17(screen_memo_4_out_21),
    .col18(screen_memo_4_out_22), .col19(screen_memo_4_out_23), .col20(screen_memo_4_out_24),
    .col21(screen_memo_4_out_25), .col22(screen_memo_4_out_26), .col23(screen_memo_4_out_27),
    .col24(screen_memo_4_out_28), .col25(screen_memo_4_out_29), .col26(screen_memo_4_out_30),
    .col27(screen_memo_4_out_31), .col28(screen_memo_4_out_32), .col29(screen_memo_4_out_33),
    .col30(screen_memo_4_out_34), .col31(screen_memo_4_out_35));
  Button reset_ball (.out(reset_ball_out));
  Decoder #(.disabled(0)) decoder_1 (.out0(code), .out1(data), .sel(cdm_8_mark5_1_p9), .en(mem));
  assign I_Odat = not_2_out ? cdm_8_mark5_1_p13 : 8'bz;  // Controlled_Buffer controlled_buffer_2
  and and_2 (RAM, nand_1_out, data);
  nand nand_1 (nand_1_out, ~cdm_8_mark5_1_p12[3], cdm_8_mark5_1_p12[4], cdm_8_mark5_1_p12[5], cdm_8_mark5_1_p12[6], cdm_8_mark5_1_p12[7]);  // NAND_Gate
  ROM rom_5 (.addr({cdm_8_mark5_1_p12, I_Oadr}), .data(I_Odat), .sel(code));
  RAM ram_5 (.addr({cdm_8_mark5_1_p12, I_Oadr}), .data(I_Odat), .sel(RAM), .clk(cl), .ld(In_Out_prime));  // open: clr
  not not_4 (not_4_out, not_4_out);
  not not_5 (not_5_out, not_5_out);
  and and_3 (read, I_Osel, In_Out_prime);
  Multiplexer #(.select(3), .width(8)) multiplexer_3 (
    .in1({rs_latch_1_p3[7], register_2_q}), .out(I_Odat), .sel(I_Oadr), .en(read));  // open: in0, in2, in3, in4, in5, in6, in7
  and and_4 (write, I_Osel, ~In_Out_prime);  // AND_Gate
  Demultiplexer #(.select(3), .width(8)) demultiplexer_1 (
    .out1(demultiplexer_1_out1), .in(I_Odat), .sel(I_Oadr), .en(write));  // open: out0, out2, out3, out4, out5, out6, out7
  Button a (.out(a_out));
  assign controlled_buffer_3_out = a_out ? 7'b1100001 : 7'bz;  // Controlled_Buffer controlled_buffer_3
  Button b (.out(b_out));
  Transistor #(.\type ("n")) transistor_4 (.in(1'b0), .out(transistor_4_out), .gate(a_out));
  Transistor #(.\type ("n")) transistor_5 (.in(1'b0), .out(transistor_4_out), .gate(b_out));
  assign controlled_buffer_3_out = b_out ? 7'b1100010 : 7'bz;  // Controlled_Buffer controlled_buffer_4
  nor nor_1 (nor_1_out, transistor_4_out, not_6_out);
  not not_6 (not_6_out, transistor_4_out);
  nor nor_2 (nor_2_out, read, not_7_out);
  not not_7 (not_7_out, read);
  Button c (.out(c_out));
  Transistor #(.\type ("n")) transistor_6 (.in(1'b0), .out(transistor_4_out), .gate(c_out));
  assign controlled_buffer_3_out = c_out ? 7'b1100011 : 7'bz;  // Controlled_Buffer controlled_buffer_5
  Hex_Digit_Display hex_digit_display_1 (.value(register_1_q_2));  // open: dp
  Hex_Digit_Display hex_digit_display_2 (.value(register_1_q));  // open: dp
  Register #(.trigger("falling")) register_1 (
    .D(demultiplexer_1_out1), .Q({register_1_q_2, register_1_q}), .clk(write));  // open: en, clr
  Pull_Resistor #(.pull(1)) pull_resistor_1 (.node(transistor_4_out));
  Button d (.out(d_out));
  Transistor #(.\type ("n")) transistor_7 (.in(1'b0), .out(transistor_4_out), .gate(d_out));
  assign controlled_buffer_3_out = d_out ? 7'b1100100 : 7'bz;  // Controlled_Buffer controlled_buffer_6
  // RS_latch rs_latch_1: pin names not known; wires that end beside it: nor_1_out, nor_2_out, rs_latch_1_p3[7]
  not not_8 (not_8_out, not_9_out);
  not not_9 (not_9_out, transistor_4_out);
  Register #(.width(7), .trigger("falling")) register_2 (
    .D(controlled_buffer_3_out), .Q(register_2_q), .clk(not_8_out));  // open: en, clr

  // Other names for the same wires on the sheet: rd_wr_prime = In_Out_prime

  // Notes on the sheet:
  //   contents of rom_1 (hex, n*v repeats v):
  //   605800c0 6000a080 60600040 6060ff40 0 40f8c0c0 40c00080 40b880c0 40804080 0 0 40408080 407840c0
  //   contents of rom_2 (hex, n*v repeats v):
  //   605800c0 6000a080 60600040 6060ff40 0 40f8c0c0 40c00080 40b880c0 40804080 0 0 40408080 407840c0
  //   contents of rom_3 (hex, n*v repeats v):
  //   605800c0 6000a080 60600040 6060ff40 0 40f8c0c0 40c00080 40b880c0 40804080 0 0 40408080 407840c0
  //   contents of rom_4 (hex, n*v repeats v):
  //   605800c0 6000a080 60600040 6060ff40 0 40f8c0c0 40c00080 40b880c0 40804080 0 0 40408080 407840c0
  //   In/Out == rd/wr'
  //   I/Osel signal plays role ef clock for the I/O Registers
  //   I/Oadr signal is a 3-bit bunch carrying 3 lower-order bits of tha address = I/O Registers
  //   instr memory
  //   data memory
  //   contents of rom_5 (hex, n*v repeats v):
  //   d0 f0 c1 d1 8 a4 c5 cd 0 d0 f1 b1 5 e4 b a1 ee b
  //   status: 0: ready
  //   key code
  //   1: waiting
endmodule

module ball (
  input  [9:0] start_vx,
  input  [9:0] start_vy,
  input  [31:0] ball_data,
  input  Clock,
  input  Reset,
  output [31:0] Updated_ball
);

  wire [9:0] adder_2_out, adder_4_out, collide0_1_res_vx, collide0_1_res_vy, multiplexer_1_out,
       multiplexer_2_out, shifter_1_out, shifter_2_out, velo_x_q, velo_y_q;

  Pull_Resistor pull_resistor_1 (.node(start_vx));
  Pull_Resistor pull_resistor_2 (.node(start_vy));
  // Probe on ball_data[1:0]
  // Probe on ball_data[31:22]
  Multiplexer #(.width(10)) multiplexer_1 (
    .in0(collide0_1_res_vx), .in1(start_vx), .out(multiplexer_1_out), .sel(Reset));  // open: en
  // Probe on ball_data[11:2]
  // Probe on ball_data[21:12]
  Register #(.width(10), .trigger("falling")) velo_x (
    .D(multiplexer_1_out), .Q(velo_x_q), .clk(Clock));  // open: en, clr
  Multiplexer #(.width(10)) multiplexer_2 (
    .in0(adder_4_out), .in1(start_vy), .out(multiplexer_2_out), .sel(Reset));  // open: en
  Shifter #(.width(10), .shift("ar")) shifter_1 (.in(velo_x_q), .\dist (4'b0011), .out(shifter_1_out));
  Adder #(.width(10)) adder_1 (.a(shifter_1_out), .b(ball_data[11:2]), .out(Updated_ball[11:2]));  // open: cin, cout
  Pull_Resistor pull_resistor_3 (.node(Reset));
  Adder #(.width(10)) adder_2 (.a({10{1'b1}}), .b(velo_y_q), .out(adder_2_out));  // open: cin, cout
  Register #(.width(10), .trigger("falling")) velo_y (
    .D(multiplexer_2_out), .Q(velo_y_q), .clk(Clock));  // open: en, clr
  Adder #(.width(10)) adder_3 (.a(shifter_2_out), .b(ball_data[21:12]), .out(Updated_ball[21:12]));  // open: cin, cout
  collide0 collide0_1 (
    .start_vx(velo_x_q), .start_vy(adder_2_out), .ball_data(ball_data), .res_vx(collide0_1_res_vx),
    .res_vy(collide0_1_res_vy));
  Shifter #(.width(10), .shift("ar")) shifter_2 (.in(velo_y_q), .\dist (4'b0011), .out(shifter_2_out));
  Adder #(.width(10)) adder_4 (.a({10{1'b1}}), .b(collide0_1_res_vy), .out(adder_4_out));  // open: cin, cout

  assign {Updated_ball[31:22], Updated_ball[1:0]} = {ball_data[31:22], ball_data[1:0]};

  // Other names for the same wires on the sheet: ball_type[1:0] = ball_data[1:0]; ball_size[9:0] = ball_data[31:22]
endmodule

module collide0 (
  input  [9:0] start_vx,
  input  [9:0] start_vy,
  input  [31:0] ball_data,
  output [9:0] res_vx,
  output [9:0] res_vy
);

  wire move_1_owf_x, move_1_owf_y;
  wire [9:0] negator_1_out, negator_2_out;

  move move_1 (
    .start_vx(start_vx), .start_vy(start_vy), .ball_data(ball_data), .owf_x(move_1_owf_x),
    .owf_y(move_1_owf_y));  // open: Updated_ball
  Negator #(.width(10)) negator_1 (.in(start_vx), .out(negator_1_out));
  Multiplexer #(.width(10)) multiplexer_1 (
    .in0(start_vx), .in1(negator_1_out), .out(res_vx), .sel(move_1_owf_x));  // open: en
  Negator #(.width(10)) negator_2 (.in(start_vy), .out(negator_2_out));
  Multiplexer #(.width(10)) multiplexer_2 (
    .in0(start_vy), .in1(negator_2_out), .out(res_vy), .sel(move_1_owf_y));  // open: en
endmodule

module move (
  input  [9:0] start_vx,
  input  [9:0] start_vy,
  input  [31:0] ball_data,
  output [31:0] Updated_ball,
  output owf_x,
  output owf_y
);

  wire adder_1_cout, adder_2_cout;
  wire [9:0] shifter_1_out, shifter_2_out;

  // Probe on ball_data[1:0]
  // Probe on ball_data[31:22]
  // Probe on ball_data[11:2]
  // Probe on ball_data[21:12]
  Shifter #(.width(10), .shift("ar")) shifter_1 (.in(start_vx), .\dist (4'b0011), .out(shifter_1_out));
  Adder #(.width(10)) adder_1 (
    .a(shifter_1_out), .b(ball_data[11:2]), .out(Updated_ball[11:2]), .cout(adder_1_cout));  // open: cin
  xor odd_parity_1 (owf_x, start_vx[9], adder_1_cout);
  Shifter #(.width(10), .shift("ar")) shifter_2 (.in(start_vy), .\dist (4'b0011), .out(shifter_2_out));
  Adder #(.width(10)) adder_2 (
    .a(shifter_2_out), .b(ball_data[21:12]), .out(Updated_ball[21:12]), .cout(adder_2_cout));  // open: cin
  xor odd_parity_2 (owf_y, start_vy[9], adder_2_cout);

  assign {Updated_ball[31:22], Updated_ball[1:0]} = {ball_data[31:22], ball_data[1:0]};

  // Other names for the same wires on the sheet: ball_type[1:0] = ball_data[1:0]; ball_size[9:0] = ball_data[31:22]
endmodule

module graphics_ultra (
  input  [31:0] base,
  input  input_ball,
  input  [4:0] ball_x,
  input  [4:0] ball_y,
  input  is_active,
  input  [25:0] object,
  input  [4:0] current_x,
  output [31:0] out_8
);

  wire adder_1_cout, and_1_out, and_2_out, comparator_1_eq, comparator_2_gt, comparator_3_eq,
       comparator_3_lt, or_2_out, or_3_out;
  wire [4:0] adder_1_out;
  wire [31:0] decoder_1_out0, demultiplexer_1_out0, multiplexer_1_out, transistor_1_out;

  // Probe on object[1:0]
  // Probe on object[9:2]
  // Probe on object[17:10]
  // Probe on object[25:18]
  // Probe on current_x
  and and_1 (and_1_out, input_ball, comparator_1_eq);
  Comparator #(.width(5), .mode("unsigned")) comparator_1 (
    .a(ball_x), .b(current_x), .eq(comparator_1_eq));  // open: gt, lt
  // Probe on object[9:5]
  // Probe on object[17:13]
  // Probe on object[25:21]
  Demultiplexer #(.select(5), .enable("false")) demultiplexer_1 (
    .out0(demultiplexer_1_out0[0]), .out1(demultiplexer_1_out0[1]), .out2(demultiplexer_1_out0[2]),
    .out3(demultiplexer_1_out0[3]), .out4(demultiplexer_1_out0[4]), .out5(demultiplexer_1_out0[5]),
    .out6(demultiplexer_1_out0[6]), .out7(demultiplexer_1_out0[7]), .out8(demultiplexer_1_out0[8]),
    .out9(demultiplexer_1_out0[9]), .out10(demultiplexer_1_out0[10]), .out11(demultiplexer_1_out0[11]),
    .out12(demultiplexer_1_out0[12]), .out13(demultiplexer_1_out0[13]), .out14(demultiplexer_1_out0[14]),
    .out15(demultiplexer_1_out0[15]), .out16(demultiplexer_1_out0[16]), .out17(demultiplexer_1_out0[17]),
    .out18(demultiplexer_1_out0[18]), .out19(demultiplexer_1_out0[19]), .out20(demultiplexer_1_out0[20]),
    .out21(demultiplexer_1_out0[21]), .out22(demultiplexer_1_out0[22]), .out23(demultiplexer_1_out0[23]),
    .out24(demultiplexer_1_out0[24]), .out25(demultiplexer_1_out0[25]), .out26(demultiplexer_1_out0[26]),
    .out27(demultiplexer_1_out0[27]), .out28(demultiplexer_1_out0[28]), .out29(demultiplexer_1_out0[29]),
    .out30(demultiplexer_1_out0[30]), .out31(demultiplexer_1_out0[31]), .in(and_1_out), .sel(ball_y));
  Decoder #(.select(5), .enable("false")) decoder_1 (
    .out0(decoder_1_out0[0]), .out1(decoder_1_out0[1]), .out2(decoder_1_out0[2]), .out3(decoder_1_out0[3]),
    .out4(decoder_1_out0[4]), .out5(decoder_1_out0[5]), .out6(decoder_1_out0[6]), .out7(decoder_1_out0[7]),
    .out8(decoder_1_out0[8]), .out9(decoder_1_out0[9]), .out10(decoder_1_out0[10]),
    .out11(decoder_1_out0[11]), .out12(decoder_1_out0[12]), .out13(decoder_1_out0[13]),
    .out14(decoder_1_out0[14]), .out15(decoder_1_out0[15]), .out16(decoder_1_out0[16]),
    .out17(decoder_1_out0[17]), .out18(decoder_1_out0[18]), .out19(decoder_1_out0[19]),
    .out20(decoder_1_out0[20]), .out21(decoder_1_out0[21]), .out22(decoder_1_out0[22]),
    .out23(decoder_1_out0[23]), .out24(decoder_1_out0[24]), .out25(decoder_1_out0[25]),
    .out26(decoder_1_out0[26]), .out27(decoder_1_out0[27]), .out28(decoder_1_out0[28]),
    .out29(decoder_1_out0[29]), .out30(decoder_1_out0[30]), .out31(decoder_1_out0[31]), .sel(object[17:13]));
  Pull_Resistor pull_resistor_1 (.node(base));
  Multiplexer #(.width(32)) multiplexer_1 (
    .in0({32{1'b0}}), .in1(transistor_1_out), .out(multiplexer_1_out), .sel(is_active));  // open: en
  Pull_Resistor pull_resistor_2 (.node(is_active));
  assign out_8 = base | demultiplexer_1_out0 | multiplexer_1_out;  // OR_Gate or_1, 32 bits wide
  Adder #(.width(5)) adder_1 (.a(object[9:5]), .b(object[25:21]), .out(adder_1_out), .cout(adder_1_cout));  // open: cin
  // Probe on decoder_1_out0
  Comparator #(.width(5), .mode("unsigned")) comparator_2 (
    .a(adder_1_out), .b(current_x), .gt(comparator_2_gt));  // open: eq, lt
  Comparator #(.width(5), .mode("unsigned")) comparator_3 (
    .a(object[9:5]), .b(current_x), .eq(comparator_3_eq), .lt(comparator_3_lt));  // open: gt
  or or_2 (or_2_out, comparator_2_gt, adder_1_cout);
  and and_2 (and_2_out, or_2_out, or_3_out);
  or or_3 (or_3_out, comparator_3_eq, comparator_3_lt);
  Transistor #(.width(32)) transistor_1 (.in({32{1'b0}}), .out(transistor_1_out), .gate(and_2_out));
  Transistor #(.\type ("n"), .width(32)) transistor_2 (.in(decoder_1_out0), .out(transistor_1_out), .gate(and_2_out));
endmodule

module screen_memo (
  input  [31:0] new_column,
  input  clock,
  input  [4:0] x,
  output [31:0] out_4,
  output [31:0] out_5,
  output [31:0] out_6,
  output [31:0] out_7,
  output [31:0] out_8,
  output [31:0] out_9,
  output [31:0] out_10,
  output [31:0] out_11,
  output [31:0] out_12,
  output [31:0] out_13,
  output [31:0] out_14,
  output [31:0] out_15,
  output [31:0] out_16,
  output [31:0] out_17,
  output [31:0] out_18,
  output [31:0] out_19,
  output [31:0] out_20,
  output [31:0] out_21,
  output [31:0] out_22,
  output [31:0] out_23,
  output [31:0] out_24,
  output [31:0] out_25,
  output [31:0] out_26,
  output [31:0] out_27,
  output [31:0] out_28,
  output [31:0] out_29,
  output [31:0] out_30,
  output [31:0] out_31,
  output [31:0] out_32,
  output [31:0] out_33,
  output [31:0] out_34,
  output [31:0] out_35
);

  wire [31:0] demultiplexer_1_out0, demultiplexer_1_out1, demultiplexer_1_out2, demultiplexer_1_out3,
       demultiplexer_1_out4, demultiplexer_1_out5, demultiplexer_1_out6, demultiplexer_1_out7,
       demultiplexer_1_out8, demultiplexer_1_out9, demultiplexer_1_out10, demultiplexer_1_out11,
       demultiplexer_1_out12, demultiplexer_1_out13, demultiplexer_1_out14, demultiplexer_1_out15,
       demultiplexer_1_out16, demultiplexer_1_out17, demultiplexer_1_out18, demultiplexer_1_out19,
       demultiplexer_1_out20, demultiplexer_1_out21, demultiplexer_1_out22, demultiplexer_1_out23,
       demultiplexer_1_out24, demultiplexer_1_out25, demultiplexer_1_out26, demultiplexer_1_out27,
       demultiplexer_1_out28, demultiplexer_1_out29, demultiplexer_1_out30, demultiplexer_1_out31;

  Demultiplexer #(.select(5), .width(32), .tristate("true")) demultiplexer_1 (
    .out0(demultiplexer_1_out0), .out1(demultiplexer_1_out1), .out2(demultiplexer_1_out2),
    .out3(demultiplexer_1_out3), .out4(demultiplexer_1_out4), .out5(demultiplexer_1_out5),
    .out6(demultiplexer_1_out6), .out7(demultiplexer_1_out7), .out8(demultiplexer_1_out8),
    .out9(demultiplexer_1_out9), .out10(demultiplexer_1_out10), .out11(demultiplexer_1_out11),
    .out12(demultiplexer_1_out12), .out13(demultiplexer_1_out13), .out14(demultiplexer_1_out14),
    .out15(demultiplexer_1_out15), .out16(demultiplexer_1_out16), .out17(demultiplexer_1_out17),
    .out18(demultiplexer_1_out18), .out19(demultiplexer_1_out19), .out20(demultiplexer_1_out20),
    .out21(demultiplexer_1_out21), .out22(demultiplexer_1_out22), .out23(demultiplexer_1_out23),
    .out24(demultiplexer_1_out24), .out25(demultiplexer_1_out25), .out26(demultiplexer_1_out26),
    .out27(demultiplexer_1_out27), .out28(demultiplexer_1_out28), .out29(demultiplexer_1_out29),
    .out30(demultiplexer_1_out30), .out31(demultiplexer_1_out31), .in(new_column), .sel(x));  // open: en
  Register #(.width(32)) register_1 (.D(demultiplexer_1_out0), .Q(out_4), .clk(clock));  // open: en, clr
  Register #(.width(32)) register_2 (.D(demultiplexer_1_out1), .Q(out_5), .clk(clock));  // open: en, clr
  Register #(.width(32)) register_3 (.D(demultiplexer_1_out2), .Q(out_6), .clk(clock));  // open: en, clr
  Register #(.width(32)) register_4 (.D(demultiplexer_1_out3), .Q(out_7), .clk(clock));  // open: en, clr
  Register #(.width(32)) register_5 (.D(demultiplexer_1_out4), .Q(out_8), .clk(clock));  // open: en, clr
  Register #(.width(32)) register_6 (.D(demultiplexer_1_out5), .Q(out_9), .clk(clock));  // open: en, clr
  Register #(.width(32)) register_7 (.D(demultiplexer_1_out6), .Q(out_10), .clk(clock));  // open: en, clr
  Register #(.width(32)) register_8 (.D(demultiplexer_1_out7), .Q(out_11), .clk(clock));  // open: en, clr
  Register #(.width(32)) register_9 (.D(demultiplexer_1_out8), .Q(out_12), .clk(clock));  // open: en, clr
  Register #(.width(32)) register_10 (.D(demultiplexer_1_out9), .Q(out_13), .clk(clock));  // open: en, clr
  Register #(.width(32)) register_11 (.D(demultiplexer_1_out10), .Q(out_14), .clk(clock));  // open: en, clr
  Register #(.width(32)) register_12 (.D(demultiplexer_1_out11), .Q(out_15), .clk(clock));  // open: en, clr
  Register #(.width(32)) register_13 (.D(demultiplexer_1_out12), .Q(out_16), .clk(clock));  // open: en, clr
  Register #(.width(32)) register_14 (.D(demultiplexer_1_out13), .Q(out_17), .clk(clock));  // open: en, clr
  Register #(.width(32)) register_15 (.D(demultiplexer_1_out14), .Q(out_18), .clk(clock));  // open: en, clr
  Register #(.width(32)) register_16 (.D(demultiplexer_1_out15), .Q(out_19), .clk(clock));  // open: en, clr
  Register #(.width(32)) register_17 (.D(demultiplexer_1_out16), .Q(out_20), .clk(clock));  // open: en, clr
  Register #(.width(32)) register_18 (.D(demultiplexer_1_out17), .Q(out_21), .clk(clock));  // open: en, clr
  Register #(.width(32)) register_19 (.D(demultiplexer_1_out18), .Q(out_22), .clk(clock));  // open: en, clr
  Register #(.width(32)) register_20 (.D(demultiplexer_1_out19), .Q(out_23), .clk(clock));  // open: en, clr
  Register #(.width(32)) register_21 (.D(demultiplexer_1_out20), .Q(out_24), .clk(clock));  // open: en, clr
  Register #(.width(32)) register_22 (.D(demultiplexer_1_out21), .Q(out_25), .clk(clock));  // open: en, clr
  Register #(.width(32)) register_23 (.D(demultiplexer_1_out22), .Q(out_26), .clk(clock));  // open: en, clr
  Register #(.width(32)) register_24 (.D(demultiplexer_1_out23), .Q(out_27), .clk(clock));  // open: en, clr
  Register #(.width(32)) register_25 (.D(demultiplexer_1_out24), .Q(out_28), .clk(clock));  // open: en, clr
  Register #(.width(32)) register_26 (.D(demultiplexer_1_out25), .Q(out_29), .clk(clock));  // open: en, clr
  Register #(.width(32)) register_27 (.D(demultiplexer_1_out26), .Q(out_30), .clk(clock));  // open: en, clr
  Register #(.width(32)) register_28 (.D(demultiplexer_1_out27), .Q(out_31), .clk(clock));  // open: en, clr
  Register #(.width(32)) register_29 (.D(demultiplexer_1_out28), .Q(out_32), .clk(clock));  // open: en, clr
  Register #(.width(32)) register_30 (.D(demultiplexer_1_out29), .Q(out_33), .clk(clock));  // open: en, clr
  Register #(.width(32)) register_31 (.D(demultiplexer_1_out30), .Q(out_34), .clk(clock));  // open: en, clr
  Register #(.width(32)) register_32 (.D(demultiplexer_1_out31), .Q(out_35), .clk(clock));  // open: en, clr
endmodule

module graphics_man (
  input  [31:0] state0,
  input  [31:0] state1,
  input  [31:0] state2,
  input  [31:0] state3,
  input  [31:0] ball_data,
  input  [4:0] x,
  input  clock,
  output [31:0] screen_1,
  output [31:0] screen_2,
  output [31:0] screen_3,
  output [31:0] screen_4,
  output [4:0] x_2
);

  wire decoder_1_out0, decoder_1_out1, decoder_1_out2, decoder_1_out3;
  wire [25:0] undriven, undriven_2, undriven_3;

  Decoder #(.select(2)) decoder_1 (
    .out0(decoder_1_out0), .out1(decoder_1_out1), .out2(decoder_1_out2), .out3(decoder_1_out3),
    .sel({ball_data[21], ball_data[11]}));  // open: en
  graphics_ultra graphics_ultra_1 (
    .input_ball(decoder_1_out0), .ball_x(ball_data[10:6]), .ball_y(ball_data[20:16]), .base(state0),
    .current_x(x), .out_8(screen_1));  // open: is_active, object
  graphics_ultra graphics_ultra_2 (
    .input_ball(decoder_1_out1), .ball_x(ball_data[10:6]), .ball_y(ball_data[20:16]), .object(undriven),
    .base(state1), .current_x(x), .out_8(screen_2));  // open: is_active
  graphics_ultra graphics_ultra_3 (
    .input_ball(decoder_1_out2), .ball_x(ball_data[10:6]), .ball_y(ball_data[20:16]), .object(undriven_2),
    .base(state2), .current_x(x), .out_8(screen_3));  // open: is_active
  graphics_ultra graphics_ultra_4 (
    .input_ball(decoder_1_out3), .ball_x(ball_data[10:6]), .ball_y(ball_data[20:16]), .object(undriven_3),
    .base(state3), .current_x(x), .out_8(screen_4));  // open: is_active

  assign x_2 = x;
endmodule

module draw_object (
  input  [31:0] base,
  input  [25:0] object,
  input  [4:0] row_x,
  output [31:0] result
);

  wire adder_2_cout, and_1_out, comparator_1_eq, comparator_2_gt, comparator_3_eq, comparator_3_lt, or_1_out,
       or_2_out;
  wire [4:0] adder_1_out, adder_2_out, multiplexer_1_out, negator_1_out, subtractor_1_out, transistor_1_out;
  wire [31:0] decoder_1_out0, multiplier_1_out, not_1_out, shifter_1_out, transistor_3_out, transistor_5_out;

  // Probe on object[1:0]
  // Probe on object[9:2]
  // Probe on object[17:10]
  // Probe on object[25:18]
  // Probe on row_x
  // Probe on object[9:5]
  // Probe on object[17:13]
  // Probe on object[25:21]
  Subtractor #(.width(5)) subtractor_1 (.a(object[9:5]), .b(row_x), .out(subtractor_1_out));  // open: bin, bout
  Multiplexer #(.select(2), .width(5)) multiplexer_1 (
    .in0({5{1'b0}}), .in1({5{1'b0}}), .in2(negator_1_out), .in3(subtractor_1_out), .out(multiplexer_1_out),
    .sel(object[1:0]));  // open: en
  Negator #(.width(5)) negator_1 (.in(subtractor_1_out), .out(negator_1_out));
  Decoder #(.select(5)) decoder_1 (
    .out0(decoder_1_out0[0]), .out1(decoder_1_out0[1]), .out2(decoder_1_out0[2]), .out3(decoder_1_out0[3]),
    .out4(decoder_1_out0[4]), .out5(decoder_1_out0[5]), .out6(decoder_1_out0[6]), .out7(decoder_1_out0[7]),
    .out8(decoder_1_out0[8]), .out9(decoder_1_out0[9]), .out10(decoder_1_out0[10]),
    .out11(decoder_1_out0[11]), .out12(decoder_1_out0[12]), .out13(decoder_1_out0[13]),
    .out14(decoder_1_out0[14]), .out15(decoder_1_out0[15]), .out16(decoder_1_out0[16]),
    .out17(decoder_1_out0[17]), .out18(decoder_1_out0[18]), .out19(decoder_1_out0[19]),
    .out20(decoder_1_out0[20]), .out21(decoder_1_out0[21]), .out22(decoder_1_out0[22]),
    .out23(decoder_1_out0[23]), .out24(decoder_1_out0[24]), .out25(decoder_1_out0[25]),
    .out26(decoder_1_out0[26]), .out27(decoder_1_out0[27]), .out28(decoder_1_out0[28]),
    .out29(decoder_1_out0[29]), .out30(decoder_1_out0[30]), .out31(decoder_1_out0[31]), .sel(adder_1_out));  // open: en
  Adder #(.width(5)) adder_1 (.a(multiplexer_1_out), .b(object[17:13]), .out(adder_1_out));  // open: cin, cout
  Comparator #(.width(2)) comparator_1 (.a(object[1:0]), .b(2'b01), .eq(comparator_1_eq));  // open: gt, lt
  // Probe on decoder_1_out0
  Shifter #(.width(32)) shifter_1 (.in({32{1'b1}}), .\dist (object[25:21]), .out(shifter_1_out));
  Transistor #(.width(5)) transistor_1 (.in(object[25:21]), .out(transistor_1_out), .gate(comparator_1_eq));
  Transistor #(.\type ("n"), .width(5)) transistor_2 (.in(5'b00001), .out(transistor_1_out), .gate(comparator_1_eq));
  assign not_1_out = ~shifter_1_out;  // NOT_Gate not_1, 32 bits wide
  Adder #(.width(5)) adder_2 (
    .a(object[9:5]), .b(transistor_1_out), .out(adder_2_out), .cout(adder_2_cout));  // open: cin
  Multiplier #(.width(32)) multiplier_1 (.a(decoder_1_out0), .b(not_1_out), .out(multiplier_1_out));  // open: cin, cout
  or or_1 (or_1_out, comparator_2_gt, adder_2_cout);
  Comparator #(.width(5), .mode("unsigned")) comparator_2 (
    .a(adder_2_out), .b(row_x), .gt(comparator_2_gt));  // open: eq, lt
  or or_2 (or_2_out, comparator_3_eq, comparator_3_lt);
  Comparator #(.width(5), .mode("unsigned")) comparator_3 (
    .a(object[9:5]), .b(row_x), .eq(comparator_3_eq), .lt(comparator_3_lt));  // open: gt
  Transistor #(.width(32)) transistor_3 (.in(decoder_1_out0), .out(transistor_3_out), .gate(comparator_1_eq));
  Transistor #(.\type ("n"), .width(32)) transistor_4 (
    .in(multiplier_1_out), .out(transistor_3_out), .gate(comparator_1_eq));
  and and_1 (and_1_out, or_1_out, or_2_out);
  Transistor #(.width(32)) transistor_5 (.in({32{1'b0}}), .out(transistor_5_out), .gate(and_1_out));
  Transistor #(.\type ("n"), .width(32)) transistor_6 (.in(transistor_3_out), .out(transistor_5_out), .gate(and_1_out));
  assign result = base | transistor_5_out;  // OR_Gate or_3, 32 bits wide
endmodule
