// Logisim project pinball.circ as structural Verilog: 18 circuits, main circuit Main
module Main (
);

  wire and_1_out, and_2_out, button1, button1pressed, button2, button2pressed, clock_1_out,
       collision_happened, counter_1_carry, door_loading, load_button, loading, not_1_out, or_1_out,
       out_of_screen, reset_all_button, reset_button;
  wire [1:0] ball_1_active_screen;
  wire [2:0] object_collide_num;
  wire [3:0] max1, max2, max3, score1, score2, score3;
  wire [4:0] ball_1_ball_x, ball_1_ball_y, column_draw, column_loading, counter_1_q;
  wire [25:0] door_1, door_2, multiplexer_2_out, multiplexer_3_out, object_collide1, object_collide2,
       object_collide3, object_collide4;
  wire [31:0] graphics_main_1_screen_1, graphics_main_1_screen_2, graphics_main_1_screen_3,
       graphics_main_1_screen_4, screen1, screen2, screen3, screen4, screen_memory_1_out_4,
       screen_memory_1_out_5, screen_memory_1_out_6, screen_memory_1_out_7, screen_memory_1_out_8,
       screen_memory_1_out_9, screen_memory_1_out_10, screen_memory_1_out_11, screen_memory_1_out_12,
       screen_memory_1_out_13, screen_memory_1_out_14, screen_memory_1_out_15, screen_memory_1_out_16,
       screen_memory_1_out_17, screen_memory_1_out_18, screen_memory_1_out_19, screen_memory_1_out_20,
       screen_memory_1_out_21, screen_memory_1_out_22, screen_memory_1_out_23, screen_memory_1_out_24,
       screen_memory_1_out_25, screen_memory_1_out_26, screen_memory_1_out_27, screen_memory_1_out_28,
       screen_memory_1_out_29, screen_memory_1_out_30, screen_memory_1_out_31, screen_memory_1_out_32,
       screen_memory_1_out_33, screen_memory_1_out_34, screen_memory_1_out_35, screen_memory_2_out_4,
       screen_memory_2_out_5, screen_memory_2_out_6, screen_memory_2_out_7, screen_memory_2_out_8,
       screen_memory_2_out_9, screen_memory_2_out_10, screen_memory_2_out_11, screen_memory_2_out_12,
       screen_memory_2_out_13, screen_memory_2_out_14, screen_memory_2_out_15, screen_memory_2_out_16,
       screen_memory_2_out_17, screen_memory_2_out_18, screen_memory_2_out_19, screen_memory_2_out_20,
       screen_memory_2_out_21, screen_memory_2_out_22, screen_memory_2_out_23, screen_memory_2_out_24,
       screen_memory_2_out_25, screen_memory_2_out_26, screen_memory_2_out_27, screen_memory_2_out_28,
       screen_memory_2_out_29, screen_memory_2_out_30, screen_memory_2_out_31, screen_memory_2_out_32,
       screen_memory_2_out_33, screen_memory_2_out_34, screen_memory_2_out_35, screen_memory_3_out_4,
       screen_memory_3_out_5, screen_memory_3_out_6, screen_memory_3_out_7, screen_memory_3_out_8,
       screen_memory_3_out_9, screen_memory_3_out_10, screen_memory_3_out_11, screen_memory_3_out_12,
       screen_memory_3_out_13, screen_memory_3_out_14, screen_memory_3_out_15, screen_memory_3_out_16,
       screen_memory_3_out_17, screen_memory_3_out_18, screen_memory_3_out_19, screen_memory_3_out_20,
       screen_memory_3_out_21, screen_memory_3_out_22, screen_memory_3_out_23, screen_memory_3_out_24,
       screen_memory_3_out_25, screen_memory_3_out_26, screen_memory_3_out_27, screen_memory_3_out_28,
       screen_memory_3_out_29, screen_memory_3_out_30, screen_memory_3_out_31, screen_memory_3_out_32,
       screen_memory_3_out_33, screen_memory_3_out_34, screen_memory_3_out_35, screen_memory_4_out_4,
       screen_memory_4_out_5, screen_memory_4_out_6, screen_memory_4_out_7, screen_memory_4_out_8,
       screen_memory_4_out_9, screen_memory_4_out_10, screen_memory_4_out_11, screen_memory_4_out_12,
       screen_memory_4_out_13, screen_memory_4_out_14, screen_memory_4_out_15, screen_memory_4_out_16,
       screen_memory_4_out_17, screen_memory_4_out_18, screen_memory_4_out_19, screen_memory_4_out_20,
       screen_memory_4_out_21, screen_memory_4_out_22, screen_memory_4_out_23, screen_memory_4_out_24,
       screen_memory_4_out_25, screen_memory_4_out_26, screen_memory_4_out_27, screen_memory_4_out_28,
       screen_memory_4_out_29, screen_memory_4_out_30, screen_memory_4_out_31, screen_memory_4_out_32,
       screen_memory_4_out_33, screen_memory_4_out_34, screen_memory_4_out_35;

  Clock clock_1 (.out(clock_1_out));
  and and_1 (and_1_out, button1, door_loading);
  and and_2 (and_2_out, button2, door_loading);
  not not_1 (not_1_out, loading);
  Counter #(.width(5), .max('h1f)) counter_1 (
    .Q(counter_1_q), .carry(counter_1_carry), .clk(clock_1_out));  // open: load, D, count, clr
  D_Flip_Flop d_ff_1 (.clk(counter_1_carry), .D(1'b0), .Q(button1), .preset(button1pressed));  // open: Qn, en, reset
  Multiplexer #(.width(5), .enable("false")) multiplexer_1 (
    .in0(column_loading), .in1(counter_1_q), .out(column_draw), .sel(not_1_out));
  D_Flip_Flop d_ff_2 (.clk(counter_1_carry), .D(1'b0), .Q(button2), .preset(button2pressed));  // open: Qn, en, reset
  Multiplexer #(.width(26), .enable("false")) multiplexer_2 (
    .in0(object_collide1), .in1(door_1), .out(multiplexer_2_out), .sel(and_1_out));
  Multiplexer #(.width(26), .enable("false")) multiplexer_3 (
    .in0(object_collide2), .in1(door_2), .out(multiplexer_3_out), .sel(and_2_out));
  or or_1 (or_1_out, reset_button, reset_all_button);
  Score_Counter score_counter_1 (
    .collision_happened(collision_happened), .out_of_screen(out_of_screen), .reset_all(reset_all_button),
    .score_AXX(score1), .score_XAX(score2), .score_XXA(score3), .max_AXX(max1), .max_XAX(max2), .max_XXA(max3));
  Ball ball_1 (
    .RESET(or_1_out), .wall_on_screen_4(object_collide4), .wall_on_screen_3(object_collide3),
    .wall_on_screen_2(multiplexer_3_out), .wall_on_screen_1(multiplexer_2_out),
    .active_screen(ball_1_active_screen), .ball_x(ball_1_ball_x), .ball_y(ball_1_ball_y),
    .collision_happened(collision_happened), .out_of_screen(out_of_screen),
    .object_collide_num(object_collide_num), .CLK(clock_1_out));
  // Probe on object_collide_num
  // Probe on ball_1_ball_x
  // Probe on ball_1_ball_y
  // Probe on ball_1_active_screen
  Button RESET_BALL (.out(reset_button));
  Button LOAD_GAME (.out(load_button));
  Button RESET_ALL (.out(reset_all_button));
  Level_Data level_data_1 (
    .object_collide_num(object_collide_num), .column_draw(column_draw), .screen_1(screen1),
    .screen_2(screen2), .screen_3(screen3), .screen_4(screen4), .object_1(object_collide1),
    .object_2(object_collide2), .object_3(object_collide3), .object_4(object_collide4),
    .Reset(reset_all_button), .Load_Game(load_button), .out_14(column_loading), .out_13(loading),
    .door_1(door_1), .door_2(door_2), .loading_door(door_loading));
  Hex_Digit_Display hex_digit_display_1 (.value(max3));  // open: dp
  Hex_Digit_Display hex_digit_display_2 (.value(score3));  // open: dp
  Graphics_Main graphics_main_1 (
    .active_screen(ball_1_active_screen), .ball_x(ball_1_ball_x), .ball_y(ball_1_ball_y), .active_1(button1),
    .active_2(button2), .screen_1(graphics_main_1_screen_1), .screen_2(graphics_main_1_screen_2),
    .screen_3(graphics_main_1_screen_3), .screen_4(graphics_main_1_screen_4), .state0(screen1),
    .state1(screen2), .state2(screen3), .state3(screen4), .x(column_draw));
  Hex_Digit_Display hex_digit_display_3 (.value(max1));  // open: dp
  Hex_Digit_Display hex_digit_display_4 (.value(max2));  // open: dp
  Hex_Digit_Display hex_digit_display_5 (.value(score1));  // open: dp
  Hex_Digit_Display hex_digit_display_6 (.value(score2));  // open: dp
  DotMatrix #(.matrixcols(32), .matrixrows(32)) dotmatrix_1 (
    .col0(screen_memory_1_out_4), .col1(screen_memory_1_out_5), .col2(screen_memory_1_out_6),
    .col3(screen_memory_1_out_7), .col4(screen_memory_1_out_8), .col5(screen_memory_1_out_9),
    .col6(screen_memory_1_out_10), .col7(screen_memory_1_out_11), .col8(screen_memory_1_out_12),
    .col9(screen_memory_1_out_13), .col10(screen_memory_1_out_14), .col11(screen_memory_1_out_15),
    .col12(screen_memory_1_out_16), .col13(screen_memory_1_out_17), .col14(screen_memory_1_out_18),
    .col15(screen_memory_1_out_19), .col16(screen_memory_1_out_20), .col17(screen_memory_1_out_21),
    .col18(screen_memory_1_out_22), .col19(screen_memory_1_out_23), .col20(screen_memory_1_out_24),
    .col21(screen_memory_1_out_25), .col22(screen_memory_1_out_26), .col23(screen_memory_1_out_27),
    .col24(screen_memory_1_out_28), .col25(screen_memory_1_out_29), .col26(screen_memory_1_out_30),
    .col27(screen_memory_1_out_31), .col28(screen_memory_1_out_32), .col29(screen_memory_1_out_33),
    .col30(screen_memory_1_out_34), .col31(screen_memory_1_out_35));
  Screen_Memory screen_memory_1 (
    .new_column(graphics_main_1_screen_3), .out_4(screen_memory_1_out_4), .out_5(screen_memory_1_out_5),
    .out_6(screen_memory_1_out_6), .out_7(screen_memory_1_out_7), .out_8(screen_memory_1_out_8),
    .out_9(screen_memory_1_out_9), .out_10(screen_memory_1_out_10), .out_11(screen_memory_1_out_11),
    .out_12(screen_memory_1_out_12), .out_13(screen_memory_1_out_13), .out_14(screen_memory_1_out_14),
    .out_15(screen_memory_1_out_15), .out_16(screen_memory_1_out_16), .out_17(screen_memory_1_out_17),
    .out_18(screen_memory_1_out_18), .out_19(screen_memory_1_out_19), .out_20(screen_memory_1_out_20),
    .out_21(screen_memory_1_out_21), .out_22(screen_memory_1_out_22), .out_23(screen_memory_1_out_23),
    .out_24(screen_memory_1_out_24), .out_25(screen_memory_1_out_25), .out_26(screen_memory_1_out_26),
    .out_27(screen_memory_1_out_27), .out_28(screen_memory_1_out_28), .out_29(screen_memory_1_out_29),
    .out_30(screen_memory_1_out_30), .out_31(screen_memory_1_out_31), .out_32(screen_memory_1_out_32),
    .out_33(screen_memory_1_out_33), .out_34(screen_memory_1_out_34), .out_35(screen_memory_1_out_35),
    .clock(clock_1_out), .x(column_draw));
  DotMatrix #(.matrixcols(32), .matrixrows(32)) dotmatrix_2 (
    .col0(screen_memory_2_out_4), .col1(screen_memory_2_out_5), .col2(screen_memory_2_out_6),
    .col3(screen_memory_2_out_7), .col4(screen_memory_2_out_8), .col5(screen_memory_2_out_9),
    .col6(screen_memory_2_out_10), .col7(screen_memory_2_out_11), .col8(screen_memory_2_out_12),
    .col9(screen_memory_2_out_13), .col10(screen_memory_2_out_14), .col11(screen_memory_2_out_15),
    .col12(screen_memory_2_out_16), .col13(screen_memory_2_out_17), .col14(screen_memory_2_out_18),
    .col15(screen_memory_2_out_19), .col16(screen_memory_2_out_20), .col17(screen_memory_2_out_21),
    .col18(screen_memory_2_out_22), .col19(screen_memory_2_out_23), .col20(screen_memory_2_out_24),
    .col21(screen_memory_2_out_25), .col22(screen_memory_2_out_26), .col23(screen_memory_2_out_27),
    .col24(screen_memory_2_out_28), .col25(screen_memory_2_out_29), .col26(screen_memory_2_out_30),
    .col27(screen_memory_2_out_31), .col28(screen_memory_2_out_32), .col29(screen_memory_2_out_33),
    .col30(screen_memory_2_out_34), .col31(screen_memory_2_out_35));
  Screen_Memory screen_memory_2 (
    .new_column(graphics_main_1_screen_1), .out_4(screen_memory_2_out_4), .out_5(screen_memory_2_out_5),
    .out_6(screen_memory_2_out_6), .out_7(screen_memory_2_out_7), .out_8(screen_memory_2_out_8),
    .out_9(screen_memory_2_out_9), .out_10(screen_memory_2_out_10), .out_11(screen_memory_2_out_11),
    .out_12(screen_memory_2_out_12), .out_13(screen_memory_2_out_13), .out_14(screen_memory_2_out_14),
    .out_15(screen_memory_2_out_15), .out_16(screen_memory_2_out_16), .out_17(screen_memory_2_out_17),
    .out_18(screen_memory_2_out_18), .out_19(screen_memory_2_out_19), .out_20(screen_memory_2_out_20),
    .out_21(screen_memory_2_out_21), .out_22(screen_memory_2_out_22), .out_23(screen_memory_2_out_23),
    .out_24(screen_memory_2_out_24), .out_25(screen_memory_2_out_25), .out_26(screen_memory_2_out_26),
    .out_27(screen_memory_2_out_27), .out_28(screen_memory_2_out_28), .out_29(screen_memory_2_out_29),
    .out_30(screen_memory_2_out_30), .out_31(screen_memory_2_out_31), .out_32(screen_memory_2_out_32),
    .out_33(screen_memory_2_out_33), .out_34(screen_memory_2_out_34), .out_35(screen_memory_2_out_35),
    .clock(clock_1_out), .x(column_draw));
  DotMatrix #(.matrixcols(32), .matrixrows(32)) dotmatrix_3 (
    .col0(screen_memory_3_out_4), .col1(screen_memory_3_out_5), .col2(screen_memory_3_out_6),
    .col3(screen_memory_3_out_7), .col4(screen_memory_3_out_8), .col5(screen_memory_3_out_9),
    .col6(screen_memory_3_out_10), .col7(screen_memory_3_out_11), .col8(screen_memory_3_out_12),
    .col9(screen_memory_3_out_13), .col10(screen_memory_3_out_14), .col11(screen_memory_3_out_15),
    .col12(screen_memory_3_out_16), .col13(screen_memory_3_out_17), .col14(screen_memory_3_out_18),
    .col15(screen_memory_3_out_19), .col16(screen_memory_3_out_20), .col17(screen_memory_3_out_21),
    .col18(screen_memory_3_out_22), .col19(screen_memory_3_out_23), .col20(screen_memory_3_out_24),
    .col21(screen_memory_3_out_25), .col22(screen_memory_3_out_26), .col23(screen_memory_3_out_27),
    .col24(screen_memory_3_out_28), .col25(screen_memory_3_out_29), .col26(screen_memory_3_out_30),
    .col27(screen_memory_3_out_31), .col28(screen_memory_3_out_32), .col29(screen_memory_3_out_33),
    .col30(screen_memory_3_out_34), .col31(screen_memory_3_out_35));
  Screen_Memory screen_memory_3 (
    .new_column(graphics_main_1_screen_4), .out_4(screen_memory_3_out_4), .out_5(screen_memory_3_out_5),
    .out_6(screen_memory_3_out_6), .out_7(screen_memory_3_out_7), .out_8(screen_memory_3_out_8),
    .out_9(screen_memory_3_out_9), .out_10(screen_memory_3_out_10), .out_11(screen_memory_3_out_11),
    .out_12(screen_memory_3_out_12), .out_13(screen_memory_3_out_13), .out_14(screen_memory_3_out_14),
    .out_15(screen_memory_3_out_15), .out_16(screen_memory_3_out_16), .out_17(screen_memory_3_out_17),
    .out_18(screen_memory_3_out_18), .out_19(screen_memory_3_out_19), .out_20(screen_memory_3_out_20),
    .out_21(screen_memory_3_out_21), .out_22(screen_memory_3_out_22), .out_23(screen_memory_3_out_23),
    .out_24(screen_memory_3_out_24), .out_25(screen_memory_3_out_25), .out_26(screen_memory_3_out_26),
    .out_27(screen_memory_3_out_27), .out_28(screen_memory_3_out_28), .out_29(screen_memory_3_out_29),
    .out_30(screen_memory_3_out_30), .out_31(screen_memory_3_out_31), .out_32(screen_memory_3_out_32),
    .out_33(screen_memory_3_out_33), .out_34(screen_memory_3_out_34), .out_35(screen_memory_3_out_35),
    .clock(clock_1_out), .x(column_draw));
  DotMatrix #(.matrixcols(32), .matrixrows(32)) dotmatrix_4 (
    .col0(screen_memory_4_out_4), .col1(screen_memory_4_out_5), .col2(screen_memory_4_out_6),
    .col3(screen_memory_4_out_7), .col4(screen_memory_4_out_8), .col5(screen_memory_4_out_9),
    .col6(screen_memory_4_out_10), .col7(screen_memory_4_out_11), .col8(screen_memory_4_out_12),
    .col9(screen_memory_4_out_13), .col10(screen_memory_4_out_14), .col11(screen_memory_4_out_15),
    .col12(screen_memory_4_out_16), .col13(screen_memory_4_out_17), .col14(screen_memory_4_out_18),
    .col15(screen_memory_4_out_19), .col16(screen_memory_4_out_20), .col17(screen_memory_4_out_21),
    .col18(screen_memory_4_out_22), .col19(screen_memory_4_out_23), .col20(screen_memory_4_out_24),
    .col21(screen_memory_4_out_25), .col22(screen_memory_4_out_26), .col23(screen_memory_4_out_27),
    .col24(screen_memory_4_out_28), .col25(screen_memory_4_out_29), .col26(screen_memory_4_out_30),
    .col27(screen_memory_4_out_31), .col28(screen_memory_4_out_32), .col29(screen_memory_4_out_33),
    .col30(screen_memory_4_out_34), .col31(screen_memory_4_out_35));
  Screen_Memory screen_memory_4 (
    .new_column(graphics_main_1_screen_2), .out_4(screen_memory_4_out_4), .out_5(screen_memory_4_out_5),
    .out_6(screen_memory_4_out_6), .out_7(screen_memory_4_out_7), .out_8(screen_memory_4_out_8),
    .out_9(screen_memory_4_out_9), .out_10(screen_memory_4_out_10), .out_11(screen_memory_4_out_11),
    .out_12(screen_memory_4_out_12), .out_13(screen_memory_4_out_13), .out_14(screen_memory_4_out_14),
    .out_15(screen_memory_4_out_15), .out_16(screen_memory_4_out_16), .out_17(screen_memory_4_out_17),
    .out_18(screen_memory_4_out_18), .out_19(screen_memory_4_out_19), .out_20(screen_memory_4_out_20),
    .out_21(screen_memory_4_out_21), .out_22(screen_memory_4_out_22), .out_23(screen_memory_4_out_23),
    .out_24(screen_memory_4_out_24), .out_25(screen_memory_4_out_25), .out_26(screen_memory_4_out_26),
    .out_27(screen_memory_4_out_27), .out_28(screen_memory_4_out_28), .out_29(screen_memory_4_out_29),
    .out_30(screen_memory_4_out_30), .out_31(screen_memory_4_out_31), .out_32(screen_memory_4_out_32),
    .out_33(screen_memory_4_out_33), .out_34(screen_memory_4_out_34), .out_35(screen_memory_4_out_35),
    .clock(clock_1_out), .x(column_draw));
  Button LEFT (.out(button1pressed));
  Button RIGHT (.out(button2pressed));

  // Notes on the sheet:
  //   y
  //   x
  //   MAX SCORE
  //   SCORE
endmodule

module Ball (
  input  [25:0] wall_on_screen_1,
  input  [25:0] wall_on_screen_2,
  input  [25:0] wall_on_screen_3,
  input  [25:0] wall_on_screen_4,
  input  CLK,
  input  RESET,
  output collision_happened,
  output [2:0] object_collide_num,
  output [1:0] active_screen,
  output [4:0] ball_x,
  output [4:0] ball_y,
  output out_of_screen
);

  wire and_2_out, and_3_out, buffer_1_out, collision_1_collision_happened, collision_2_collision_happened,
       collision_3_collision_happened, collision_4_collision_happened, collision_check_end,
       collision_happened_t, comparator_1_eq, comparator_2_eq, comparator_3_eq, comparator_4_eq,
       controlled_buffer_1_out, controlled_buffer_3_out, counter_2_carry, frame_reset, frame_update,
       move_1_out_of_screen, multiplexer_5_out, not_1_out, not_2_out, not_3_out, not_4_out, not_5_out,
       not_6_out, not_7_out, not_8_out, not_9_out, not_10_out, not_11_out, not_12_out, not_13_out,
       not_14_out, not_15_out, not_16_out, not_17_out, not_18_out, not_19_out, not_20_out, not_21_out,
       not_22_out, not_23_out, not_24_out, not_25_out, not_26_out, not_27_out, not_28_out, not_29_out,
       not_30_out, not_31_out, not_32_out, not_33_out, not_34_out, not_35_out, not_36_out, or_1_out,
       or_2_out, out_screen, pull_resistor_4_node, rs_latch_1_q, rs_latch_2_q, zero_wall;
  wire [1:0] ball_x_t, ball_y_t, wall_type;
  wire [4:0] counter_1_q;
  wire [5:0] random_2_out, random_4_out;
  wire [7:0] collision_1_x_correct, collision_1_y_correct, collision_2_x_correct, collision_2_y_correct,
       collision_3_x_correct, collision_3_y_correct, collision_4_x_correct, collision_4_y_correct,
       multiplexer_3_out, multiplexer_4_out, speed_y, wall_size, wall_x, wall_y;
  wire [7:7] random_1_out, random_3_out;
  wire [31:0] move_ball_data, multiplexer_2_out, new_ball_data;

  buf buffer_1 (buffer_1_out, buffer_1_out);
  Comparator #(.width(2), .mode("unsigned")) comparator_1 (
    .a(wall_type), .b(2'b00), .eq(comparator_1_eq));  // open: gt, lt
  Comparator #(.mode("unsigned")) comparator_2 (.a(wall_x), .b({8{1'b0}}), .eq(comparator_2_eq));  // open: gt, lt
  Comparator #(.mode("unsigned")) comparator_3 (.a(wall_y), .b({8{1'b0}}), .eq(comparator_3_eq));  // open: gt, lt
  Comparator #(.mode("unsigned")) comparator_4 (.a(wall_size), .b({8{1'b0}}), .eq(comparator_4_eq));  // open: gt, lt
  Random #(.width(1), .seed(3)) random_1 (.clk(out_of_screen), .out(random_1_out[7]));  // open: next, clr
  Random #(.width(6), .seed(3)) random_2 (.clk(out_of_screen), .out(random_2_out));  // open: next, clr
  Random #(.width(1)) random_3 (.clk(out_of_screen), .out(random_3_out[7]));  // open: next, clr
  Random #(.width(6)) random_4 (.clk(out_of_screen), .out(random_4_out));  // open: next, clr
  Counter #(.width(5), .max('h1f), .trigger("falling")) counter_1 (
    .Q(counter_1_q), .carry(frame_reset), .clk(CLK));  // open: load, D, count, clr
  and and_1 (zero_wall, comparator_1_eq, comparator_2_eq, comparator_3_eq, comparator_4_eq);
  Multiplexer #(.select(2), .width(26), .enable("false")) multiplexer_1 (
    .in0(wall_on_screen_1), .in1(wall_on_screen_2), .in2(wall_on_screen_3), .in3(wall_on_screen_4),
    .out({wall_type, wall_size, wall_y, wall_x}), .sel(active_screen));
  // Probe on {{2{random_1_out[7]}}, random_2_out[5:4]}
  // Probe on {5{1'b0}}
  Comparator #(.width(5), .mode("unsigned")) comparator_5 (
    .a(5'b11110), .b(counter_1_q), .eq(frame_update));  // open: gt, lt
  // Probe on wall_type
  // Probe on wall_x
  // Probe on wall_y
  // Probe on wall_size
  // Probe on {{2{random_3_out[7]}}, random_4_out[5:4]}
  // Probe on 5'b10011
  Multiplexer #(.select(2), .width(32), .enable("false")) multiplexer_2 (
    .in0(move_ball_data), .in1(new_ball_data),
    .in2({16'hcf80, {2{random_3_out[7]}}, random_4_out, {2{random_1_out[7]}}, random_2_out}),
    .out(multiplexer_2_out), .sel({out_of_screen, collision_happened}));  // open: in3
  and and_2 (and_2_out, ~collision_happened, CLK);  // AND_Gate
  // Probe on move_ball_data[7:4]
  Register #(.width(32)) ball_data (
    .D(multiplexer_2_out),
    .Q({active_screen[1], ball_y, ball_y_t, active_screen[0], ball_x, ball_x_t, speed_y, move_ball_data[7:0]}),
    .clk(frame_update));  // open: en, clr
  // Probe on ball_x
  Register #(.width(1)) register_1 (
    .D(collision_happened_t), .Q(collision_happened), .clk(and_2_out), .clr(or_1_out));  // open: en
  or or_1 (or_1_out, frame_reset, out_of_screen);
  // Probe on speed_y[7:4]
  // Probe on ball_y
  Collision_2_2_2 collision_1 (
    .wall_x(wall_x), .wall_y(wall_y), .ball_x({active_screen[0], ball_x, ball_x_t}),
    .ball_y({active_screen[1], ball_y, ball_y_t}), .V_x(move_ball_data[7:0]), .V_y(speed_y),
    .wall_size(wall_size), .collision_happened(collision_1_collision_happened),
    .x_correct(collision_1_x_correct), .y_correct(collision_1_y_correct));
  Collision_2_2 collision_2 (
    .wall_x(wall_x), .wall_y(wall_y), .ball_x({active_screen[0], ball_x, ball_x_t}),
    .ball_y({active_screen[1], ball_y, ball_y_t}), .V_x(move_ball_data[7:0]), .V_y(speed_y),
    .wall_size(wall_size), .collision_happened(collision_2_collision_happened),
    .x_correct(collision_2_x_correct), .y_correct(collision_2_y_correct));
  Collision_2 collision_3 (
    .wall_x(wall_x), .wall_y(wall_y), .ball_x({active_screen[0], ball_x, ball_x_t}),
    .ball_y({active_screen[1], ball_y, ball_y_t}), .V_x(move_ball_data[7:0]), .V_y(speed_y),
    .wall_size(wall_size), .collision_happened(collision_3_collision_happened),
    .x_correct(collision_3_x_correct), .y_correct(collision_3_y_correct));
  Collision collision_4 (
    .wall_x(wall_x), .wall_y(wall_y), .ball_x({active_screen[0], ball_x, ball_x_t}),
    .ball_y({active_screen[1], ball_y, ball_y_t}), .V_x(move_ball_data[7:0]), .V_y(speed_y),
    .wall_size(wall_size), .collision_happened(collision_4_collision_happened),
    .x_correct(collision_4_x_correct), .y_correct(collision_4_y_correct));
  not not_1 (not_1_out, CLK);
  not not_2 (not_2_out, not_1_out);
  not not_3 (not_3_out, not_14_out);
  not not_4 (not_4_out, not_3_out);
  not not_5 (not_5_out, not_6_out);
  not not_6 (not_6_out, not_2_out);
  not not_7 (not_7_out, not_8_out);
  not not_8 (not_8_out, not_5_out);
  not not_9 (not_9_out, not_4_out);
  not not_10 (not_10_out, not_9_out);
  not not_11 (not_11_out, not_12_out);
  not not_12 (not_12_out, not_10_out);
  not not_13 (not_13_out, not_7_out);
  not not_14 (not_14_out, not_13_out);
  not not_15 (not_15_out, not_16_out);
  assign controlled_buffer_1_out = not_17_out ? not_15_out : 1'bz;  // Controlled_Buffer controlled_buffer_1
  not not_16 (not_16_out, not_11_out);
  not not_17 (not_17_out, collision_happened);
  Multiplexer #(.select(2), .width(8), .enable("false")) multiplexer_3 (
    .in0(collision_1_x_correct), .in1(collision_2_x_correct), .in2(collision_3_x_correct),
    .in3(collision_4_x_correct), .out(multiplexer_3_out), .sel(wall_type));
  Multiplexer #(.select(2), .width(8), .enable("false")) multiplexer_4 (
    .in0(collision_1_y_correct), .in1(collision_2_y_correct), .in2(collision_3_y_correct),
    .in3(collision_4_y_correct), .out(multiplexer_4_out), .sel(wall_type));
  Multiplexer #(.select(2), .enable("false")) multiplexer_5 (
    .in0(collision_1_collision_happened), .in1(collision_2_collision_happened),
    .in2(collision_3_collision_happened), .in3(collision_4_collision_happened), .out(multiplexer_5_out),
    .sel(wall_type));
  assign collision_happened_t = not_18_out ? multiplexer_5_out : 1'bz;  // Controlled_Buffer controlled_buffer_2
  not not_18 (not_18_out, zero_wall);
  Counter #(.width(3), .max('h7), .trigger("falling")) counter_2 (
    .Q(object_collide_num), .carry(counter_2_carry), .clk(controlled_buffer_1_out), .clr(or_2_out));  // open: load, D, count
  Pull_Resistor pull_resistor_1 (.node(controlled_buffer_1_out));
  or or_2 (or_2_out, frame_reset, out_of_screen);
  RS_latch rs_latch_1 (.S(RESET), .R(frame_reset), .Q(rs_latch_1_q));  // open: Q_prime, reset
  RS_latch rs_latch_2 (.S(out_screen), .R(frame_reset), .Q(rs_latch_2_q));  // open: Q_prime, reset
  Pull_Resistor pull_resistor_2 (.node(collision_happened_t));
  and and_3 (and_3_out, ~collision_check_end, CLK);  // AND_Gate
  or or_3 (out_of_screen, rs_latch_1_q, rs_latch_2_q);
  Register #(.width(1), .trigger("falling")) register_2 (
    .D(counter_2_carry), .Q(collision_check_end), .clk(and_3_out), .clr(frame_reset));  // open: en
  Move move_1 (
    .start_ball_x({active_screen[0], ball_x, ball_x_t}), .start_ball_y({active_screen[1], ball_y, ball_y_t}),
    .start_vy(speed_y), .start_vx(move_ball_data[7:0]), .result_x(move_ball_data[23:16]),
    .result_y(move_ball_data[31:24]), .Out_of_screen(move_1_out_of_screen), .result_Vy(move_ball_data[15:8]));
  not not_19 (not_19_out, move_1_out_of_screen);
  not not_20 (not_20_out, not_19_out);
  not not_21 (not_21_out, not_31_out);
  not not_22 (not_22_out, not_21_out);
  not not_23 (not_23_out, not_20_out);
  not not_24 (not_24_out, not_26_out);
  not not_25 (not_25_out, not_24_out);
  not not_26 (not_26_out, not_23_out);
  not not_27 (not_27_out, not_22_out);
  not not_28 (not_28_out, not_29_out);
  not not_29 (not_29_out, not_30_out);
  not not_30 (not_30_out, not_27_out);
  update_ball_param update_ball_param_1 (
    .x_correct(multiplexer_3_out), .y_correct(multiplexer_4_out), .V_x(move_ball_data[7:0]), .V_y(speed_y),
    .wall_type(wall_type), .new_V_x(new_ball_data[7:0]), .new_V_y(new_ball_data[15:8]),
    .new_x_ball(new_ball_data[23:16]), .new_y_ball(new_ball_data[31:24]));
  not not_31 (not_31_out, not_32_out);
  not not_32 (not_32_out, not_25_out);
  not not_33 (not_33_out, not_28_out);
  not not_34 (not_34_out, not_33_out);
  assign controlled_buffer_3_out = collision_check_end ? not_34_out : 1'bz;  // Controlled_Buffer controlled_buffer_3
  Pull_Resistor pull_resistor_3 (.node(controlled_buffer_3_out));
  Pull_Resistor pull_resistor_4 (.node(pull_resistor_4_node));
  assign pull_resistor_4_node = not_35_out ? controlled_buffer_3_out : 1'bz;  // Controlled_Buffer controlled_buffer_4
  not not_35 (not_35_out, frame_update);
  // Probe on active_screen
  Pull_Resistor pull_resistor_5 (.node(out_screen));
  assign out_screen = not_36_out ? pull_resistor_4_node : 1'bz;  // Controlled_Buffer controlled_buffer_5
  not not_36 (not_36_out, collision_happened);

  // Other names for the same wires on the sheet: current_state = collision_happened; RESET_t = out_of_screen;
  //   ball_x_t[7:2] = {active_screen[0], ball_x}; ball_y_t[7:2] = {active_screen[1], ball_y};
  //   speed_x[7:0] = move_ball_data[7:0]

  // Notes on the sheet:
  //   buffer_1 drives only 1 and floats otherwise
  //   ball x, y
  //   Frame Counter
  //   speed x, y
  //   Ball Register
  //   Current State Holder
  //   x_corr
  //   y_corr
  //   Wall Sequencer
  //   Combinational Logic
endmodule

module Move (
  input  [7:0] start_ball_x,
  input  [7:0] start_ball_y,
  input  [7:0] start_vx,
  input  [7:0] start_vy,
  output [7:0] result_x,
  output [7:0] result_Vy,
  output [7:0] result_y,
  output Out_of_screen
);

  wire and_1_out, and_2_out, and_3_out, and_4_out, comparator_1_eq, comparator_1_gt, comparator_2_eq,
       comparator_2_gt, comparator_3_eq, comparator_3_gt, comparator_4_eq, comparator_4_gt, or_1_out,
       or_2_out, or_3_out, or_4_out, or_5_out, or_6_out, or_8_out, or_9_out, out_x, out_y;
  wire [3:0] adder_1_out, adder_7_out, not_1_out, not_4_out;
  wire [6:0] adder_2_out, adder_3_out, adder_8_out, adder_9_out, not_2_out, not_3_out, not_5_out, not_6_out;
  wire [7:0] adder_4_out, multiplexer_4_out, multiplexer_5_out, multiplexer_6_out, multiplexer_7_out,
       subtractor_1_out;
  wire [10:0] adder_5_out, adder_6_out, subtractor_2_out, subtractor_3_out, subtractor_4_out,
       subtractor_5_out, subtractor_6_out, subtractor_7_out, vel_x, vel_y, x_res, y_res;

  // Probe on start_ball_x[6:2]
  // Probe on start_ball_y[6:2]
  // Probe on start_vx[7:4]
  // Probe on start_vy[7:4]
  assign vel_x = {{3{start_vx[7]}}, start_vx};  // Bit_Extender bit_extender_1
  assign vel_y = {{3{start_vy[7]}}, start_vy};  // Bit_Extender bit_extender_2
  // Probe on {2'b00, start_ball_x[6:0], 2'b00}
  // Probe on {2'b00, start_ball_y[6:0], 2'b00}
  // Probe on vel_x
  // Probe on vel_y
  assign not_1_out = ~start_vy[7:4];  // NOT_Gate not_1, 4 bits wide
  Adder #(.width(4)) adder_1 (.a(not_1_out), .b(4'b0001), .out(adder_1_out));  // open: cin, cout
  assign not_2_out = ~vel_x[10:4];  // NOT_Gate not_2, 7 bits wide
  Adder #(.width(7)) adder_2 (.a(not_2_out), .b(7'b0000001), .out(adder_2_out));  // open: cin, cout
  assign not_3_out = ~vel_y[10:4];  // NOT_Gate not_3, 7 bits wide
  Adder #(.width(7)) adder_3 (.a(not_3_out), .b(7'b0000001), .out(adder_3_out));  // open: cin, cout
  Adder adder_4 (.a(8'h4), .b({adder_1_out, start_vy[3:0]}), .out(adder_4_out));  // open: cin, cout
  // Probe on subtractor_1_out[7:4]
  Subtractor subtractor_1 (.a(start_vy), .b(8'h4), .out(subtractor_1_out));  // open: bin, bout
  assign not_4_out = ~adder_4_out[7:4];  // NOT_Gate not_4, 4 bits wide
  Adder #(.width(11)) adder_5 (.a({2'b00, start_ball_x[6:0], 2'b00}), .b(vel_x), .out(adder_5_out));  // open: cin, cout
  Adder #(.width(11)) adder_6 (.a({2'b00, start_ball_y[6:0], 2'b00}), .b(vel_y), .out(adder_6_out));  // open: cin, cout
  Adder #(.width(4)) adder_7 (.a(not_4_out), .b(4'b0001), .out(adder_7_out));  // open: cin, cout
  Subtractor #(.width(11)) subtractor_2 (
    .a({2'b00, start_ball_x[6:0], 2'b00}), .b({adder_2_out, vel_x[3:0]}), .out(subtractor_2_out));  // open: bin, bout
  Subtractor #(.width(11)) subtractor_3 (
    .a({2'b00, start_ball_y[6:0], 2'b00}), .b({adder_3_out, vel_y[3:0]}), .out(subtractor_3_out));  // open: bin, bout
  // Probe on result_Vy[7:4]
  Multiplexer #(.width(8)) multiplexer_1 (
    .in0(subtractor_1_out), .in1({adder_7_out, adder_4_out[3:0]}), .out(result_Vy), .sel(start_vy[7]));  // open: en
  // Probe on x_res[10:4]
  Multiplexer #(.width(11)) multiplexer_2 (
    .in0(adder_5_out), .in1(subtractor_2_out), .out(x_res), .sel(vel_x[10]));  // open: en
  // Probe on y_res[10:4]
  Multiplexer #(.width(11)) multiplexer_3 (
    .in0(adder_6_out), .in1(subtractor_3_out), .out(y_res), .sel(vel_y[10]));  // open: en
  assign not_5_out = ~x_res[10:4];  // NOT_Gate not_5, 7 bits wide
  assign not_6_out = ~y_res[10:4];  // NOT_Gate not_6, 7 bits wide
  Adder #(.width(7)) adder_8 (.a(not_5_out), .b(7'b0000001), .out(adder_8_out));  // open: cin, cout
  Adder #(.width(7)) adder_9 (.a(not_6_out), .b(7'b0000001), .out(adder_9_out));  // open: cin, cout
  // Probe on subtractor_4_out[10:4]
  Subtractor #(.width(11)) subtractor_4 (.a(x_res), .b(11'h200), .out(subtractor_4_out));  // open: bin, bout
  // Probe on subtractor_5_out[10:4]
  Subtractor #(.width(11)) subtractor_5 (
    .a(11'h200), .b({adder_8_out, x_res[3:0]}), .out(subtractor_5_out));  // open: bin, bout
  Subtractor #(.width(11)) subtractor_6 (.a(y_res), .b(11'h200), .out(subtractor_6_out));  // open: bin, bout
  Subtractor #(.width(11)) subtractor_7 (
    .a(11'h200), .b({adder_9_out, y_res[3:0]}), .out(subtractor_7_out));  // open: bin, bout
  // Probe on subtractor_6_out[10:4]
  // Probe on subtractor_7_out[10:4]
  Multiplexer #(.width(8)) multiplexer_4 (
    .in0({1'b1, subtractor_4_out[8:2]}), .in1({1'b0, subtractor_5_out[8:2]}), .out(multiplexer_4_out),
    .sel(start_ball_x[7]));  // open: en
  Multiplexer #(.width(8)) multiplexer_5 (
    .in0({1'b1, subtractor_6_out[8:2]}), .in1({1'b0, subtractor_7_out[8:2]}), .out(multiplexer_5_out),
    .sel(start_ball_y[7]));  // open: en
  or or_1 (or_1_out, comparator_1_gt, comparator_1_eq);
  Comparator #(.width(11)) comparator_1 (
    .a(x_res), .b(11'h200), .gt(comparator_1_gt), .eq(comparator_1_eq));  // open: lt
  or or_2 (or_2_out, comparator_2_gt, comparator_2_eq);
  Comparator #(.width(11)) comparator_2 (
    .a(x_res), .b(11'h200), .gt(comparator_2_gt), .eq(comparator_2_eq));  // open: lt
  Comparator #(.width(11)) comparator_3 (
    .a(y_res), .b(11'h200), .gt(comparator_3_gt), .eq(comparator_3_eq));  // open: lt
  Comparator #(.width(11)) comparator_4 (
    .a(y_res), .b(11'h200), .gt(comparator_4_gt), .eq(comparator_4_eq));  // open: lt
  Multiplexer #(.width(8)) multiplexer_6 (
    .in0({start_ball_x[7], x_res[8:2]}), .in1(multiplexer_4_out), .out(multiplexer_6_out), .sel(or_3_out));  // open: en
  or or_3 (or_3_out, x_res[10], or_1_out);
  Multiplexer #(.width(8)) multiplexer_7 (
    .in0({start_ball_y[7], y_res[8:2]}), .in1(multiplexer_5_out), .out(multiplexer_7_out), .sel(or_4_out));  // open: en
  or or_4 (or_4_out, y_res[10], or_5_out);
  or or_5 (or_5_out, comparator_3_gt, comparator_3_eq);
  or or_6 (or_6_out, comparator_4_gt, comparator_4_eq);
  or or_7 (Out_of_screen, out_x, out_y);
  // Probe on result_x[6:2]
  Multiplexer #(.width(8)) multiplexer_8 (
    .in0(multiplexer_6_out), .in1(start_ball_x), .out(result_x), .sel(or_8_out));  // open: en
  or or_8 (or_8_out, out_x, out_y);
  and and_1 (and_1_out, or_2_out, start_ball_x[7], ~vel_x[10]);  // AND_Gate
  and and_2 (and_2_out, x_res[10], ~start_ball_x[7], vel_x[10]);  // AND_Gate
  // Probe on result_y[6:2]
  Multiplexer #(.width(8)) multiplexer_9 (
    .in0(multiplexer_7_out), .in1(start_ball_y), .out(result_y), .sel(or_9_out));  // open: en
  or or_9 (or_9_out, out_x, out_y);
  and and_3 (and_3_out, or_6_out, start_ball_y[7], ~vel_y[10]);  // AND_Gate
  and and_4 (and_4_out, y_res[10], ~start_ball_y[7], vel_y[10]);  // AND_Gate
  or or_10 (out_x, and_1_out, and_2_out);
  or or_11 (out_y, and_3_out, and_4_out);

  // Other names for the same wires on the sheet: V_y[7:0] = start_vy; ball_x[7:0] = start_ball_x;
  //   ball_y[7:0] = start_ball_y; V_x[7:0] = start_vx; x_b[8:2] = start_ball_x[6:0]; y_b[8:2] = start_ball_y[6:0]

  // Notes on the sheet:
  //   Format: SXXXXXXFFFF
  //   32 - (inv(x_res)FFFF)
  //   x_res - 32
  //   y_res - 32
  //   32 - (inv(y_res)FFFF)
endmodule

module Graphics_Ultra (
  input  [31:0] base,
  input  input_ball,
  input  [4:0] ball_x,
  input  [4:0] ball_y,
  input  is_active,
  input  [4:0] x,
  input  [4:0] size,
  input  [4:0] current_x,
  output [31:0] out_9
);

  wire adder_1_cout, and_1_out, and_2_out, and_3_out, comparator_1_eq, comparator_2_gt, comparator_3_eq,
       comparator_3_lt, or_1_out, or_2_out;
  wire [4:0] adder_1_out;
  wire [31:0] demultiplexer_1_out0, multiplexer_1_out;

  Pull_Resistor pull_resistor_1 (.node(x));
  Pull_Resistor pull_resistor_2 (.node(size));
  Comparator #(.width(5), .mode("unsigned")) comparator_1 (
    .a(ball_x), .b(current_x), .eq(comparator_1_eq));  // open: gt, lt
  and and_1 (and_1_out, input_ball, comparator_1_eq);
  Adder #(.width(5)) adder_1 (.a(x), .b(size), .out(adder_1_out), .cout(adder_1_cout));  // open: cin
  Comparator #(.width(5), .mode("unsigned")) comparator_2 (
    .a(adder_1_out), .b(current_x), .gt(comparator_2_gt));  // open: eq, lt
  Comparator #(.width(5), .mode("unsigned")) comparator_3 (
    .a(x), .b(current_x), .eq(comparator_3_eq), .lt(comparator_3_lt));  // open: gt
  Demultiplexer #(.select(5), .enable("false")) demultiplexer_1 (
    .out0(demultiplexer_1_out0[0]), .out1(demultiplexer_1_out0[1]), .out2(demultiplexer_1_out0[2]),
    .out3(demultiplexer_1_out0[3]), .out4(demultiplexer_1_out0[4]), .out5(demultiplexer_1_out0[5]),
    .out6(demultiplexer_1_out0[6]), .out7(demultiplexer_1_out0[7]), .out8(demultiplexer_1_out0[8]),
    .out9(demultiplexer_1_out0[9]), .out10(demultiplexer_1_out0[10]), .out11(demultiplexer_1_out0[11]),
    .out12(demultiplexer_1_out0[12]), .out13(demultiplexer_1_out0[13]), .out14(demultiplexer_1_out0[14]),
    .out15(demultiplexer_1_out0[15]), .out16(demultiplexer_1_out0[16]), .out17(demultiplexer_1_out0[17]),
    .out18(demultiplexer_1_out0[18]), .out19(demultiplexer_1_out0[19]), .out20(demultiplexer_1_out0[20]),
    .out21(demultiplexer_1_out0[21]), .out22(demultiplexer_1_out0[22]), .out23(demultiplexer_1_out0[23]),
    .out24(demultiplexer_1_out0[24]), .out25(demultiplexer_1_out0[25]), .out26(demultiplexer_1_out0[26]),
    .out27(demultiplexer_1_out0[27]), .out28(demultiplexer_1_out0[28]), .out29(demultiplexer_1_out0[29]),
    .out30(demultiplexer_1_out0[30]), .out31(demultiplexer_1_out0[31]), .in(and_1_out), .sel(ball_y));
  Pull_Resistor pull_resistor_3 (.node(is_active));
  or or_1 (or_1_out, comparator_2_gt, adder_1_cout);
  and and_2 (and_2_out, or_1_out, or_2_out);
  or or_2 (or_2_out, comparator_3_eq, comparator_3_lt);
  Pull_Resistor pull_resistor_4 (.node(base));
  Multiplexer #(.width(32)) multiplexer_1 (
    .in0({32{1'b0}}), .in1(32'h2), .out(multiplexer_1_out), .sel(and_3_out));  // open: en
  and and_3 (and_3_out, is_active, and_2_out);
  assign out_9 = base | demultiplexer_1_out0 | multiplexer_1_out;  // OR_Gate or_3, 32 bits wide

  // Other names for the same wires on the sheet: current_row[4:0] = current_x
endmodule

module Intersect (
  input  [7:0] V_x,
  input  [7:0] wall_x,
  input  [7:0] wall_y,
  input  [7:0] ball_x,
  input  [7:0] V_y,
  input  [7:0] ball_y,
  output [9:0] Intersection_X,
  output [9:0] Intersection_Y,
  output NO_Intersection
);

  wire and_1_out, comparator_2_eq, comparator_3_eq, xor_1_out, xor_2_out, Zero_Division;
  wire [3:0] adder_10_out, adder_11_out, not_5_out, not_6_out;
  wire [5:0] adder_12_out, adder_13_out, multiplexer_5_out, multiplexer_6_out, not_7_out, not_8_out;
  wire [15:0] adder_1_out, adder_2_out, adder_3_out, adder_4_out, adder_5_out, adder_6_out, adder_7_out,
       adder_8_out, adder_9_out, adder_14_out, adder_15_out, ball_x_t, ball_y_t, divider_1_out,
       divider_2_out, multiplexer_1_out, multiplexer_2_out, multiplexer_3_out, multiplexer_4_out,
       multiplier_1_out, multiplier_2_out, multiplier_3_out, multiplier_4_out, multiplier_5_out,
       multiplier_6_out, not_1_out, not_2_out, not_3_out, not_4_out, not_9_out, not_10_out, subtractor_1_out,
       subtractor_2_out, subtractor_3_out, V_x_t, V_y_t, wall_x_t, wall_y_t;
  wire [15:8] multiplexer_7_out, multiplexer_8_out;

  // Probe on wall_x
  // Probe on wall_y
  // Probe on ball_x[6:2]
  // Probe on ball_y[6:2]
  Adder #(.width(16)) adder_1 (.a(wall_x_t), .b(wall_y_t), .out(adder_1_out));  // open: cin, cout
  Multiplier #(.width(16)) multiplier_1 (.a(ball_x_t), .b(V_y_t), .out(multiplier_1_out));  // open: cin, cout
  Multiplier #(.width(16)) multiplier_2 (.a(ball_y_t), .b(V_x_t), .out(multiplier_2_out));  // open: cin, cout
  Adder #(.width(16)) adder_2 (.a(wall_x_t), .b(wall_y_t), .out(adder_2_out));  // open: cin, cout
  Multiplier #(.width(16)) multiplier_3 (.a(ball_x_t), .b(V_y_t), .out(multiplier_3_out));  // open: cin, cout
  Multiplier #(.width(16)) multiplier_4 (.a(ball_y_t), .b(V_x_t), .out(multiplier_4_out));  // open: cin, cout
  // Probe on wall_x_t
  assign wall_x_t = {{8{1'b0}}, wall_x};  // Bit_Extender bit_extender_1
  // Probe on wall_y_t
  assign wall_y_t = {{8{1'b0}}, wall_y};  // Bit_Extender bit_extender_2
  // Probe on ball_x_t
  assign ball_x_t = {{11{1'b0}}, ball_x[6:2]};  // Bit_Extender bit_extender_3
  // Probe on ball_y_t
  assign ball_y_t = {{11{1'b0}}, ball_y[6:2]};  // Bit_Extender bit_extender_4
  // Probe on multiplier_5_out
  Multiplier #(.width(16)) multiplier_5 (.a(V_x_t), .b(adder_1_out), .out(multiplier_5_out));  // open: cin, cout
  // Probe on subtractor_1_out
  Subtractor #(.width(16)) subtractor_1 (
    .a(multiplier_1_out), .b(multiplier_2_out), .out(subtractor_1_out));  // open: bin, bout
  // Probe on multiplier_6_out
  Multiplier #(.width(16)) multiplier_6 (.a(V_y_t), .b(adder_2_out), .out(multiplier_6_out));  // open: cin, cout
  // Probe on subtractor_2_out
  Subtractor #(.width(16)) subtractor_2 (
    .a(multiplier_3_out), .b(multiplier_4_out), .out(subtractor_2_out));  // open: bin, bout
  // Probe on adder_3_out
  Adder #(.width(16)) adder_3 (.a(multiplier_5_out), .b(subtractor_1_out), .out(adder_3_out));  // open: cin, cout
  // Probe on adder_4_out
  Adder #(.width(16)) adder_4 (.a(V_x_t), .b(V_y_t), .out(adder_4_out));  // open: cin, cout
  // Probe on subtractor_3_out
  Subtractor #(.width(16)) subtractor_3 (
    .a(multiplier_6_out), .b(subtractor_2_out), .out(subtractor_3_out));  // open: bin, bout
  // Probe on adder_5_out
  Adder #(.width(16)) adder_5 (.a(V_x_t), .b(V_y_t), .out(adder_5_out));  // open: cin, cout
  Comparator #(.width(16)) comparator_1 (.a(adder_5_out), .b({16{1'b0}}), .eq(Zero_Division));  // open: gt, lt
  assign not_1_out = ~adder_3_out;  // NOT_Gate not_1, 16 bits wide
  assign not_2_out = ~adder_4_out;  // NOT_Gate not_2, 16 bits wide
  assign not_3_out = ~subtractor_3_out;  // NOT_Gate not_3, 16 bits wide
  assign not_4_out = ~adder_5_out;  // NOT_Gate not_4, 16 bits wide
  Multiplexer #(.width(16)) multiplexer_1 (
    .in0(adder_3_out), .in1(adder_6_out), .out(multiplexer_1_out), .sel(adder_3_out[15]));  // open: en
  Adder #(.width(16)) adder_6 (.a(16'h1), .b(not_1_out), .out(adder_6_out));  // open: cin, cout
  Multiplexer #(.width(16)) multiplexer_2 (
    .in0(adder_4_out), .in1(adder_7_out), .out(multiplexer_2_out), .sel(adder_4_out[15]));  // open: en
  Adder #(.width(16)) adder_7 (.a(16'h1), .b(not_2_out), .out(adder_7_out));  // open: cin, cout
  Multiplexer #(.width(16)) multiplexer_3 (
    .in0(subtractor_3_out), .in1(adder_8_out), .out(multiplexer_3_out), .sel(subtractor_3_out[15]));  // open: en
  Adder #(.width(16)) adder_8 (.a(16'h1), .b(not_3_out), .out(adder_8_out));  // open: cin, cout
  Multiplexer #(.width(16)) multiplexer_4 (
    .in0(adder_5_out), .in1(adder_9_out), .out(multiplexer_4_out), .sel(adder_5_out[15]));  // open: en
  Adder #(.width(16)) adder_9 (.a(16'h1), .b(not_4_out), .out(adder_9_out));  // open: cin, cout
  // Probe on V_x[7:4]
  // Probe on V_x[7:2]
  Adder #(.width(4)) adder_10 (.a(4'b0001), .b(not_5_out), .out(adder_10_out));  // open: cin, cout
  assign not_5_out = ~V_x[7:4];  // NOT_Gate not_5, 4 bits wide
  // Probe on V_y[7:4]
  // Probe on V_y[7:2]
  Adder #(.width(4)) adder_11 (.a(4'b0001), .b(not_6_out), .out(adder_11_out));  // open: cin, cout
  assign not_6_out = ~V_y[7:4];  // NOT_Gate not_6, 4 bits wide
  xor xor_1 (xor_1_out, adder_4_out[15], adder_3_out[15]);
  // Probe on divider_1_out
  Divider #(.width(16)) divider_1 (
    .a(multiplexer_1_out), .b(multiplexer_2_out), .out(divider_1_out));  // open: upper, rem
  xor xor_2 (xor_2_out, adder_5_out[15], subtractor_3_out[15]);
  // Probe on divider_2_out
  Divider #(.width(16)) divider_2 (
    .a(multiplexer_3_out), .b(multiplexer_4_out), .out(divider_2_out));  // open: upper, rem
  // Probe on {adder_10_out, V_x[3:2]}
  assign not_7_out = ~{adder_10_out, V_x[3:2]};  // NOT_Gate not_7, 6 bits wide
  // Probe on {adder_11_out, V_y[3:2]}
  assign not_8_out = ~{adder_11_out, V_y[3:2]};  // NOT_Gate not_8, 6 bits wide
  assign not_9_out = ~divider_1_out;  // NOT_Gate not_9, 16 bits wide
  assign not_10_out = ~divider_2_out;  // NOT_Gate not_10, 16 bits wide
  Adder #(.width(6)) adder_12 (.a(6'b000001), .b(not_7_out), .out(adder_12_out));  // open: cin, cout
  Adder #(.width(6)) adder_13 (.a(6'b000001), .b(not_8_out), .out(adder_13_out));  // open: cin, cout
  Adder #(.width(16)) adder_14 (.a(16'h1), .b(not_9_out), .out(adder_14_out));  // open: cin, cout
  Adder #(.width(16)) adder_15 (.a(16'h1), .b(not_10_out), .out(adder_15_out));  // open: cin, cout
  Comparator #(.width(16)) comparator_2 (.a(V_x_t), .b({16{1'b0}}), .eq(comparator_2_eq));  // open: gt, lt
  Comparator #(.width(16)) comparator_3 (.a(V_x_t), .b(V_y_t), .eq(comparator_3_eq));  // open: gt, lt
  Multiplexer #(.width(6)) multiplexer_5 (
    .in0(V_x[7:2]), .in1(adder_12_out), .out(multiplexer_5_out), .sel(V_x[7]));  // open: en
  // Probe on adder_12_out
  Multiplexer #(.width(6)) multiplexer_6 (
    .in0(V_y[7:2]), .in1(adder_13_out), .out(multiplexer_6_out), .sel(V_y[7]));  // open: en
  // Probe on adder_13_out
  // Probe on {multiplexer_7_out, Intersection_X[9:2]}
  Multiplexer #(.width(16)) multiplexer_7 (
    .in0(divider_1_out), .in1(adder_14_out), .out({multiplexer_7_out, Intersection_X[9:2]}), .sel(xor_1_out));  // open: en
  // Probe on {multiplexer_8_out, Intersection_Y[9:2]}
  Multiplexer #(.width(16)) multiplexer_8 (
    .in0(divider_2_out), .in1(adder_15_out), .out({multiplexer_8_out, Intersection_Y[9:2]}), .sel(xor_2_out));  // open: en
  and and_1 (and_1_out, comparator_2_eq, comparator_3_eq);
  // Probe on multiplexer_5_out
  assign V_x_t = {{10{multiplexer_5_out[5]}}, multiplexer_5_out};  // Bit_Extender bit_extender_5
  // Probe on multiplexer_6_out
  assign V_y_t = {{10{multiplexer_6_out[5]}}, multiplexer_6_out};  // Bit_Extender bit_extender_6
  // Probe on {multiplexer_7_out, Intersection_X[9:2]}
  // Probe on {multiplexer_8_out, Intersection_Y[9:2]}
  or or_1 (NO_Intersection, Zero_Division, and_1_out);
  // Probe on V_x_t
  // Probe on V_y_t
  // Probe on Intersection_X[9:2]
  // Probe on Intersection_Y[9:2]

  assign Intersection_X[1:0] = 2'b00;
  assign Intersection_Y[1:0] = 2'b00;
endmodule

module Intersect_2 (
  input  [7:0] V_x,
  input  [7:0] wall_x,
  input  [7:0] wall_y,
  input  [7:0] ball_x,
  input  [7:0] V_y,
  input  [7:0] ball_y,
  output [9:0] Intersection_X,
  output NO_Intersection,
  output [9:0] Intersection_Y
);

  wire and_1_out, comparator_2_eq, comparator_3_eq, xor_1_out, xor_2_out, Zero_Division;
  wire [3:0] adder_7_out, adder_8_out, not_5_out, not_6_out;
  wire [5:0] adder_9_out, adder_10_out, multiplexer_5_out, multiplexer_6_out, not_7_out, not_8_out;
  wire [15:0] adder_1_out, adder_2_out, adder_3_out, adder_4_out, adder_5_out, adder_6_out, adder_11_out,
       adder_12_out, ball_x_t, ball_y_t, divider_1_out, divider_2_out, multiplexer_1_out, multiplexer_2_out,
       multiplexer_3_out, multiplexer_4_out, multiplier_1_out, multiplier_2_out, multiplier_3_out,
       multiplier_4_out, multiplier_5_out, multiplier_6_out, not_1_out, not_2_out, not_3_out, not_4_out,
       not_9_out, not_10_out, subtractor_1_out, subtractor_2_out, subtractor_3_out, subtractor_4_out,
       subtractor_5_out, subtractor_6_out, V_x_t, V_y_t, wall_x_t, wall_y_t;
  wire [15:8] multiplexer_7_out, multiplexer_8_out;

  // Probe on wall_x
  // Probe on wall_y
  // Probe on ball_x[6:2]
  // Probe on ball_y[6:2]
  Subtractor #(.width(16)) subtractor_1 (.a(wall_y_t), .b(wall_x_t), .out(subtractor_1_out));  // open: bin, bout
  Multiplier #(.width(16)) multiplier_1 (.a(ball_x_t), .b(V_y_t), .out(multiplier_1_out));  // open: cin, cout
  Multiplier #(.width(16)) multiplier_2 (.a(ball_y_t), .b(V_x_t), .out(multiplier_2_out));  // open: cin, cout
  Subtractor #(.width(16)) subtractor_2 (.a(wall_y_t), .b(wall_x_t), .out(subtractor_2_out));  // open: bin, bout
  Multiplier #(.width(16)) multiplier_3 (.a(ball_x_t), .b(V_y_t), .out(multiplier_3_out));  // open: cin, cout
  Multiplier #(.width(16)) multiplier_4 (.a(ball_y_t), .b(V_x_t), .out(multiplier_4_out));  // open: cin, cout
  // Probe on wall_x_t
  assign wall_x_t = {{8{1'b0}}, wall_x};  // Bit_Extender bit_extender_1
  // Probe on wall_y_t
  assign wall_y_t = {{8{1'b0}}, wall_y};  // Bit_Extender bit_extender_2
  // Probe on ball_x_t
  assign ball_x_t = {{11{1'b0}}, ball_x[6:2]};  // Bit_Extender bit_extender_3
  // Probe on ball_y_t
  assign ball_y_t = {{11{1'b0}}, ball_y[6:2]};  // Bit_Extender bit_extender_4
  // Probe on multiplier_5_out
  Multiplier #(.width(16)) multiplier_5 (.a(V_x_t), .b(subtractor_1_out), .out(multiplier_5_out));  // open: cin, cout
  // Probe on subtractor_3_out
  Subtractor #(.width(16)) subtractor_3 (
    .a(multiplier_1_out), .b(multiplier_2_out), .out(subtractor_3_out));  // open: bin, bout
  // Probe on multiplier_6_out
  Multiplier #(.width(16)) multiplier_6 (.a(V_y_t), .b(subtractor_2_out), .out(multiplier_6_out));  // open: cin, cout
  // Probe on subtractor_4_out
  Subtractor #(.width(16)) subtractor_4 (
    .a(multiplier_3_out), .b(multiplier_4_out), .out(subtractor_4_out));  // open: bin, bout
  // Probe on adder_1_out
  Adder #(.width(16)) adder_1 (.a(multiplier_5_out), .b(subtractor_3_out), .out(adder_1_out));  // open: cin, cout
  // Probe on subtractor_5_out
  Subtractor #(.width(16)) subtractor_5 (.a(V_y_t), .b(V_x_t), .out(subtractor_5_out));  // open: bin, bout
  // Probe on adder_2_out
  Adder #(.width(16)) adder_2 (.a(multiplier_6_out), .b(subtractor_4_out), .out(adder_2_out));  // open: cin, cout
  // Probe on subtractor_6_out
  Subtractor #(.width(16)) subtractor_6 (.a(V_y_t), .b(V_x_t), .out(subtractor_6_out));  // open: bin, bout
  Comparator #(.width(16)) comparator_1 (.a(subtractor_6_out), .b({16{1'b0}}), .eq(Zero_Division));  // open: gt, lt
  assign not_1_out = ~adder_1_out;  // NOT_Gate not_1, 16 bits wide
  assign not_2_out = ~subtractor_5_out;  // NOT_Gate not_2, 16 bits wide
  assign not_3_out = ~adder_2_out;  // NOT_Gate not_3, 16 bits wide
  assign not_4_out = ~subtractor_6_out;  // NOT_Gate not_4, 16 bits wide
  Multiplexer #(.width(16)) multiplexer_1 (
    .in0(adder_1_out), .in1(adder_3_out), .out(multiplexer_1_out), .sel(adder_1_out[15]));  // open: en
  Adder #(.width(16)) adder_3 (.a(16'h1), .b(not_1_out), .out(adder_3_out));  // open: cin, cout
  Multiplexer #(.width(16)) multiplexer_2 (
    .in0(subtractor_5_out), .in1(adder_4_out), .out(multiplexer_2_out), .sel(subtractor_5_out[15]));  // open: en
  Adder #(.width(16)) adder_4 (.a(16'h1), .b(not_2_out), .out(adder_4_out));  // open: cin, cout
  Multiplexer #(.width(16)) multiplexer_3 (
    .in0(adder_2_out), .in1(adder_5_out), .out(multiplexer_3_out), .sel(adder_2_out[15]));  // open: en
  Adder #(.width(16)) adder_5 (.a(16'h1), .b(not_3_out), .out(adder_5_out));  // open: cin, cout
  Multiplexer #(.width(16)) multiplexer_4 (
    .in0(subtractor_6_out), .in1(adder_6_out), .out(multiplexer_4_out), .sel(subtractor_6_out[15]));  // open: en
  Adder #(.width(16)) adder_6 (.a(16'h1), .b(not_4_out), .out(adder_6_out));  // open: cin, cout
  // Probe on V_x[7:4]
  // Probe on V_x[7:2]
  Adder #(.width(4)) adder_7 (.a(4'b0001), .b(not_5_out), .out(adder_7_out));  // open: cin, cout
  assign not_5_out = ~V_x[7:4];  // NOT_Gate not_5, 4 bits wide
  // Probe on V_y[7:4]
  // Probe on V_y[7:2]
  Adder #(.width(4)) adder_8 (.a(4'b0001), .b(not_6_out), .out(adder_8_out));  // open: cin, cout
  assign not_6_out = ~V_y[7:4];  // NOT_Gate not_6, 4 bits wide
  xor xor_1 (xor_1_out, subtractor_5_out[15], adder_1_out[15]);
  // Probe on divider_1_out
  Divider #(.width(16)) divider_1 (
    .a(multiplexer_1_out), .b(multiplexer_2_out), .out(divider_1_out));  // open: upper, rem
  xor xor_2 (xor_2_out, subtractor_6_out[15], adder_2_out[15]);
  // Probe on divider_2_out
  Divider #(.width(16)) divider_2 (
    .a(multiplexer_3_out), .b(multiplexer_4_out), .out(divider_2_out));  // open: upper, rem
  // Probe on {adder_7_out, V_x[3:2]}
  assign not_7_out = ~{adder_7_out, V_x[3:2]};  // NOT_Gate not_7, 6 bits wide
  // Probe on {adder_8_out, V_y[3:2]}
  assign not_8_out = ~{adder_8_out, V_y[3:2]};  // NOT_Gate not_8, 6 bits wide
  assign not_9_out = ~divider_1_out;  // NOT_Gate not_9, 16 bits wide
  assign not_10_out = ~divider_2_out;  // NOT_Gate not_10, 16 bits wide
  Adder #(.width(6)) adder_9 (.a(6'b000001), .b(not_7_out), .out(adder_9_out));  // open: cin, cout
  Adder #(.width(6)) adder_10 (.a(6'b000001), .b(not_8_out), .out(adder_10_out));  // open: cin, cout
  Adder #(.width(16)) adder_11 (.a(16'h1), .b(not_9_out), .out(adder_11_out));  // open: cin, cout
  Adder #(.width(16)) adder_12 (.a(16'h1), .b(not_10_out), .out(adder_12_out));  // open: cin, cout
  Multiplexer #(.width(6)) multiplexer_5 (
    .in0(V_x[7:2]), .in1(adder_9_out), .out(multiplexer_5_out), .sel(V_x[7]));  // open: en
  // Probe on adder_9_out
  Multiplexer #(.width(6)) multiplexer_6 (
    .in0(V_y[7:2]), .in1(adder_10_out), .out(multiplexer_6_out), .sel(V_y[7]));  // open: en
  // Probe on adder_10_out
  // Probe on {multiplexer_7_out, Intersection_X[9:2]}
  Multiplexer #(.width(16)) multiplexer_7 (
    .in0(divider_1_out), .in1(adder_11_out), .out({multiplexer_7_out, Intersection_X[9:2]}), .sel(xor_1_out));  // open: en
  // Probe on {multiplexer_8_out, Intersection_Y[9:2]}
  Multiplexer #(.width(16)) multiplexer_8 (
    .in0(divider_2_out), .in1(adder_12_out), .out({multiplexer_8_out, Intersection_Y[9:2]}), .sel(xor_2_out));  // open: en
  // Probe on multiplexer_5_out
  assign V_x_t = {{10{multiplexer_5_out[5]}}, multiplexer_5_out};  // Bit_Extender bit_extender_5
  // Probe on multiplexer_6_out
  assign V_y_t = {{10{multiplexer_6_out[5]}}, multiplexer_6_out};  // Bit_Extender bit_extender_6
  // Probe on {multiplexer_7_out, Intersection_X[9:2]}
  // Probe on {multiplexer_8_out, Intersection_Y[9:2]}
  // Probe on V_x_t
  // Probe on V_y_t
  // Probe on Intersection_X[9:2]
  // Probe on Intersection_Y[9:2]
  Comparator #(.width(16)) comparator_2 (.a(V_x_t), .b({16{1'b0}}), .eq(comparator_2_eq));  // open: gt, lt
  Comparator #(.width(16)) comparator_3 (.a(V_x_t), .b(V_y_t), .eq(comparator_3_eq));  // open: gt, lt
  or or_1 (NO_Intersection, Zero_Division, and_1_out);
  and and_1 (and_1_out, comparator_2_eq, comparator_3_eq);

  assign Intersection_X[1:0] = 2'b00;
  assign Intersection_Y[1:0] = 2'b00;
endmodule

module Intersect_2_2 (
  input  [7:0] V_x,
  input  [7:0] wall_x,
  input  [7:0] ball_x,
  input  [7:0] V_y,
  input  [7:0] ball_y,
  output [9:0] Intersection_X,
  output NO_Intersection,
  output [9:0] Intersection_Y
);

  wire and_1_out, comparator_2_eq, comparator_3_eq, xor_1_out, Zero_Division;
  wire [3:0] adder_4_out, adder_5_out, not_3_out, not_4_out;
  wire [5:0] adder_6_out, adder_7_out, multiplexer_3_out, multiplexer_4_out, not_5_out, not_6_out;
  wire [15:0] adder_1_out, adder_2_out, adder_3_out, adder_8_out, ball_x_t, ball_y_t, divider_1_out,
       multiplexer_1_out, multiplexer_2_out, multiplier_1_out, multiplier_2_out, multiplier_3_out, not_1_out,
       not_2_out, not_7_out, subtractor_1_out, V_x_t, V_y_t;
  wire [15:8] multiplexer_5_out, wall_x_t;

  // Probe on wall_x
  // Probe on ball_x[6:2]
  // Probe on ball_y[6:2]
  Multiplier #(.width(16)) multiplier_1 (.a(ball_y_t), .b(V_x_t), .out(multiplier_1_out));  // open: cin, cout
  Multiplier #(.width(16)) multiplier_2 (.a(ball_x_t), .b(V_y_t), .out(multiplier_2_out));  // open: cin, cout
  // Probe on {wall_x_t, Intersection_X[9:2]}
  assign {wall_x_t, Intersection_X[9:2]} = {{8{1'b0}}, wall_x};  // Bit_Extender bit_extender_1
  // Probe on ball_x_t
  assign ball_x_t = {{11{1'b0}}, ball_x[6:2]};  // Bit_Extender bit_extender_2
  // Probe on ball_y_t
  assign ball_y_t = {{11{1'b0}}, ball_y[6:2]};  // Bit_Extender bit_extender_3
  // Probe on multiplier_3_out
  Multiplier #(.width(16)) multiplier_3 (
    .a(V_y_t), .b({wall_x_t, Intersection_X[9:2]}), .out(multiplier_3_out));  // open: cin, cout
  // Probe on subtractor_1_out
  Subtractor #(.width(16)) subtractor_1 (
    .a(multiplier_1_out), .b(multiplier_2_out), .out(subtractor_1_out));  // open: bin, bout
  // Probe on adder_1_out
  Adder #(.width(16)) adder_1 (.a(multiplier_3_out), .b(subtractor_1_out), .out(adder_1_out));  // open: cin, cout
  // Probe on V_x_t
  Comparator #(.width(16)) comparator_1 (.a(V_x_t), .b({16{1'b0}}), .eq(Zero_Division));  // open: gt, lt
  assign not_1_out = ~adder_1_out;  // NOT_Gate not_1, 16 bits wide
  assign not_2_out = ~V_x_t;  // NOT_Gate not_2, 16 bits wide
  Multiplexer #(.width(16)) multiplexer_1 (
    .in0(adder_1_out), .in1(adder_2_out), .out(multiplexer_1_out), .sel(adder_1_out[15]));  // open: en
  Adder #(.width(16)) adder_2 (.a(16'h1), .b(not_1_out), .out(adder_2_out));  // open: cin, cout
  Multiplexer #(.width(16)) multiplexer_2 (
    .in0(V_x_t), .in1(adder_3_out), .out(multiplexer_2_out), .sel(V_x_t[15]));  // open: en
  Adder #(.width(16)) adder_3 (.a(16'h1), .b(not_2_out), .out(adder_3_out));  // open: cin, cout
  // Probe on V_x[7:4]
  // Probe on V_x[7:2]
  Adder #(.width(4)) adder_4 (.a(4'b0001), .b(not_3_out), .out(adder_4_out));  // open: cin, cout
  assign not_3_out = ~V_x[7:4];  // NOT_Gate not_3, 4 bits wide
  // Probe on V_y[7:4]
  // Probe on V_y[7:2]
  Adder #(.width(4)) adder_5 (.a(4'b0001), .b(not_4_out), .out(adder_5_out));  // open: cin, cout
  assign not_4_out = ~V_y[7:4];  // NOT_Gate not_4, 4 bits wide
  xor xor_1 (xor_1_out, V_x_t[15], adder_1_out[15]);
  // Probe on divider_1_out
  Divider #(.width(16)) divider_1 (
    .a(multiplexer_1_out), .b(multiplexer_2_out), .out(divider_1_out));  // open: upper, rem
  // Probe on {adder_4_out, V_x[3:2]}
  assign not_5_out = ~{adder_4_out, V_x[3:2]};  // NOT_Gate not_5, 6 bits wide
  // Probe on {adder_5_out, V_y[3:2]}
  assign not_6_out = ~{adder_5_out, V_y[3:2]};  // NOT_Gate not_6, 6 bits wide
  assign not_7_out = ~divider_1_out;  // NOT_Gate not_7, 16 bits wide
  Adder #(.width(6)) adder_6 (.a(6'b000001), .b(not_5_out), .out(adder_6_out));  // open: cin, cout
  Adder #(.width(6)) adder_7 (.a(6'b000001), .b(not_6_out), .out(adder_7_out));  // open: cin, cout
  Adder #(.width(16)) adder_8 (.a(16'h1), .b(not_7_out), .out(adder_8_out));  // open: cin, cout
  Multiplexer #(.width(6)) multiplexer_3 (
    .in0(V_x[7:2]), .in1(adder_6_out), .out(multiplexer_3_out), .sel(V_x[7]));  // open: en
  // Probe on adder_6_out
  Multiplexer #(.width(6)) multiplexer_4 (
    .in0(V_y[7:2]), .in1(adder_7_out), .out(multiplexer_4_out), .sel(V_y[7]));  // open: en
  // Probe on adder_7_out
  // Probe on {multiplexer_5_out, Intersection_Y[9:2]}
  Multiplexer #(.width(16)) multiplexer_5 (
    .in0(divider_1_out), .in1(adder_8_out), .out({multiplexer_5_out, Intersection_Y[9:2]}), .sel(xor_1_out));  // open: en
  // Probe on multiplexer_3_out
  assign V_x_t = {{10{multiplexer_3_out[5]}}, multiplexer_3_out};  // Bit_Extender bit_extender_4
  // Probe on multiplexer_4_out
  assign V_y_t = {{10{multiplexer_4_out[5]}}, multiplexer_4_out};  // Bit_Extender bit_extender_5
  // Probe on {multiplexer_5_out, Intersection_Y[9:2]}
  // Probe on V_x_t
  // Probe on V_y_t
  // Probe on Intersection_X[9:2]
  // Probe on Intersection_Y[9:2]
  Comparator #(.width(16)) comparator_2 (.a(V_x_t), .b({16{1'b0}}), .eq(comparator_2_eq));  // open: gt, lt
  Comparator #(.width(16)) comparator_3 (.a(V_x_t), .b(V_y_t), .eq(comparator_3_eq));  // open: gt, lt
  or or_1 (NO_Intersection, Zero_Division, and_1_out);
  and and_1 (and_1_out, comparator_2_eq, comparator_3_eq);

  assign Intersection_X[1:0] = 2'b00;
  assign Intersection_Y[1:0] = 2'b00;

  // Other names for the same wires on the sheet: wall_x_t[7:0] = Intersection_X[9:2]
endmodule

module Intersect_2_2_2 (
  input  [7:0] V_x,
  input  [7:0] wall_y,
  input  [7:0] ball_x,
  input  [7:0] V_y,
  input  [7:0] ball_y,
  output [9:0] Intersection_X,
  output NO_Intersection,
  output [9:0] Intersection_Y
);

  wire and_1_out, comparator_2_eq, comparator_3_eq, xor_1_out, Zero_Division;
  wire [3:0] adder_4_out, adder_5_out, not_3_out, not_4_out;
  wire [5:0] adder_6_out, adder_7_out, multiplexer_3_out, multiplexer_4_out, not_5_out, not_6_out;
  wire [15:0] adder_1_out, adder_2_out, adder_3_out, adder_8_out, ball_x_t, ball_y_t, divider_1_out,
       multiplexer_1_out, multiplexer_2_out, multiplier_1_out, multiplier_2_out, multiplier_3_out, not_1_out,
       not_2_out, not_7_out, subtractor_1_out, V_x_t, V_y_t;
  wire [15:8] multiplexer_5_out, wall_y_t;

  // Probe on wall_y
  // Probe on ball_x[6:2]
  // Probe on ball_y[6:2]
  Multiplier #(.width(16)) multiplier_1 (.a(ball_x_t), .b(V_y_t), .out(multiplier_1_out));  // open: cin, cout
  Multiplier #(.width(16)) multiplier_2 (.a(ball_y_t), .b(V_x_t), .out(multiplier_2_out));  // open: cin, cout
  // Probe on {wall_y_t, Intersection_Y[9:2]}
  assign {wall_y_t, Intersection_Y[9:2]} = {{8{1'b0}}, wall_y};  // Bit_Extender bit_extender_1
  // Probe on ball_x_t
  assign ball_x_t = {{11{1'b0}}, ball_x[6:2]};  // Bit_Extender bit_extender_2
  // Probe on ball_y_t
  assign ball_y_t = {{11{1'b0}}, ball_y[6:2]};  // Bit_Extender bit_extender_3
  // Probe on multiplier_3_out
  Multiplier #(.width(16)) multiplier_3 (
    .a(V_x_t), .b({wall_y_t, Intersection_Y[9:2]}), .out(multiplier_3_out));  // open: cin, cout
  // Probe on subtractor_1_out
  Subtractor #(.width(16)) subtractor_1 (
    .a(multiplier_1_out), .b(multiplier_2_out), .out(subtractor_1_out));  // open: bin, bout
  // Probe on adder_1_out
  Adder #(.width(16)) adder_1 (.a(multiplier_3_out), .b(subtractor_1_out), .out(adder_1_out));  // open: cin, cout
  // Probe on V_y_t
  Comparator #(.width(16)) comparator_1 (.a(V_y_t), .b({16{1'b0}}), .eq(Zero_Division));  // open: gt, lt
  assign not_1_out = ~adder_1_out;  // NOT_Gate not_1, 16 bits wide
  assign not_2_out = ~V_y_t;  // NOT_Gate not_2, 16 bits wide
  Multiplexer #(.width(16)) multiplexer_1 (
    .in0(adder_1_out), .in1(adder_2_out), .out(multiplexer_1_out), .sel(adder_1_out[15]));  // open: en
  Adder #(.width(16)) adder_2 (.a(16'h1), .b(not_1_out), .out(adder_2_out));  // open: cin, cout
  Multiplexer #(.width(16)) multiplexer_2 (
    .in0(V_y_t), .in1(adder_3_out), .out(multiplexer_2_out), .sel(V_y_t[15]));  // open: en
  Adder #(.width(16)) adder_3 (.a(16'h1), .b(not_2_out), .out(adder_3_out));  // open: cin, cout
  // Probe on V_x[7:4]
  // Probe on V_x[7:2]
  Adder #(.width(4)) adder_4 (.a(4'b0001), .b(not_3_out), .out(adder_4_out));  // open: cin, cout
  assign not_3_out = ~V_x[7:4];  // NOT_Gate not_3, 4 bits wide
  // Probe on V_y[7:4]
  // Probe on V_y[7:2]
  Adder #(.width(4)) adder_5 (.a(4'b0001), .b(not_4_out), .out(adder_5_out));  // open: cin, cout
  assign not_4_out = ~V_y[7:4];  // NOT_Gate not_4, 4 bits wide
  xor xor_1 (xor_1_out, V_y_t[15], adder_1_out[15]);
  // Probe on divider_1_out
  Divider #(.width(16)) divider_1 (
    .a(multiplexer_1_out), .b(multiplexer_2_out), .out(divider_1_out));  // open: upper, rem
  // Probe on {adder_4_out, V_x[3:2]}
  assign not_5_out = ~{adder_4_out, V_x[3:2]};  // NOT_Gate not_5, 6 bits wide
  // Probe on {adder_5_out, V_y[3:2]}
  assign not_6_out = ~{adder_5_out, V_y[3:2]};  // NOT_Gate not_6, 6 bits wide
  assign not_7_out = ~divider_1_out;  // NOT_Gate not_7, 16 bits wide
  Adder #(.width(6)) adder_6 (.a(6'b000001), .b(not_5_out), .out(adder_6_out));  // open: cin, cout
  Adder #(.width(6)) adder_7 (.a(6'b000001), .b(not_6_out), .out(adder_7_out));  // open: cin, cout
  Adder #(.width(16)) adder_8 (.a(16'h1), .b(not_7_out), .out(adder_8_out));  // open: cin, cout
  Multiplexer #(.width(6)) multiplexer_3 (
    .in0(V_x[7:2]), .in1(adder_6_out), .out(multiplexer_3_out), .sel(V_x[7]));  // open: en
  // Probe on adder_6_out
  Multiplexer #(.width(6)) multiplexer_4 (
    .in0(V_y[7:2]), .in1(adder_7_out), .out(multiplexer_4_out), .sel(V_y[7]));  // open: en
  // Probe on adder_7_out
  // Probe on {multiplexer_5_out, Intersection_X[9:2]}
  Multiplexer #(.width(16)) multiplexer_5 (
    .in0(divider_1_out), .in1(adder_8_out), .out({multiplexer_5_out, Intersection_X[9:2]}), .sel(xor_1_out));  // open: en
  // Probe on multiplexer_3_out
  assign V_x_t = {{10{multiplexer_3_out[5]}}, multiplexer_3_out};  // Bit_Extender bit_extender_4
  // Probe on multiplexer_4_out
  assign V_y_t = {{10{multiplexer_4_out[5]}}, multiplexer_4_out};  // Bit_Extender bit_extender_5
  // Probe on {multiplexer_5_out, Intersection_X[9:2]}
  // Probe on V_x_t
  // Probe on V_y_t
  // Probe on Intersection_X[9:2]
  // Probe on Intersection_Y[9:2]
  Comparator #(.width(16)) comparator_2 (.a(V_x_t), .b({16{1'b0}}), .eq(comparator_2_eq));  // open: gt, lt
  Comparator #(.width(16)) comparator_3 (.a(V_x_t), .b(V_y_t), .eq(comparator_3_eq));  // open: gt, lt
  or or_1 (NO_Intersection, Zero_Division, and_1_out);
  and and_1 (and_1_out, comparator_2_eq, comparator_3_eq);

  assign Intersection_X[1:0] = 2'b00;
  assign Intersection_Y[1:0] = 2'b00;

  // Other names for the same wires on the sheet: wall_y_t[7:0] = Intersection_Y[9:2]
endmodule

module Collision (
  input  [7:0] wall_x,
  input  [7:0] wall_y,
  input  [7:0] ball_x,
  input  [7:0] ball_y,
  input  [7:0] V_x,
  input  [7:0] V_y,
  input  [7:0] wall_size,
  output collision_happened,
  output [7:0] x_correct,
  output [7:0] y_correct
);

  wire and_1_out, and_2_out, and_3_out, and_4_out, and_5_out, and_6_out, and_7_out, and_8_out, and_9_out,
       and_11_out, comparator_1_lt, comparator_2_lt, comparator_3_eq, comparator_3_gt, comparator_4_eq,
       comparator_4_lt, comparator_5_eq, comparator_6_eq, comparator_7_eq, comparator_8_eq, comparator_9_lt,
       comparator_10_lt, comparator_11_eq, comparator_11_gt, comparator_12_eq, comparator_12_lt,
       comparator_13_eq, comparator_13_gt, comparator_14_eq, comparator_14_lt, comparator_15_eq,
       comparator_15_lt, comparator_16_eq, comparator_16_gt, Intersection_impossible,
       Intersection_point_border_condition, not_2_out, not_3_out, or_1_out, or_2_out, or_3_out, or_5_out,
       or_6_out, or_7_out, or_8_out, or_9_out, or_10_out, wall_crossing, xor_1_out;
  wire [7:0] adder_3_out, adder_7_out, not_1_out, not_4_out;
  wire [9:0] adder_1_out, adder_2_out, adder_4_out, adder_6_out, adder_8_out, Inter_x, Inter_y,
       multiplexer_1_out, multiplexer_2_out, multiplexer_4_out, multiplexer_5_out, Py_1, Py_2,
       subtractor_1_out, subtractor_2_out, subtractor_3_out, subtractor_4_out, subtractor_5_out,
       subtractor_6_out, subtractor_7_out, subtractor_8_out, subtractor_9_out, vel_x, vel_y, x_b, x_res, y_b,
       y_res;
  wire [9:7] controlled_buffer_1_out, controlled_buffer_2_out, controlled_buffer_3_out,
       controlled_buffer_4_out;

  // Probe on wall_x
  // Probe on wall_y
  // Probe on ball_x[6:2]
  // Probe on ball_y[6:2]
  // Probe on V_x[7:4]
  // Probe on V_y[7:4]
  // Probe on wall_size
  Adder #(.width(10)) adder_1 (.a(10'h4), .b(Inter_x), .out(adder_1_out));  // open: cin, cout
  Adder #(.width(10)) adder_2 (.a(10'h4), .b(Inter_y), .out(adder_2_out));  // open: cin, cout
  assign x_b = {{3{1'b0}}, ball_x[6:0]};  // Bit_Extender bit_extender_1
  assign y_b = {{3{1'b0}}, ball_y[6:0]};  // Bit_Extender bit_extender_2
  assign vel_x = {{4{V_x[7]}}, V_x[7:2]};  // Bit_Extender bit_extender_3
  assign vel_y = {{4{V_y[7]}}, V_y[7:2]};  // Bit_Extender bit_extender_4
  Comparator #(.width(10)) comparator_1 (.a(adder_1_out), .b(10'h80), .lt(comparator_1_lt));  // open: gt, eq
  Comparator #(.width(10)) comparator_2 (.a(adder_2_out), .b(10'h80), .lt(comparator_2_lt));  // open: gt, eq
  // Probe on {wall_x, 2'b00}
  // Probe on {wall_y, 2'b00}
  // Probe on x_b
  // Probe on y_b
  // Probe on vel_x
  // Probe on vel_y
  // Probe on {wall_size, 2'b00}
  and and_1 (and_1_out, comparator_1_lt, ~adder_1_out[9]);  // AND_Gate
  and and_2 (and_2_out, comparator_2_lt, ~adder_2_out[9]);  // AND_Gate
  Comparator comparator_3 (.a(Py_1[9:2]), .b({8{1'b0}}), .gt(comparator_3_gt), .eq(comparator_3_eq));  // open: lt
  Comparator comparator_4 (.a(Py_2[9:2]), .b({8{1'b0}}), .eq(comparator_4_eq), .lt(comparator_4_lt));  // open: gt
  or or_1 (or_1_out, comparator_3_gt, comparator_3_eq);
  or or_2 (or_2_out, comparator_4_eq, comparator_4_lt);
  assign {controlled_buffer_1_out, x_correct[6:0]} = and_3_out ? multiplexer_1_out : 10'bz;  // Controlled_Buffer controlled_buffer_1
  Multiplexer #(.width(10)) multiplexer_1 (
    .in0(Inter_x), .in1(adder_1_out), .out(multiplexer_1_out), .sel(and_1_out));  // open: en
  Multiplexer #(.width(10)) multiplexer_2 (
    .in0(Inter_y), .in1(adder_2_out), .out(multiplexer_2_out), .sel(and_2_out));  // open: en
  assign not_1_out = ~vel_x[9:2];  // NOT_Gate not_1, 8 bits wide
  Adder adder_3 (.a(not_1_out), .b(8'h1), .out(adder_3_out));  // open: cin, cout
  Comparator comparator_5 (.a({8{1'b0}}), .b(Py_1[9:2]), .eq(comparator_5_eq));  // open: gt, lt
  Comparator comparator_6 (.a(Py_2[9:2]), .b({8{1'b0}}), .eq(comparator_6_eq));  // open: gt, lt
  Comparator comparator_7 (.a({8{1'b0}}), .b(Py_2[9:2]), .eq(comparator_7_eq));  // open: gt, lt
  Comparator comparator_8 (.a(Py_1[9:2]), .b({8{1'b0}}), .eq(comparator_8_eq));  // open: gt, lt
  and and_3 (and_3_out, or_1_out, or_2_out);
  assign {controlled_buffer_2_out, y_correct[6:0]} = and_3_out ? multiplexer_2_out : 10'bz;  // Controlled_Buffer controlled_buffer_2
  Subtractor #(.width(10)) subtractor_1 (.a(x_b), .b({wall_x, 2'b00}), .out(subtractor_1_out));  // open: bin, bout
  Subtractor #(.width(10)) subtractor_2 (.a(y_b), .b({wall_y, 2'b00}), .out(subtractor_2_out));  // open: bin, bout
  xor xor_1 (xor_1_out, Py_1[9], Py_2[9]);
  and and_4 (and_4_out, comparator_5_eq, not_2_out);
  not not_2 (not_2_out, comparator_6_eq);
  and and_5 (and_5_out, comparator_7_eq, not_3_out);
  not not_3 (not_3_out, comparator_8_eq);
  Adder #(.width(10)) adder_4 (.a(x_b), .b(vel_x), .out(adder_4_out));  // open: cin, cout
  // Probe on Py_1[9:2]
  Adder #(.width(10)) adder_5 (.a(subtractor_1_out), .b(subtractor_2_out), .out(Py_1));  // open: cin, cout
  or or_3 (or_3_out, and_4_out, and_5_out);
  // Probe on Inter_x[9:2]
  Intersect intersect_1 (
    .V_x(V_x), .wall_x(wall_x), .wall_y(wall_y), .ball_x(ball_x), .V_y(V_y), .ball_y(ball_y),
    .Intersection_X(Inter_x), .NO_Intersection(Intersection_impossible), .Intersection_Y(Inter_y));
  // Probe on x_res[9:2]
  Multiplexer #(.width(10)) multiplexer_3 (
    .in0(adder_4_out), .in1(subtractor_3_out), .out(x_res), .sel(vel_x[9]));  // open: en
  Subtractor #(.width(10)) subtractor_3 (
    .a(x_b), .b({adder_3_out, vel_x[1:0]}), .out(subtractor_3_out));  // open: bin, bout
  or or_4 (wall_crossing, xor_1_out, or_3_out);
  // Probe on Inter_y[9:2]
  Subtractor #(.width(10)) subtractor_4 (.a(Inter_x), .b(10'h4), .out(subtractor_4_out));  // open: bin, bout
  Subtractor #(.width(10)) subtractor_5 (.a(Inter_y), .b(10'h4), .out(subtractor_5_out));  // open: bin, bout
  Subtractor #(.width(10)) subtractor_6 (
    .a({wall_y, 2'b00}), .b({wall_size, 2'b00}), .out(subtractor_6_out));  // open: bin, bout
  Comparator #(.width(10)) comparator_9 (.a(subtractor_4_out), .b(10'h80), .lt(comparator_9_lt));  // open: gt, eq
  Comparator #(.width(10)) comparator_10 (.a(subtractor_5_out), .b(10'h80), .lt(comparator_10_lt));  // open: gt, eq
  assign not_4_out = ~vel_y[9:2];  // NOT_Gate not_4, 8 bits wide
  Comparator #(.width(10)) comparator_11 (
    .a(Inter_x), .b({wall_x, 2'b00}), .gt(comparator_11_gt), .eq(comparator_11_eq));  // open: lt
  Comparator #(.width(10)) comparator_12 (
    .a(Inter_x), .b(adder_6_out), .eq(comparator_12_eq), .lt(comparator_12_lt));  // open: gt
  Adder #(.width(10)) adder_6 (.a({wall_x, 2'b00}), .b({wall_size, 2'b00}), .out(adder_6_out));  // open: cin, cout
  Comparator #(.width(10)) comparator_13 (
    .a(Inter_y), .b(subtractor_6_out), .gt(comparator_13_gt), .eq(comparator_13_eq));  // open: lt
  Comparator #(.width(10)) comparator_14 (
    .a(Inter_y), .b({wall_y, 2'b00}), .eq(comparator_14_eq), .lt(comparator_14_lt));  // open: gt
  and and_6 (and_6_out, comparator_9_lt, ~subtractor_4_out[9]);  // AND_Gate
  and and_7 (and_7_out, comparator_10_lt, ~subtractor_5_out[9]);  // AND_Gate
  Adder adder_7 (.a(not_4_out), .b(8'h1), .out(adder_7_out));  // open: cin, cout
  Subtractor #(.width(10)) subtractor_7 (.a(x_res), .b({wall_x, 2'b00}), .out(subtractor_7_out));  // open: bin, bout
  Subtractor #(.width(10)) subtractor_8 (.a(y_res), .b({wall_y, 2'b00}), .out(subtractor_8_out));  // open: bin, bout
  or or_5 (or_5_out, comparator_11_gt, comparator_11_eq);
  or or_6 (or_6_out, comparator_12_eq, comparator_12_lt);
  or or_7 (or_7_out, comparator_13_gt, comparator_13_eq);
  or or_8 (or_8_out, comparator_14_eq, comparator_14_lt);
  Adder #(.width(10)) adder_8 (.a(y_b), .b(vel_y), .out(adder_8_out));  // open: cin, cout
  // Probe on Py_2[9:2]
  Adder #(.width(10)) adder_9 (.a(subtractor_7_out), .b(subtractor_8_out), .out(Py_2));  // open: cin, cout
  and and_8 (and_8_out, or_5_out, or_6_out);
  and and_9 (and_9_out, or_7_out, or_8_out);
  Comparator comparator_15 (.a(Py_1[9:2]), .b({8{1'b0}}), .eq(comparator_15_eq), .lt(comparator_15_lt));  // open: gt
  Comparator comparator_16 (.a(Py_2[9:2]), .b({8{1'b0}}), .gt(comparator_16_gt), .eq(comparator_16_eq));  // open: lt
  Multiplexer #(.width(10)) multiplexer_4 (
    .in0(Inter_x), .in1(subtractor_4_out), .out(multiplexer_4_out), .sel(and_6_out));  // open: en
  Multiplexer #(.width(10)) multiplexer_5 (
    .in0(Inter_y), .in1(subtractor_5_out), .out(multiplexer_5_out), .sel(and_7_out));  // open: en
  Subtractor #(.width(10)) subtractor_9 (
    .a(y_b), .b({adder_7_out, vel_y[1:0]}), .out(subtractor_9_out));  // open: bin, bout
  and and_10 (Intersection_point_border_condition, and_8_out, and_9_out);
  or or_9 (or_9_out, comparator_15_eq, comparator_15_lt);
  and and_11 (and_11_out, or_9_out, or_10_out);
  or or_10 (or_10_out, comparator_16_gt, comparator_16_eq);
  assign {controlled_buffer_3_out, x_correct[6:0]} = and_11_out ? multiplexer_4_out : 10'bz;  // Controlled_Buffer controlled_buffer_3
  assign {controlled_buffer_4_out, y_correct[6:0]} = and_11_out ? multiplexer_5_out : 10'bz;  // Controlled_Buffer controlled_buffer_4
  // Probe on y_res[9:2]
  Multiplexer #(.width(10)) multiplexer_6 (
    .in0(adder_8_out), .in1(subtractor_9_out), .out(y_res), .sel(vel_y[9]));  // open: en
  and and_12 (collision_happened, wall_crossing, Intersection_point_border_condition, ~Intersection_impossible);  // AND_Gate

  assign x_correct[7] = ball_x[7];
  assign y_correct[7] = ball_y[7];

  // Other names for the same wires on the sheet: w_x[9:2] = wall_x; w_y[9:2] = wall_y; wall_size_t[9:2] = wall_size;
  //   x_corr[7:0] = {ball_x[7], x_correct[6:0]}; y_corr[7:0] = {ball_y[7], y_correct[6:0]}

  // Notes on the sheet:
  //   Format: SXXXXXXXFF
endmodule

module Collision_2 (
  input  [7:0] wall_x,
  input  [7:0] wall_y,
  input  [7:0] ball_x,
  input  [7:0] ball_y,
  input  [7:0] V_x,
  input  [7:0] V_y,
  input  [7:0] wall_size,
  output collision_happened,
  output [7:0] x_correct,
  output [7:0] y_correct
);

  wire and_1_out, and_2_out, and_3_out, and_4_out, and_5_out, and_6_out, and_7_out, and_9_out, and_10_out,
       and_12_out, comparator_1_lt, comparator_2_lt, comparator_3_eq, comparator_4_eq, comparator_5_eq,
       comparator_6_eq, comparator_7_eq, comparator_7_gt, comparator_8_eq, comparator_8_lt, comparator_9_eq,
       comparator_9_gt, comparator_10_eq, comparator_10_lt, comparator_11_eq, comparator_11_gt,
       comparator_12_eq, comparator_12_lt, comparator_13_lt, comparator_14_lt, comparator_15_eq,
       comparator_15_lt, comparator_16_eq, comparator_16_gt, Intersection_impossible,
       Intersection_point_border_condition, not_1_out, not_2_out, or_1_out, or_2_out, or_3_out, or_5_out,
       or_6_out, or_7_out, or_8_out, or_9_out, or_10_out, wall_crossing, xor_1_out;
  wire [7:0] adder_7_out, adder_8_out, not_3_out, not_4_out;
  wire [9:0] adder_1_out, adder_3_out, adder_4_out, adder_5_out, adder_9_out, adder_10_out, Inter_x, Inter_y,
       multiplexer_1_out, multiplexer_2_out, multiplexer_3_out, multiplexer_4_out, Py_1, Py_2,
       subtractor_1_out, subtractor_2_out, subtractor_3_out, subtractor_4_out, subtractor_5_out,
       subtractor_6_out, subtractor_7_out, subtractor_8_out, vel_x, vel_y, x_b, x_res, y_b, y_res;
  wire [9:7] controlled_buffer_1_out, controlled_buffer_2_out, controlled_buffer_3_out,
       controlled_buffer_4_out;

  // Probe on wall_x
  // Probe on wall_y
  // Probe on ball_x[6:2]
  // Probe on ball_y[6:2]
  // Probe on V_x[7:4]
  // Probe on V_y[7:4]
  // Probe on wall_size
  assign x_b = {{3{1'b0}}, ball_x[6:0]};  // Bit_Extender bit_extender_1
  assign y_b = {{3{1'b0}}, ball_y[6:0]};  // Bit_Extender bit_extender_2
  assign vel_x = {{4{V_x[7]}}, V_x[7:2]};  // Bit_Extender bit_extender_3
  assign vel_y = {{4{V_y[7]}}, V_y[7:2]};  // Bit_Extender bit_extender_4
  Subtractor #(.width(10)) subtractor_1 (.a(Inter_x), .b(10'h4), .out(subtractor_1_out));  // open: bin, bout
  Adder #(.width(10)) adder_1 (.a(10'h4), .b(Inter_y), .out(adder_1_out));  // open: cin, cout
  // Probe on {wall_x, 2'b00}
  // Probe on {wall_y, 2'b00}
  // Probe on x_b
  // Probe on y_b
  // Probe on vel_x
  // Probe on vel_y
  // Probe on {wall_size, 2'b00}
  Comparator #(.width(10)) comparator_1 (.a(subtractor_1_out), .b(10'h80), .lt(comparator_1_lt));  // open: gt, eq
  Comparator #(.width(10)) comparator_2 (.a(adder_1_out), .b(10'h80), .lt(comparator_2_lt));  // open: gt, eq
  and and_1 (and_1_out, comparator_1_lt, ~subtractor_1_out[9]);  // AND_Gate
  and and_2 (and_2_out, comparator_2_lt, ~adder_1_out[9]);  // AND_Gate
  xor xor_1 (xor_1_out, Py_1[9], Py_2[9]);
  Comparator comparator_3 (.a({8{1'b0}}), .b(Py_1[9:2]), .eq(comparator_3_eq));  // open: gt, lt
  not not_1 (not_1_out, comparator_4_eq);
  Comparator comparator_4 (.a(Py_2[9:2]), .b({8{1'b0}}), .eq(comparator_4_eq));  // open: gt, lt
  Comparator comparator_5 (.a({8{1'b0}}), .b(Py_2[9:2]), .eq(comparator_5_eq));  // open: gt, lt
  not not_2 (not_2_out, comparator_6_eq);
  Comparator comparator_6 (.a(Py_1[9:2]), .b({8{1'b0}}), .eq(comparator_6_eq));  // open: gt, lt
  or or_1 (or_1_out, comparator_7_gt, comparator_7_eq);
  Comparator comparator_7 (.a(Py_1[9:2]), .b({8{1'b0}}), .gt(comparator_7_gt), .eq(comparator_7_eq));  // open: lt
  Comparator comparator_8 (.a(Py_2[9:2]), .b({8{1'b0}}), .eq(comparator_8_eq), .lt(comparator_8_lt));  // open: gt
  or or_2 (or_2_out, comparator_8_eq, comparator_8_lt);
  Multiplexer #(.width(10)) multiplexer_1 (
    .in0(Inter_x), .in1(subtractor_1_out), .out(multiplexer_1_out), .sel(and_1_out));  // open: en
  Multiplexer #(.width(10)) multiplexer_2 (
    .in0(Inter_y), .in1(adder_1_out), .out(multiplexer_2_out), .sel(and_2_out));  // open: en
  and and_3 (and_3_out, comparator_3_eq, not_1_out);
  and and_4 (and_4_out, comparator_5_eq, not_2_out);
  and and_5 (and_5_out, or_1_out, or_2_out);
  assign {controlled_buffer_1_out, x_correct[6:0]} = and_5_out ? multiplexer_1_out : 10'bz;  // Controlled_Buffer controlled_buffer_1
  assign {controlled_buffer_2_out, y_correct[6:0]} = and_5_out ? multiplexer_2_out : 10'bz;  // Controlled_Buffer controlled_buffer_2
  or or_3 (or_3_out, and_3_out, and_4_out);
  // Probe on Inter_x[9:2]
  Intersect_2 intersect_1 (
    .V_x(V_x), .wall_x(wall_x), .wall_y(wall_y), .ball_x(ball_x), .V_y(V_y), .ball_y(ball_y),
    .NO_Intersection(Intersection_impossible), .Intersection_X(Inter_x), .Intersection_Y(Inter_y));
  or or_4 (wall_crossing, xor_1_out, or_3_out);
  // Probe on Inter_y[9:2]
  Subtractor #(.width(10)) subtractor_2 (.a({wall_x, 2'b00}), .b(x_b), .out(subtractor_2_out));  // open: bin, bout
  Subtractor #(.width(10)) subtractor_3 (.a(y_b), .b({wall_y, 2'b00}), .out(subtractor_3_out));  // open: bin, bout
  Adder #(.width(10)) adder_2 (.a(subtractor_2_out), .b(subtractor_3_out), .out(Py_1));  // open: cin, cout
  Comparator #(.width(10)) comparator_9 (
    .a(Inter_x), .b({wall_x, 2'b00}), .gt(comparator_9_gt), .eq(comparator_9_eq));  // open: lt
  Comparator #(.width(10)) comparator_10 (
    .a(Inter_x), .b(adder_3_out), .eq(comparator_10_eq), .lt(comparator_10_lt));  // open: gt
  Adder #(.width(10)) adder_3 (.a({wall_x, 2'b00}), .b({wall_size, 2'b00}), .out(adder_3_out));  // open: cin, cout
  Comparator #(.width(10)) comparator_11 (
    .a(Inter_y), .b({wall_y, 2'b00}), .gt(comparator_11_gt), .eq(comparator_11_eq));  // open: lt
  Comparator #(.width(10)) comparator_12 (
    .a(Inter_y), .b(adder_4_out), .eq(comparator_12_eq), .lt(comparator_12_lt));  // open: gt
  Adder #(.width(10)) adder_4 (.a({wall_y, 2'b00}), .b({wall_size, 2'b00}), .out(adder_4_out));  // open: cin, cout
  Adder #(.width(10)) adder_5 (.a(Inter_x), .b(10'h4), .out(adder_5_out));  // open: cin, cout
  Subtractor #(.width(10)) subtractor_4 (.a(Inter_y), .b(10'h4), .out(subtractor_4_out));  // open: bin, bout
  // Probe on Py_1[9:2]
  or or_5 (or_5_out, comparator_9_gt, comparator_9_eq);
  or or_6 (or_6_out, comparator_10_eq, comparator_10_lt);
  or or_7 (or_7_out, comparator_11_gt, comparator_11_eq);
  or or_8 (or_8_out, comparator_12_eq, comparator_12_lt);
  Comparator #(.width(10)) comparator_13 (.a(adder_5_out), .b(10'h80), .lt(comparator_13_lt));  // open: gt, eq
  and and_6 (and_6_out, comparator_13_lt, ~adder_5_out[9]);  // AND_Gate
  Comparator #(.width(10)) comparator_14 (.a(subtractor_4_out), .b(10'h80), .lt(comparator_14_lt));  // open: gt, eq
  and and_7 (and_7_out, comparator_14_lt, ~subtractor_4_out[9]);  // AND_Gate
  and and_8 (collision_happened, wall_crossing, Intersection_point_border_condition, ~Intersection_impossible);  // AND_Gate
  and and_9 (and_9_out, or_5_out, or_6_out);
  and and_10 (and_10_out, or_7_out, or_8_out);
  // Probe on x_correct[6:2]
  // Probe on y_correct[6:2]
  and and_11 (Intersection_point_border_condition, and_9_out, and_10_out);
  Comparator comparator_15 (.a(Py_1[9:2]), .b({8{1'b0}}), .eq(comparator_15_eq), .lt(comparator_15_lt));  // open: gt
  Comparator comparator_16 (.a(Py_2[9:2]), .b({8{1'b0}}), .gt(comparator_16_gt), .eq(comparator_16_eq));  // open: lt
  Multiplexer #(.width(10)) multiplexer_3 (
    .in0(Inter_x), .in1(adder_5_out), .out(multiplexer_3_out), .sel(and_6_out));  // open: en
  Multiplexer #(.width(10)) multiplexer_4 (
    .in0(Inter_y), .in1(subtractor_4_out), .out(multiplexer_4_out), .sel(and_7_out));  // open: en
  Subtractor #(.width(10)) subtractor_5 (.a({wall_x, 2'b00}), .b(x_res), .out(subtractor_5_out));  // open: bin, bout
  Subtractor #(.width(10)) subtractor_6 (.a(y_res), .b({wall_y, 2'b00}), .out(subtractor_6_out));  // open: bin, bout
  or or_9 (or_9_out, comparator_15_eq, comparator_15_lt);
  and and_12 (and_12_out, or_9_out, or_10_out);
  or or_10 (or_10_out, comparator_16_gt, comparator_16_eq);
  assign {controlled_buffer_3_out, x_correct[6:0]} = and_12_out ? multiplexer_3_out : 10'bz;  // Controlled_Buffer controlled_buffer_3
  assign {controlled_buffer_4_out, y_correct[6:0]} = and_12_out ? multiplexer_4_out : 10'bz;  // Controlled_Buffer controlled_buffer_4
  // Probe on Py_2[9:2]
  Adder #(.width(10)) adder_6 (.a(subtractor_5_out), .b(subtractor_6_out), .out(Py_2));  // open: cin, cout
  assign not_3_out = ~vel_x[9:2];  // NOT_Gate not_3, 8 bits wide
  Adder adder_7 (.a(not_3_out), .b(8'h1), .out(adder_7_out));  // open: cin, cout
  assign not_4_out = ~vel_y[9:2];  // NOT_Gate not_4, 8 bits wide
  Adder adder_8 (.a(not_4_out), .b(8'h1), .out(adder_8_out));  // open: cin, cout
  Adder #(.width(10)) adder_9 (.a(x_b), .b(vel_x), .out(adder_9_out));  // open: cin, cout
  Subtractor #(.width(10)) subtractor_7 (
    .a(x_b), .b({adder_7_out, vel_x[1:0]}), .out(subtractor_7_out));  // open: bin, bout
  Adder #(.width(10)) adder_10 (.a(y_b), .b(vel_y), .out(adder_10_out));  // open: cin, cout
  Subtractor #(.width(10)) subtractor_8 (
    .a(y_b), .b({adder_8_out, vel_y[1:0]}), .out(subtractor_8_out));  // open: bin, bout
  // Probe on x_res[9:2]
  Multiplexer #(.width(10)) multiplexer_5 (
    .in0(adder_9_out), .in1(subtractor_7_out), .out(x_res), .sel(vel_x[9]));  // open: en
  // Probe on y_res[9:2]
  Multiplexer #(.width(10)) multiplexer_6 (
    .in0(adder_10_out), .in1(subtractor_8_out), .out(y_res), .sel(vel_y[9]));  // open: en

  assign x_correct[7] = ball_x[7];
  assign y_correct[7] = ball_y[7];

  // Other names for the same wires on the sheet: w_x[9:2] = wall_x; w_y[9:2] = wall_y; wall_size_t[9:2] = wall_size;
  //   x_corr[7:0] = {ball_x[7], x_correct[6:0]}; y_corr[7:0] = {ball_y[7], y_correct[6:0]}

  // Notes on the sheet:
  //   Format: SXXXXXXXFF
endmodule

module Collision_2_2 (
  input  [7:0] wall_x,
  input  [7:0] wall_y,
  input  [7:0] ball_x,
  input  [7:0] ball_y,
  input  [7:0] V_x,
  input  [7:0] V_y,
  input  [7:0] wall_size,
  output collision_happened,
  output [7:0] x_correct,
  output [7:0] y_correct
);

  wire and_1_out, and_2_out, and_3_out, and_4_out, and_5_out, and_8_out, comparator_1_lt, comparator_2_eq,
       comparator_3_eq, comparator_4_eq, comparator_5_eq, comparator_6_eq, comparator_6_gt, comparator_7_eq,
       comparator_7_lt, comparator_8_eq, comparator_8_gt, comparator_9_eq, comparator_9_lt, comparator_10_lt,
       comparator_11_eq, comparator_11_lt, comparator_12_eq, comparator_12_gt, Intersection_impossible,
       Intersection_point_border_condition, not_2_out, not_3_out, or_1_out, or_2_out, or_3_out, or_5_out,
       or_6_out, or_7_out, or_8_out, wall_crossing, xor_1_out;
  wire [7:0] adder_2_out, not_1_out;
  wire [9:0] adder_1_out, adder_3_out, adder_4_out, Inter_x, Inter_y, multiplexer_1_out, multiplexer_3_out,
       Px_1, Px_2, subtractor_1_out, subtractor_2_out, vel_x, vel_y, x_b, x_res, y_b;
  wire [9:7] controlled_buffer_1_out, controlled_buffer_2_out, controlled_buffer_3_out,
       controlled_buffer_4_out;

  // Probe on wall_x
  // Probe on wall_y
  // Probe on ball_x[6:2]
  // Probe on ball_y[6:2]
  // Probe on V_x[7:4]
  // Probe on V_y[7:4]
  // Probe on wall_size
  assign x_b = {{3{1'b0}}, ball_x[6:0]};  // Bit_Extender bit_extender_1
  assign y_b = {{3{1'b0}}, ball_y[6:0]};  // Bit_Extender bit_extender_2
  assign vel_x = {{4{V_x[7]}}, V_x[7:2]};  // Bit_Extender bit_extender_3
  assign vel_y = {{4{V_y[7]}}, V_y[7:2]};  // Bit_Extender bit_extender_4
  Adder #(.width(10)) adder_1 (.a(Inter_x), .b(10'h4), .out(adder_1_out));  // open: cin, cout
  // Probe on {wall_x, 2'b00}
  // Probe on {wall_y, 2'b00}
  // Probe on x_b
  // Probe on y_b
  // Probe on vel_x
  // Probe on vel_y
  // Probe on {wall_size, 2'b00}
  Comparator #(.width(10)) comparator_1 (.a(adder_1_out), .b(10'h80), .lt(comparator_1_lt));  // open: gt, eq
  and and_1 (and_1_out, comparator_1_lt, ~adder_1_out[9]);  // AND_Gate
  assign not_1_out = ~vel_x[9:2];  // NOT_Gate not_1, 8 bits wide
  Adder adder_2 (.a(not_1_out), .b(8'h1), .out(adder_2_out));  // open: cin, cout
  xor xor_1 (xor_1_out, Px_1[9], Px_2[9]);
  Comparator comparator_2 (.a({8{1'b0}}), .b(Px_1[9:2]), .eq(comparator_2_eq));  // open: gt, lt
  Comparator comparator_3 (.a(Px_2[9:2]), .b({8{1'b0}}), .eq(comparator_3_eq));  // open: gt, lt
  not not_2 (not_2_out, comparator_3_eq);
  Comparator comparator_4 (.a({8{1'b0}}), .b(Px_2[9:2]), .eq(comparator_4_eq));  // open: gt, lt
  Comparator comparator_5 (.a(Px_1[9:2]), .b({8{1'b0}}), .eq(comparator_5_eq));  // open: gt, lt
  not not_3 (not_3_out, comparator_5_eq);
  or or_1 (or_1_out, comparator_6_gt, comparator_6_eq);
  Comparator comparator_6 (.a(Px_1[9:2]), .b({8{1'b0}}), .gt(comparator_6_gt), .eq(comparator_6_eq));  // open: lt
  or or_2 (or_2_out, comparator_7_eq, comparator_7_lt);
  Comparator comparator_7 (.a(Px_2[9:2]), .b({8{1'b0}}), .eq(comparator_7_eq), .lt(comparator_7_lt));  // open: gt
  Multiplexer #(.width(10)) multiplexer_1 (
    .in0(Inter_x), .in1(adder_1_out), .out(multiplexer_1_out), .sel(and_1_out));  // open: en
  and and_2 (and_2_out, comparator_2_eq, not_2_out);
  and and_3 (and_3_out, comparator_4_eq, not_3_out);
  and and_4 (and_4_out, or_1_out, or_2_out);
  assign {controlled_buffer_1_out, x_correct[6:0]} = and_4_out ? multiplexer_1_out : 10'bz;  // Controlled_Buffer controlled_buffer_1
  assign {controlled_buffer_2_out, y_correct[6:0]} = and_4_out ? Inter_y : 10'bz;  // Controlled_Buffer controlled_buffer_2
  Adder #(.width(10)) adder_3 (.a(x_b), .b(vel_x), .out(adder_3_out));  // open: cin, cout
  Subtractor #(.width(10)) subtractor_1 (
    .a(x_b), .b({adder_2_out, vel_x[1:0]}), .out(subtractor_1_out));  // open: bin, bout
  or or_3 (or_3_out, and_2_out, and_3_out);
  // Probe on Inter_x[9:2]
  Intersect_2_2 intersect_1 (
    .V_x(V_x), .wall_x(wall_x), .ball_x(ball_x), .V_y(V_y), .ball_y(ball_y),
    .NO_Intersection(Intersection_impossible), .Intersection_X(Inter_x), .Intersection_Y(Inter_y));
  // Probe on x_res[9:2]
  Multiplexer #(.width(10)) multiplexer_2 (
    .in0(adder_3_out), .in1(subtractor_1_out), .out(x_res), .sel(vel_x[9]));  // open: en
  or or_4 (wall_crossing, xor_1_out, or_3_out);
  // Probe on Inter_y[9:2]
  Subtractor #(.width(10)) subtractor_2 (.a(Inter_x), .b(10'h4), .out(subtractor_2_out));  // open: bin, bout
  Subtractor #(.width(10)) subtractor_3 (.a(x_b), .b({wall_x, 2'b00}), .out(Px_1));  // open: bin, bout
  Comparator #(.width(10)) comparator_8 (
    .a(Inter_y), .b({wall_y, 2'b00}), .gt(comparator_8_gt), .eq(comparator_8_eq));  // open: lt
  Comparator #(.width(10)) comparator_9 (
    .a(Inter_y), .b(adder_4_out), .eq(comparator_9_eq), .lt(comparator_9_lt));  // open: gt
  Adder #(.width(10)) adder_4 (.a({wall_y, 2'b00}), .b({wall_size, 2'b00}), .out(adder_4_out));  // open: cin, cout
  // Probe on Px_1[9:2]
  or or_5 (or_5_out, comparator_8_gt, comparator_8_eq);
  or or_6 (or_6_out, comparator_9_eq, comparator_9_lt);
  Comparator #(.width(10)) comparator_10 (.a(subtractor_2_out), .b(10'h80), .lt(comparator_10_lt));  // open: gt, eq
  and and_5 (and_5_out, comparator_10_lt, ~subtractor_2_out[9]);  // AND_Gate
  and and_6 (collision_happened, wall_crossing, Intersection_point_border_condition, ~Intersection_impossible);  // AND_Gate
  and and_7 (Intersection_point_border_condition, or_5_out, or_6_out);
  Comparator comparator_11 (.a(Px_1[9:2]), .b({8{1'b0}}), .eq(comparator_11_eq), .lt(comparator_11_lt));  // open: gt
  or or_7 (or_7_out, comparator_11_eq, comparator_11_lt);
  or or_8 (or_8_out, comparator_12_gt, comparator_12_eq);
  Comparator comparator_12 (.a(Px_2[9:2]), .b({8{1'b0}}), .gt(comparator_12_gt), .eq(comparator_12_eq));  // open: lt
  Multiplexer #(.width(10)) multiplexer_3 (
    .in0(Inter_x), .in1(subtractor_2_out), .out(multiplexer_3_out), .sel(and_5_out));  // open: en
  Subtractor #(.width(10)) subtractor_4 (.a(x_res), .b({wall_x, 2'b00}), .out(Px_2));  // open: bin, bout
  and and_8 (and_8_out, or_7_out, or_8_out);
  assign {controlled_buffer_3_out, x_correct[6:0]} = and_8_out ? multiplexer_3_out : 10'bz;  // Controlled_Buffer controlled_buffer_3
  assign {controlled_buffer_4_out, y_correct[6:0]} = and_8_out ? Inter_y : 10'bz;  // Controlled_Buffer controlled_buffer_4
  // Probe on Px_2[9:2]

  assign x_correct[7] = ball_x[7];
  assign y_correct[7] = ball_y[7];

  // Other names for the same wires on the sheet: w_x[9:2] = wall_x; w_y[9:2] = wall_y; wall_size_t[9:2] = wall_size;
  //   x_corr[7:0] = {ball_x[7], x_correct[6:0]}; y_corr[7:0] = {ball_y[7], y_correct[6:0]}

  // Notes on the sheet:
  //   Format: SXXXXXXXFF
endmodule

module Collision_2_2_2 (
  input  [7:0] wall_x,
  input  [7:0] wall_y,
  input  [7:0] ball_x,
  input  [7:0] ball_y,
  input  [7:0] V_x,
  input  [7:0] V_y,
  input  [7:0] wall_size,
  output collision_happened,
  output [7:0] x_correct,
  output [7:0] y_correct
);

  wire and_1_out, and_2_out, and_3_out, and_4_out, and_7_out, and_8_out, comparator_1_lt, comparator_2_eq,
       comparator_3_eq, comparator_4_eq, comparator_5_eq, comparator_6_eq, comparator_6_gt, comparator_7_eq,
       comparator_7_lt, comparator_8_eq, comparator_8_gt, comparator_9_eq, comparator_9_lt, comparator_10_lt,
       comparator_11_eq, comparator_11_lt, comparator_12_eq, comparator_12_gt, Intersection_impossible,
       Intersection_point_border_condition, not_2_out, not_3_out, or_1_out, or_2_out, or_3_out, or_5_out,
       or_6_out, or_7_out, or_8_out, wall_crossing, xor_1_out;
  wire [7:0] adder_2_out, not_1_out;
  wire [9:0] adder_1_out, adder_3_out, adder_4_out, Inter_x, Inter_y, multiplexer_1_out, multiplexer_3_out,
       Py_1, Py_2, subtractor_1_out, subtractor_3_out, vel_x, vel_y, x_b, y_b, y_res;
  wire [9:7] controlled_buffer_1_out, controlled_buffer_2_out, controlled_buffer_3_out,
       controlled_buffer_4_out;

  // Probe on wall_x
  // Probe on wall_y
  // Probe on ball_x[6:2]
  // Probe on ball_y[6:2]
  // Probe on V_x[7:4]
  // Probe on V_y[7:4]
  // Probe on wall_size
  assign x_b = {{3{1'b0}}, ball_x[6:0]};  // Bit_Extender bit_extender_1
  assign y_b = {{3{1'b0}}, ball_y[6:0]};  // Bit_Extender bit_extender_2
  assign vel_x = {{4{V_x[7]}}, V_x[7:2]};  // Bit_Extender bit_extender_3
  assign vel_y = {{4{V_y[7]}}, V_y[7:2]};  // Bit_Extender bit_extender_4
  // Probe on {wall_x, 2'b00}
  // Probe on {wall_y, 2'b00}
  // Probe on x_b
  // Probe on y_b
  // Probe on vel_x
  // Probe on vel_y
  // Probe on {wall_size, 2'b00}
  Adder #(.width(10)) adder_1 (.a(Inter_y), .b(10'h4), .out(adder_1_out));  // open: cin, cout
  Comparator #(.width(10)) comparator_1 (.a(adder_1_out), .b(10'h80), .lt(comparator_1_lt));  // open: gt, eq
  and and_1 (and_1_out, comparator_1_lt, ~adder_1_out[9]);  // AND_Gate
  assign not_1_out = ~vel_y[9:2];  // NOT_Gate not_1, 8 bits wide
  Adder adder_2 (.a(not_1_out), .b(8'h1), .out(adder_2_out));  // open: cin, cout
  xor xor_1 (xor_1_out, Py_1[9], Py_2[9]);
  Comparator comparator_2 (.a({8{1'b0}}), .b(Py_1[9:2]), .eq(comparator_2_eq));  // open: gt, lt
  not not_2 (not_2_out, comparator_3_eq);
  Comparator comparator_3 (.a(Py_2[9:2]), .b({8{1'b0}}), .eq(comparator_3_eq));  // open: gt, lt
  Comparator comparator_4 (.a({8{1'b0}}), .b(Py_2[9:2]), .eq(comparator_4_eq));  // open: gt, lt
  not not_3 (not_3_out, comparator_5_eq);
  Comparator comparator_5 (.a(Py_1[9:2]), .b({8{1'b0}}), .eq(comparator_5_eq));  // open: gt, lt
  or or_1 (or_1_out, comparator_6_gt, comparator_6_eq);
  Comparator comparator_6 (.a(Py_1[9:2]), .b({8{1'b0}}), .gt(comparator_6_gt), .eq(comparator_6_eq));  // open: lt
  Comparator comparator_7 (.a(Py_2[9:2]), .b({8{1'b0}}), .eq(comparator_7_eq), .lt(comparator_7_lt));  // open: gt
  or or_2 (or_2_out, comparator_7_eq, comparator_7_lt);
  and and_2 (and_2_out, comparator_2_eq, not_2_out);
  and and_3 (and_3_out, comparator_4_eq, not_3_out);
  and and_4 (and_4_out, or_1_out, or_2_out);
  assign {controlled_buffer_1_out, x_correct[6:0]} = and_4_out ? Inter_x : 10'bz;  // Controlled_Buffer controlled_buffer_1
  assign {controlled_buffer_2_out, y_correct[6:0]} = and_4_out ? multiplexer_1_out : 10'bz;  // Controlled_Buffer controlled_buffer_2
  Multiplexer #(.width(10)) multiplexer_1 (
    .in0(Inter_y), .in1(adder_1_out), .out(multiplexer_1_out), .sel(and_1_out));  // open: en
  Adder #(.width(10)) adder_3 (.a(y_b), .b(vel_y), .out(adder_3_out));  // open: cin, cout
  Subtractor #(.width(10)) subtractor_1 (
    .a(y_b), .b({adder_2_out, vel_y[1:0]}), .out(subtractor_1_out));  // open: bin, bout
  or or_3 (or_3_out, and_2_out, and_3_out);
  // Probe on Inter_x[9:2]
  Intersect_2_2_2 intersect_1 (
    .V_x(V_x), .wall_y(wall_y), .ball_x(ball_x), .V_y(V_y), .ball_y(ball_y),
    .NO_Intersection(Intersection_impossible), .Intersection_X(Inter_x), .Intersection_Y(Inter_y));
  // Probe on y_res[9:2]
  Multiplexer #(.width(10)) multiplexer_2 (
    .in0(adder_3_out), .in1(subtractor_1_out), .out(y_res), .sel(vel_y[9]));  // open: en
  or or_4 (wall_crossing, xor_1_out, or_3_out);
  // Probe on Inter_y[9:2]
  Subtractor #(.width(10)) subtractor_2 (.a(y_b), .b({wall_y, 2'b00}), .out(Py_1));  // open: bin, bout
  Comparator #(.width(10)) comparator_8 (
    .a(Inter_x), .b({wall_x, 2'b00}), .gt(comparator_8_gt), .eq(comparator_8_eq));  // open: lt
  Comparator #(.width(10)) comparator_9 (
    .a(Inter_x), .b(adder_4_out), .eq(comparator_9_eq), .lt(comparator_9_lt));  // open: gt
  Adder #(.width(10)) adder_4 (.a({wall_x, 2'b00}), .b({wall_size, 2'b00}), .out(adder_4_out));  // open: cin, cout
  // Probe on Py_1[9:2]
  or or_5 (or_5_out, comparator_8_gt, comparator_8_eq);
  or or_6 (or_6_out, comparator_9_eq, comparator_9_lt);
  Subtractor #(.width(10)) subtractor_3 (.a(Inter_y), .b(10'h4), .out(subtractor_3_out));  // open: bin, bout
  and and_5 (collision_happened, wall_crossing, Intersection_point_border_condition, ~Intersection_impossible);  // AND_Gate
  and and_6 (Intersection_point_border_condition, or_5_out, or_6_out);
  Comparator #(.width(10)) comparator_10 (.a(subtractor_3_out), .b(10'h80), .lt(comparator_10_lt));  // open: gt, eq
  and and_7 (and_7_out, comparator_10_lt, ~subtractor_3_out[9]);  // AND_Gate
  Subtractor #(.width(10)) subtractor_4 (.a(y_res), .b({wall_y, 2'b00}), .out(Py_2));  // open: bin, bout
  or or_7 (or_7_out, comparator_11_eq, comparator_11_lt);
  Comparator comparator_11 (.a(Py_1[9:2]), .b({8{1'b0}}), .eq(comparator_11_eq), .lt(comparator_11_lt));  // open: gt
  Comparator comparator_12 (.a(Py_2[9:2]), .b({8{1'b0}}), .gt(comparator_12_gt), .eq(comparator_12_eq));  // open: lt
  or or_8 (or_8_out, comparator_12_gt, comparator_12_eq);
  // Probe on Py_2[9:2]
  and and_8 (and_8_out, or_7_out, or_8_out);
  assign {controlled_buffer_3_out, x_correct[6:0]} = and_8_out ? Inter_x : 10'bz;  // Controlled_Buffer controlled_buffer_3
  assign {controlled_buffer_4_out, y_correct[6:0]} = and_8_out ? multiplexer_3_out : 10'bz;  // Controlled_Buffer controlled_buffer_4
  Multiplexer #(.width(10)) multiplexer_3 (
    .in0(Inter_y), .in1(subtractor_3_out), .out(multiplexer_3_out), .sel(and_7_out));  // open: en

  assign x_correct[7] = ball_x[7];
  assign y_correct[7] = ball_y[7];

  // Other names for the same wires on the sheet: w_x[9:2] = wall_x; w_y[9:2] = wall_y; wall_size_t[9:2] = wall_size;
  //   x_corr[7:0] = {ball_x[7], x_correct[6:0]}; y_corr[7:0] = {ball_y[7], y_correct[6:0]}

  // Notes on the sheet:
  //   Format: SXXXXXXXFF
endmodule

module update_ball_param (
  input  [7:0] x_correct,
  input  [7:0] y_correct,
  input  [7:0] V_x,
  input  [7:0] V_y,
  input  [1:0] wall_type,
  output [7:0] new_V_x,
  output [7:0] new_V_y,
  output [7:0] new_x_ball,
  output [7:0] new_y_ball
);

  wire [3:0] not_1_out, not_2_out;
  wire [7:4] Inv_V_x, Inv_V_y;

  // Probe on x_correct[6:2]
  // Probe on y_correct[6:2]
  // Probe on V_x[7:4]
  // Probe on V_y[7:4]
  assign not_1_out = ~V_x[7:4];  // NOT_Gate not_1, 4 bits wide
  assign not_2_out = ~V_y[7:4];  // NOT_Gate not_2, 4 bits wide
  Adder #(.width(4)) adder_1 (.a(4'b0001), .b(not_1_out), .out(Inv_V_x));  // open: cin, cout
  Adder #(.width(4)) adder_2 (.a(4'b0001), .b(not_2_out), .out(Inv_V_y));  // open: cin, cout
  Multiplexer #(.select(2), .width(8)) multiplexer_1 (
    .in0(V_x), .in1({Inv_V_x, V_x[3:0]}), .in2(V_y), .in3({Inv_V_y, V_y[3:0]}), .out(new_V_x), .sel(wall_type));  // open: en
  Multiplexer #(.select(2), .width(8)) multiplexer_2 (
    .in0({Inv_V_y, V_y[3:0]}), .in1(V_y), .in2(V_x), .in3({Inv_V_x, V_x[3:0]}), .out(new_V_y), .sel(wall_type));  // open: en
  // Probe on new_V_x[7:4]
  // Probe on new_V_y[7:4]
  // Probe on x_correct[6:2]
  // Probe on y_correct[6:2]

  assign new_x_ball = x_correct;
  assign new_y_ball = y_correct;

  // Other names for the same wires on the sheet: Inv_V_x[3:0] = V_x[3:0]; Inv_V_y[3:0] = V_y[3:0];
  //   new_Vx[7:0] = new_V_x; new_Vy[7:0] = new_V_y
endmodule
module Level_Data (
  input  [2:0] object_collide_num,
  input  [4:0] column_draw,
  input  Reset,
  input  Load_Game,
  output [31:0] screen_1,
  output [25:0] object_1,
  output [31:0] screen_2,
  output [25:0] object_2,
  output [31:0] screen_3,
  output [25:0] object_3,
  output [31:0] screen_4,
  output [25:0] object_4,
  output out_13,
  output [4:0] out_14,
  output [25:0] door_1,
  output [25:0] door_2,
  output loading_door
);

  wire and_1_out, and_5_out, buffer_1_out, buffer_2_out, buffer_3_out, buffer_4_out, buffer_5_out,
       buffer_6_out, cdm_8_mark5_1_p1, cdm_8_mark5_1_p2, cdm_8_mark5_1_p4, cdm_8_mark5_1_p5,
       cdm_8_mark5_1_p6, cdm_8_mark5_1_p7, cdm_8_mark5_1_p8, cdm_8_mark5_1_p9, cl, clock_1_out, code,
       counter_2_carry, counter_3_carry, data, decoder_1_out0, decoder_1_out1, decoder_1_out2,
       decoder_1_out3, demultiplexer_1_out0, demultiplexer_1_out1, demultiplexer_1_out2,
       demultiplexer_1_out3, finished, I_Osel, In_Out_prime, LOAD_GAME_out, mem, nand_1_out, not_1_out,
       not_2_out, not_3_out, or_1_out, or_2_out, or_3_out, or_4_out, or_9_out, or_10_out, or_11_out,
       or_12_out, or_14_out, RAM, RESET_out, update_screen, write;
  wire [1:0] screen_num;
  wire [2:0] multiplexer_1_out, object_load;
  wire [2:2] counter_3_q;
  wire [3:0] I_Oadr;
  wire [3:3] counter_2_q;
  wire [4:0] multiplexer_6_out, row_load;
  wire [7:0] bit_extender_1_out, cdm_8_mark5_1_p13, cdm_8_mark5_1_p14, demultiplexer_2_out1,
       demultiplexer_2_out2, demultiplexer_2_out3, demultiplexer_2_out4, I_Odat, ready;
  wire [7:1] finished_q;
  wire [7:4] cdm_8_mark5_1_p12;
  wire [7:5] x_q, y_q;
  wire [25:0] obj, rom_1_data, rom_2_data;
  wire [31:0] counter_1_q, decoder_3_out0, or_5_out, or_6_out, or_7_out, or_8_out;

  buf buffer_1 (buffer_1_out, buffer_1_out);
  Decoder #(.select(2), .enable("false")) decoder_1 (
    .out0(decoder_1_out0), .out1(decoder_1_out1), .out2(decoder_1_out2), .out3(decoder_1_out3),
    .sel(screen_num));
  buf buffer_2 (buffer_2_out, buffer_2_out);
  // Probe on obj[25:24]
  // Probe on obj[7:0]
  Multiplexer #(.width(3), .enable("false")) multiplexer_1 (
    .in0(object_collide_num), .in1(object_load), .out(multiplexer_1_out), .sel(out_13));
  // Probe on ready
  assign bit_extender_1_out = {{6{1'b0}}, obj[25:24]};  // Bit_Extender bit_extender_1
  // Probe on obj[15:8]
  Comparator #(.width(3)) comparator_1 (.a(3'b111), .b(multiplexer_1_out), .eq(loading_door));  // open: gt, lt
  or or_1 (or_1_out, decoder_1_out0, ~out_13);  // OR_Gate
  or or_2 (or_2_out, decoder_1_out1, ~out_13);  // OR_Gate
  or or_3 (or_3_out, decoder_1_out2, ~out_13);  // OR_Gate
  or or_4 (or_4_out, decoder_1_out3, ~out_13);  // OR_Gate
  and and_1 (and_1_out, I_Osel, In_Out_prime);
  Multiplexer #(.select(4), .width(8)) multiplexer_2 (
    .in1(ready), .in2(bit_extender_1_out), .in3(obj[7:0]), .in4(obj[15:8]), .in5(obj[23:16]), .out(I_Odat),
    .sel(I_Oadr), .en(and_1_out));  // open: in0, in6, in7, in8, in9, in10, in11, in12, in13, in14, in15
  ROM #(.addrWidth(3), .dataWidth(26)) rom_1 (.addr(multiplexer_1_out), .data(rom_1_data), .sel(or_1_out));
  ROM #(.addrWidth(3), .dataWidth(26)) rom_2 (.addr(multiplexer_1_out), .data(rom_2_data), .sel(or_2_out));
  ROM #(.addrWidth(3), .dataWidth(26)) rom_3 (.addr(multiplexer_1_out), .data(object_3), .sel(or_3_out));
  ROM #(.addrWidth(3), .dataWidth(26)) rom_4 (.addr(multiplexer_1_out), .data(object_4), .sel(or_4_out));
  Register #(.width(26), .trigger("falling")) register_1 (
    .D(rom_1_data), .en(out_13), .Q(door_1), .clk(loading_door));  // open: clr
  Register #(.width(26), .trigger("falling")) register_2 (
    .D(rom_2_data), .en(out_13), .Q(door_2), .clk(loading_door));  // open: clr
  Clock clock_1 (.out(clock_1_out));
  // Probe on cdm_8_mark5_1_p2
  // Probe on cdm_8_mark5_1_p5
  // Probe on cdm_8_mark5_1_p4
  // Probe on cdm_8_mark5_1_p1
  buf buffer_3 (buffer_3_out, buffer_3_out);
  Multiplexer #(.width(26)) multiplexer_3 (
    .in0(rom_1_data), .in1({26{1'b0}}), .out(object_1), .sel(loading_door));  // open: en
  Multiplexer #(.width(26)) multiplexer_4 (
    .in0(rom_2_data), .in1({26{1'b0}}), .out(object_2), .sel(loading_door));  // open: en
  and and_2 (cl, clock_1_out, out_13);
  // Probe on cdm_8_mark5_1_p7
  // Probe on cdm_8_mark5_1_p8
  // Probe on cdm_8_mark5_1_p6
  // CdM_8_mark5 cdm_8_mark5_1: pin names not known; wires that end beside it: cdm_8_mark5_1_p1, cdm_8_mark5_1_p2, cl, cdm_8_mark5_1_p4, cdm_8_mark5_1_p5, cdm_8_mark5_1_p6, cdm_8_mark5_1_p7, cdm_8_mark5_1_p8, cdm_8_mark5_1_p9, mem, In_Out_prime, {cdm_8_mark5_1_p12, I_Oadr}, cdm_8_mark5_1_p13, cdm_8_mark5_1_p14
  and and_3 (I_Osel, not_2_out, cl, data);
  assign I_Odat = not_1_out ? cdm_8_mark5_1_p13 : 8'bz;  // Controlled_Buffer controlled_buffer_1
  not not_1 (not_1_out, In_Out_prime);
  assign cdm_8_mark5_1_p14 = In_Out_prime ? I_Odat : 8'bz;  // Controlled_Buffer controlled_buffer_2
  not not_2 (not_2_out, nand_1_out);
  and and_4 (RAM, nand_1_out, data);
  Multiplexer #(.select(2), .width(26)) multiplexer_5 (
    .in0(object_1), .in1(object_2), .in2(object_3), .in3(object_4), .out(obj), .sel(screen_num));  // open: en
  Decoder #(.disabled(0)) decoder_2 (.out0(code), .out1(data), .sel(cdm_8_mark5_1_p9), .en(mem));
  nand nand_1 (nand_1_out, cdm_8_mark5_1_p12[4], cdm_8_mark5_1_p12[5], cdm_8_mark5_1_p12[6], cdm_8_mark5_1_p12[7]);
  // Probe on counter_1_q
  Counter #(.width(32), .max('hffffffff)) counter_1 (.Q(counter_1_q), .clk(cl));  // open: load, D, count, carry, clr
  buf buffer_4 (buffer_4_out, buffer_4_out);
  Decoder #(.select(5), .enable("false")) decoder_3 (
    .out0(decoder_3_out0[0]), .out1(decoder_3_out0[1]), .out2(decoder_3_out0[2]), .out3(decoder_3_out0[3]),
    .out4(decoder_3_out0[4]), .out5(decoder_3_out0[5]), .out6(decoder_3_out0[6]), .out7(decoder_3_out0[7]),
    .out8(decoder_3_out0[8]), .out9(decoder_3_out0[9]), .out10(decoder_3_out0[10]),
    .out11(decoder_3_out0[11]), .out12(decoder_3_out0[12]), .out13(decoder_3_out0[13]),
    .out14(decoder_3_out0[14]), .out15(decoder_3_out0[15]), .out16(decoder_3_out0[16]),
    .out17(decoder_3_out0[17]), .out18(decoder_3_out0[18]), .out19(decoder_3_out0[19]),
    .out20(decoder_3_out0[20]), .out21(decoder_3_out0[21]), .out22(decoder_3_out0[22]),
    .out23(decoder_3_out0[23]), .out24(decoder_3_out0[24]), .out25(decoder_3_out0[25]),
    .out26(decoder_3_out0[26]), .out27(decoder_3_out0[27]), .out28(decoder_3_out0[28]),
    .out29(decoder_3_out0[29]), .out30(decoder_3_out0[30]), .out31(decoder_3_out0[31]), .sel(row_load));
  Demultiplexer #(.select(2)) demultiplexer_1 (
    .out0(demultiplexer_1_out0), .out1(demultiplexer_1_out1), .out2(demultiplexer_1_out2),
    .out3(demultiplexer_1_out3), .in(update_screen), .sel(screen_num));  // open: en
  buf buffer_5 (buffer_5_out, buffer_5_out);
  Multiplexer #(.width(5), .enable("false")) multiplexer_6 (
    .in0(column_draw), .in1(out_14), .out(multiplexer_6_out), .sel(out_13));
  assign or_5_out = screen_1 | decoder_3_out0;  // OR_Gate or_5, 32 bits wide
  assign or_6_out = screen_2 | decoder_3_out0;  // OR_Gate or_6, 32 bits wide
  assign or_7_out = screen_3 | decoder_3_out0;  // OR_Gate or_7, 32 bits wide
  assign or_8_out = screen_4 | decoder_3_out0;  // OR_Gate or_8, 32 bits wide
  and and_5 (and_5_out, out_13, or_9_out);
  or or_9 (or_9_out, finished, or_14_out);
  ROM rom_5 (.addr({cdm_8_mark5_1_p12, I_Oadr}), .data(I_Odat), .sel(code));
  RAM ram_1 (.addr({cdm_8_mark5_1_p12, I_Oadr}), .data(I_Odat), .sel(RAM), .clk(cl), .ld(In_Out_prime));  // open: clr
  assign ready = {{7{1'b0}}, and_5_out};  // Bit_Extender bit_extender_2
  RAM #(.addrWidth(5), .dataWidth(32), .bus("separate")) ram_2 (
    .addr(multiplexer_6_out), .din(or_5_out), .data(screen_1), .clk(demultiplexer_1_out0), .clr(or_11_out));  // open: str, sel, ld
  RAM #(.addrWidth(5), .dataWidth(32), .bus("separate")) ram_3 (
    .addr(multiplexer_6_out), .din(or_6_out), .data(screen_2), .clk(demultiplexer_1_out1), .clr(or_11_out));  // open: str, sel, ld
  RAM #(.addrWidth(5), .dataWidth(32), .bus("separate")) ram_4 (
    .addr(multiplexer_6_out), .din(or_7_out), .data(screen_3), .clk(demultiplexer_1_out2), .clr(or_11_out));  // open: str, sel, ld
  RAM #(.addrWidth(5), .dataWidth(32), .bus("separate")) ram_5 (
    .addr(multiplexer_6_out), .din(or_8_out), .data(screen_4), .clk(demultiplexer_1_out3), .clr(or_11_out));  // open: str, sel, ld
  Counter #(.width(4), .max('h8), .trigger("falling")) counter_2 (
    .Q({counter_2_q[3], object_load}), .carry(counter_2_carry), .clk(finished), .clr(or_10_out));  // open: load, D, count
  or or_10 (or_10_out, counter_2_carry, not_3_out, or_14_out);
  buf buffer_6 (buffer_6_out, buffer_6_out);
  Counter #(.width(3), .max('h4)) counter_3 (
    .Q({counter_3_q[2], screen_num}), .carry(counter_3_carry), .clk(counter_2_carry), .clr(or_14_out));  // open: load, D, count
  and and_6 (write, I_Osel, ~In_Out_prime);  // AND_Gate
  Demultiplexer #(.select(4), .width(8), .tristate("true"), .disabled(0)) demultiplexer_2 (
    .out1(demultiplexer_2_out1), .out2(demultiplexer_2_out2), .out3(demultiplexer_2_out3),
    .out4(demultiplexer_2_out4), .in(I_Odat), .sel(I_Oadr), .en(write));  // open: out0, out5, out6, out7, out8, out9, out10, out11, out12, out13, out14, out15
  or or_11 (or_11_out, RESET_out, Reset, or_14_out);
  Counter #(.width(1), .max('h1)) counter_4 (.Q(out_13), .clk(or_12_out));  // open: load, D, count, carry, clr
  or or_12 (or_12_out, counter_3_carry, or_14_out);
  not not_3 (not_3_out, out_13);
  Register #(.trigger("falling")) u_finished (
    .D(demultiplexer_2_out1), .Q({finished_q, finished}), .clk(write));  // open: en, clr
  // Probe on {x_q, out_14}
  Register #(.trigger("falling")) x (.D(demultiplexer_2_out2), .Q({x_q, out_14}), .clk(write));  // open: en, clr
  // Probe on {y_q, row_load}
  Register #(.trigger("falling")) y (.D(demultiplexer_2_out3), .Q({y_q, row_load}), .clk(write));  // open: en, clr
  or or_13 (update_screen, demultiplexer_2_out4[0], demultiplexer_2_out4[1], demultiplexer_2_out4[2], demultiplexer_2_out4[3], demultiplexer_2_out4[4], demultiplexer_2_out4[5], demultiplexer_2_out4[6], demultiplexer_2_out4[7]);
  Button u_RESET (.out(RESET_out));
  or or_14 (or_14_out, LOAD_GAME_out, Load_Game);
  Button u_LOAD_GAME (.out(LOAD_GAME_out));
  // NOT_Gate not_4 is placed but not wired

  // Other names for the same wires on the sheet: column_load[4:0] = out_14; door1[25:0] = door_1;
  //   door2[25:0] = door_2; loading = out_13; rd_wr_prime = In_Out_prime

  // Notes on the sheet:
  //   buffer_1 drives only 1 and floats otherwise
  //   buffer_2 drives only 1 and floats otherwise
  //   Wall Data
  //   Input to processor
  //   contents of rom_1 (hex, n*v repeats v):
  //   0 3071601 1071601 30a1c13 1070907 3080808 0 100110
  //   contents of rom_2 (hex, n*v repeats v):
  //   0 2080110 1070918 2071018 106171e 20a1303 0 100100
  //   contents of rom_3 (hex, n*v repeats v):
  //   0 0 10b0301 2110e01 e1e12 20a0a0b 0 20a0313
  //   contents of rom_4 (hex, n*v repeats v):
  //   0 10b031e 3111e0e f1e00 30a0c03 30a130b
  //   buffer_3 drives only 1 and floats otherwise
  //   CDM
  //   Hz checker
  //   buffer_4 drives only 1 and floats otherwise
  //   buffer_5 drives only 1 and floats otherwise
  //   Draw Data
  //   instr memory
  //   data memory
  //   contents of rom_5 (hex, n*v repeats v):
  //   d0 f0 c1 d1 8 a4 c5 cd 0 d0 f1 35 3a 3f b1 5 e0 e a2 8c b1 8c b2 8c b3 8c 5 e1 35 b1 88 88 88 5 e0
  //   2f a2 8c a3 8c a1 8e 89 88 88 ee 21 88 d1 1 a1 ee 9 89 5 e1 51 b1 88 88 88 5 e0 4b a2 8c a3 8c a1 8f
  //   89 88 88 ee 3d 88 d1 1 a1 ee 9 89 5 e1 6e b1 88 88 88 5 e0 68 a2 8c a3 8c a1 8e 8f 89 88 88 ee 59 88
  //   d1 1 a1 ee 9 89 5 e1 8b b1 88 88 88 5 e0 85 a2 8c a3 8c a1 8e 8b 89 88 88 ee 76 88 d1 1 a1 ee 9
  //   buffer_6 drives only 1 and floats otherwise
  //   output
endmodule

module Screen_Memory (
  input  [31:0] new_column,
  input  clock,
  input  [4:0] x,
  output [31:0] out_4,
  output [31:0] out_5,
  output [31:0] out_6,
  output [31:0] out_7,
  output [31:0] out_8,
  output [31:0] out_9,
  output [31:0] out_10,
  output [31:0] out_11,
  output [31:0] out_12,
  output [31:0] out_13,
  output [31:0] out_14,
  output [31:0] out_15,
  output [31:0] out_16,
  output [31:0] out_17,
  output [31:0] out_18,
  output [31:0] out_19,
  output [31:0] out_20,
  output [31:0] out_21,
  output [31:0] out_22,
  output [31:0] out_23,
  output [31:0] out_24,
  output [31:0] out_25,
  output [31:0] out_26,
  output [31:0] out_27,
  output [31:0] out_28,
  output [31:0] out_29,
  output [31:0] out_30,
  output [31:0] out_31,
  output [31:0] out_32,
  output [31:0] out_33,
  output [31:0] out_34,
  output [31:0] out_35
);

  wire [31:0] demultiplexer_1_out0, demultiplexer_1_out1, demultiplexer_1_out2, demultiplexer_1_out3,
       demultiplexer_1_out4, demultiplexer_1_out5, demultiplexer_1_out6, demultiplexer_1_out7,
       demultiplexer_1_out8, demultiplexer_1_out9, demultiplexer_1_out10, demultiplexer_1_out11,
       demultiplexer_1_out12, demultiplexer_1_out13, demultiplexer_1_out14, demultiplexer_1_out15,
       demultiplexer_1_out16, demultiplexer_1_out17, demultiplexer_1_out18, demultiplexer_1_out19,
       demultiplexer_1_out20, demultiplexer_1_out21, demultiplexer_1_out22, demultiplexer_1_out23,
       demultiplexer_1_out24, demultiplexer_1_out25, demultiplexer_1_out26, demultiplexer_1_out27,
       demultiplexer_1_out28, demultiplexer_1_out29, demultiplexer_1_out30, demultiplexer_1_out31;

  Demultiplexer #(.select(5), .width(32), .tristate("true")) demultiplexer_1 (
    .out0(demultiplexer_1_out0), .out1(demultiplexer_1_out1), .out2(demultiplexer_1_out2),
    .out3(demultiplexer_1_out3), .out4(demultiplexer_1_out4), .out5(demultiplexer_1_out5),
    .out6(demultiplexer_1_out6), .out7(demultiplexer_1_out7), .out8(demultiplexer_1_out8),
    .out9(demultiplexer_1_out9), .out10(demultiplexer_1_out10), .out11(demultiplexer_1_out11),
    .out12(demultiplexer_1_out12), .out13(demultiplexer_1_out13), .out14(demultiplexer_1_out14),
    .out15(demultiplexer_1_out15), .out16(demultiplexer_1_out16), .out17(demultiplexer_1_out17),
    .out18(demultiplexer_1_out18), .out19(demultiplexer_1_out19), .out20(demultiplexer_1_out20),
    .out21(demultiplexer_1_out21), .out22(demultiplexer_1_out22), .out23(demultiplexer_1_out23),
    .out24(demultiplexer_1_out24), .out25(demultiplexer_1_out25), .out26(demultiplexer_1_out26),
    .out27(demultiplexer_1_out27), .out28(demultiplexer_1_out28), .out29(demultiplexer_1_out29),
    .out30(demultiplexer_1_out30), .out31(demultiplexer_1_out31), .in(new_column), .sel(x));  // open: en
  Register #(.width(32)) register_1 (.D(demultiplexer_1_out0), .Q(out_4), .clk(clock));  // open: en, clr
  Register #(.width(32)) register_2 (.D(demultiplexer_1_out1), .Q(out_5), .clk(clock));  // open: en, clr
  Register #(.width(32)) register_3 (.D(demultiplexer_1_out2), .Q(out_6), .clk(clock));  // open: en, clr
  Register #(.width(32)) register_4 (.D(demultiplexer_1_out3), .Q(out_7), .clk(clock));  // open: en, clr
  Register #(.width(32)) register_5 (.D(demultiplexer_1_out4), .Q(out_8), .clk(clock));  // open: en, clr
  Register #(.width(32)) register_6 (.D(demultiplexer_1_out5), .Q(out_9), .clk(clock));  // open: en, clr
  Register #(.width(32)) register_7 (.D(demultiplexer_1_out6), .Q(out_10), .clk(clock));  // open: en, clr
  Register #(.width(32)) register_8 (.D(demultiplexer_1_out7), .Q(out_11), .clk(clock));  // open: en, clr
  Register #(.width(32)) register_9 (.D(demultiplexer_1_out8), .Q(out_12), .clk(clock));  // open: en, clr
  Register #(.width(32)) register_10 (.D(demultiplexer_1_out9), .Q(out_13), .clk(clock));  // open: en, clr
  Register #(.width(32)) register_11 (.D(demultiplexer_1_out10), .Q(out_14), .clk(clock));  // open: en, clr
  Register #(.width(32)) register_12 (.D(demultiplexer_1_out11), .Q(out_15), .clk(clock));  // open: en, clr
  Register #(.width(32)) register_13 (.D(demultiplexer_1_out12), .Q(out_16), .clk(clock));  // open: en, clr
  Register #(.width(32)) register_14 (.D(demultiplexer_1_out13), .Q(out_17), .clk(clock));  // open: en, clr
  Register #(.width(32)) register_15 (.D(demultiplexer_1_out14), .Q(out_18), .clk(clock));  // open: en, clr
  Register #(.width(32)) register_16 (.D(demultiplexer_1_out15), .Q(out_19), .clk(clock));  // open: en, clr
  Register #(.width(32)) register_17 (.D(demultiplexer_1_out16), .Q(out_20), .clk(clock));  // open: en, clr
  Register #(.width(32)) register_18 (.D(demultiplexer_1_out17), .Q(out_21), .clk(clock));  // open: en, clr
  Register #(.width(32)) register_19 (.D(demultiplexer_1_out18), .Q(out_22), .clk(clock));  // open: en, clr
  Register #(.width(32)) register_20 (.D(demultiplexer_1_out19), .Q(out_23), .clk(clock));  // open: en, clr
  Register #(.width(32)) register_21 (.D(demultiplexer_1_out20), .Q(out_24), .clk(clock));  // open: en, clr
  Register #(.width(32)) register_22 (.D(demultiplexer_1_out21), .Q(out_25), .clk(clock));  // open: en, clr
  Register #(.width(32)) register_23 (.D(demultiplexer_1_out22), .Q(out_26), .clk(clock));  // open: en, clr
  Register #(.width(32)) register_24 (.D(demultiplexer_1_out23), .Q(out_27), .clk(clock));  // open: en, clr
  Register #(.width(32)) register_25 (.D(demultiplexer_1_out24), .Q(out_28), .clk(clock));  // open: en, clr
  Register #(.width(32)) register_26 (.D(demultiplexer_1_out25), .Q(out_29), .clk(clock));  // open: en, clr
  Register #(.width(32)) register_27 (.D(demultiplexer_1_out26), .Q(out_30), .clk(clock));  // open: en, clr
  Register #(.width(32)) register_28 (.D(demultiplexer_1_out27), .Q(out_31), .clk(clock));  // open: en, clr
  Register #(.width(32)) register_29 (.D(demultiplexer_1_out28), .Q(out_32), .clk(clock));  // open: en, clr
  Register #(.width(32)) register_30 (.D(demultiplexer_1_out29), .Q(out_33), .clk(clock));  // open: en, clr
  Register #(.width(32)) register_31 (.D(demultiplexer_1_out30), .Q(out_34), .clk(clock));  // open: en, clr
  Register #(.width(32)) register_32 (.D(demultiplexer_1_out31), .Q(out_35), .clk(clock));  // open: en, clr
endmodule

module Graphics_Main (
  input  [31:0] state0,
  input  [31:0] state1,
  input  [31:0] state2,
  input  [31:0] state3,
  input  [1:0] active_screen,
  input  [4:0] ball_x,
  input  [4:0] ball_y,
  input  active_1,
  input  active_2,
  input  [4:0] x,
  output [31:0] screen_1,
  output [31:0] screen_2,
  output [31:0] screen_3,
  output [31:0] screen_4
);

  wire decoder_1_out0, decoder_1_out1, decoder_1_out2, decoder_1_out3;

  Decoder #(.select(2)) decoder_1 (
    .out0(decoder_1_out0), .out1(decoder_1_out1), .out2(decoder_1_out2), .out3(decoder_1_out3),
    .sel(active_screen));  // open: en
  Graphics_Ultra graphics_ultra_1 (
    .input_ball(decoder_1_out0), .ball_x(ball_x), .ball_y(ball_y), .x(5'b10000), .size(5'b10000),
    .out_9(screen_1), .base(state0), .current_x(x), .is_active(active_1));
  Graphics_Ultra graphics_ultra_2 (
    .input_ball(decoder_1_out1), .ball_x(ball_x), .ball_y(ball_y), .x({5{1'b0}}), .size(5'b10000),
    .out_9(screen_2), .base(state1), .current_x(x), .is_active(active_2));
  Graphics_Ultra graphics_ultra_3 (
    .input_ball(decoder_1_out2), .ball_x(ball_x), .ball_y(ball_y), .out_9(screen_3), .base(state2),
    .current_x(x));  // open: x, size, is_active
  Graphics_Ultra graphics_ultra_4 (
    .input_ball(decoder_1_out3), .ball_x(ball_x), .ball_y(ball_y), .out_9(screen_4), .base(state3),
    .current_x(x));  // open: x, size, is_active
endmodule

module RS_latch (
  input  S,
  input  R,
  input  reset,
  output Q,
  output Q_prime
);

  S_R_Flip_Flop #(.trigger("high")) s_r_ff_1 (
    .S(S), .clk(1'b1), .R(R), .Q(Q), .Qn(Q_prime), .reset(reset));  // open: preset, en
endmodule

module Score_Counter (
  input  collision_happened,
  input  out_of_screen,
  input  reset_all,
  output [3:0] score_AXX,
  output [3:0] score_XAX,
  output [3:0] score_XXA,
  output [3:0] max_AXX,
  output [3:0] max_XAX,
  output [3:0] max_XXA
);

  wire comparator_1_gt, controlled_buffer_1_out, counter_2_carry, counter_3_carry;

  Counter #(.width(4), .max('h9), .trigger("falling")) counter_1 (
    .Q(score_XXA), .clk(counter_2_carry), .clr(out_of_screen));  // open: load, D, count, carry
  Counter #(.width(4), .max('h9), .trigger("falling")) counter_2 (
    .Q(score_XAX), .carry(counter_2_carry), .clk(counter_3_carry), .clr(out_of_screen));  // open: load, D, count
  Counter #(.width(4), .max('h9)) counter_3 (
    .Q(score_AXX), .carry(counter_3_carry), .clk(collision_happened), .clr(out_of_screen));  // open: load, D, count
  Comparator #(.width(12), .mode("unsigned")) comparator_1 (
    .a({score_XXA, score_XAX, score_AXX}), .b({max_XXA, max_XAX, max_AXX}), .gt(comparator_1_gt));  // open: eq, lt
  assign controlled_buffer_1_out = comparator_1_gt ? out_of_screen : 1'bz;  // Controlled_Buffer controlled_buffer_1
  Register #(.width(4)) register_1 (
    .D(score_XXA), .Q(max_XXA), .clk(controlled_buffer_1_out), .clr(reset_all));  // open: en
  Register #(.width(4)) register_2 (
    .D(score_XAX), .Q(max_XAX), .clk(controlled_buffer_1_out), .clr(reset_all));  // open: en
  Register #(.width(4)) register_3 (
    .D(score_AXX), .Q(max_AXX), .clk(controlled_buffer_1_out), .clr(reset_all));  // open: en

  // Other names for the same wires on the sheet: max1[3:0] = max_AXX; max_score[11:0] = {max_XXA, max_XAX, max_AXX};
  //   max2[3:0] = max_XAX; max3[3:0] = max_XXA; sc1[3:0] = score_AXX; score[11:0] = {score_XXA, score_XAX, score_AXX};
  //   sc2[3:0] = score_XAX; sc3[3:0] = score_XXA
endmodule
